// Logisim project Minimap.circ as structural Verilog: 9 circuits, main circuit maps
// Maps
module maps (
  input  [7:0] ADDR,
  input  [11:0] ELEM,
  output [11:0] Width,
  output [11:0] Height,
  output [7:0] Xpp,
  output [7:0] Ypp,
  output [7:0] DATA,
  output [11:0] LEN
);

  wire [7:0] mgeD0, mgeD1, mgeD2, undriven_4, undriven_5;
  wire [11:0] undriven, undriven_2, undriven_3;

  ROM #(.addrWidth(12)) rom_1 (.addr(ELEM), .data(mgeD0));  // open: sel
  ROM #(.addrWidth(12)) rom_2 (.addr(ELEM), .data(mgeD1));  // open: sel
  ROM #(.addrWidth(12)) rom_3 (.addr(ELEM), .data(mgeD2));  // open: sel
  Multiplexer #(.select(5), .width(8), .enable("false")) multiplexer_1 (
    .in0(mgeD0), .in1(mgeD1), .in2(mgeD2), .out(DATA), .sel(ADDR[4:0]));  // open: in3, in4, in5, in6, in7, in8, in9, in10, in11, in12, in13, in14, in15, in16, in17, in18, in19, in20, in21, in22, in23, in24, in25, in26, in27, in28, in29, in30, in31
  Multiplexer #(.select(5), .width(12), .enable("false")) multiplexer_2 (
    .in0(12'h64), .in1(12'h2e5), .in2(12'hab), .in30(undriven), .in31(undriven), .out(LEN), .sel(ADDR[4:0]));  // open: in3, in4, in5, in6, in7, in8, in9, in10, in11, in12, in13, in14, in15, in16, in17, in18, in19, in20, in21, in22, in23, in24, in25, in26, in27, in28, in29
  Multiplexer #(.select(5), .width(12), .enable("false")) multiplexer_3 (
    .in0(12'hb), .in1(12'h25), .in2(12'h11), .in30(undriven_2), .in31(undriven_2), .out(Width),
    .sel(ADDR[4:0]));  // open: in3, in4, in5, in6, in7, in8, in9, in10, in11, in12, in13, in14, in15, in16, in17, in18, in19, in20, in21, in22, in23, in24, in25, in26, in27, in28, in29
  Multiplexer #(.select(5), .width(12), .enable("false")) multiplexer_4 (
    .in0(12'h8), .in1(12'h14), .in2(12'ha), .in30(undriven_3), .in31(undriven_3), .out(Height),
    .sel(ADDR[4:0]));  // open: in3, in4, in5, in6, in7, in8, in9, in10, in11, in12, in13, in14, in15, in16, in17, in18, in19, in20, in21, in22, in23, in24, in25, in26, in27, in28, in29
  Multiplexer #(.select(5), .width(8), .enable("false")) multiplexer_5 (
    .in0(8'h4), .in1(8'h13), .in2(8'h4), .in30(undriven_4), .in31(undriven_4), .out(Xpp), .sel(ADDR[4:0]));  // open: in3, in4, in5, in6, in7, in8, in9, in10, in11, in12, in13, in14, in15, in16, in17, in18, in19, in20, in21, in22, in23, in24, in25, in26, in27, in28, in29
  Multiplexer #(.select(5), .width(8), .enable("false")) multiplexer_6 (
    .in0(8'h3), .in1(8'hc), .in2(8'h4), .in30(undriven_5), .in31(undriven_5), .out(Ypp), .sel(ADDR[4:0]));  // open: in3, in4, in5, in6, in7, in8, in9, in10, in11, in12, in13, in14, in15, in16, in17, in18, in19, in20, in21, in22, in23, in24, in25, in26, in27, in28, in29

  // Other names for the same wires on the sheet: mdeMux1[7:0] = DATA; mdeMuxl1[11:0] = LEN; mgeAddr1[4:0] = ADDR[4:0];
  //   mgeEl[11:0] = ELEM; mhMuxl1[11:0] = Height; mwMuxl1[11:0] = Width; mXMuxl1[7:0] = Xpp; mYMuxl1[7:0] = Ypp

  // Notes on the sheet:
  //   TEST MAP
  //   Level 1
  //   Level 2
  //   contents of rom_1 (hex, n*v repeats v):
  //   36*23 20 66 6a 61 20 6*23 20 23 23 20 32 6*23 20 20 23 23 20 36*23
  //   contents of rom_2 (hex, n*v repeats v):
  //   114*23 20 45 23 63 4*20 23 20 20 20 23 20 20 20 23 4*20 23 20 62 20 20 32 31 31 31 68 6*23 20 23 23
  //   20 23 23 23 20 23 20 23 63 23 20 23 20 20 20 23 23 20 23 23 20 23 20 11*23 33 23 23 20 20 20 23 20
  //   31 20 23 20 20 20 5*23 20 20 20 32 20 23 4*20 23 67 6*23 20 64 23 23 23 20 5*23 20 4*23 20 20 23 20
  //   5*23 20 23 20 20 23 34 6*23 34 23 23 20 20 20 23 20 23 23 23 20 20 62 20 23 20 4*23 20 20 20 23 23
  //   23 20 23 23 32 6*23 34 23 23 20 23 20 23 20 20 20 23 20 20 23 31 23 20 23 23 20 23 20 23 5*20 62 20
  //   20 6*23 4*20 23 20 20 20 23 20 20 61 23 23 20 23 20 23 4*20 15*23 20 5*23 20 23 23 31 23 23 23 4*20
  //   23 32 23 23 4*20 64 23 4*20 6*23 31 23 23 4*20 23 6*20 4*23 20 23 23 23 20 4*23 20 23 20 7*23 20 23
  //   23 20 23 20 9*23 66 4*20 6a 23 6*20 23 20 20 6*23 20 23 20 20 23 20 20 23 20 23 23 20 20 23 23 20
  //   6*23 20 23 20 5*23 20 6*23 20 23 23 20 4*23 20 31 20 20 20 23 62 8*20 23 5*20 23 31 6*23 20 23 23 32
  //   20 20 20 23 20 7*23 20 23 23 23 20 23 20 5*23 20 23 20 6*23 20 20 20 61 23 7*20 62 5*20 23 20 20 20
  //   31 32 20 69 20 23 20 20 63 114*23
  //   contents of rom_3 (hex, n*v repeats v):
  //   54*23 4*20 23 20 20 23 20 20 20 6*23 20 20 23 4*20 45 20 23 20 6*23 20 20 8*23 20 6*23 11*20 54*23
  //   Возращает данные карты по адресу
  //   Предоставляет поэлементный доступ к ее элеменнтам
endmodule

module x_y__to_memory_elem_number (
  input  [11:0] H,
  input  [7:0] Y,
  input  [7:0] X,
  output [11:0] ELEM
);

  wire [11:0] bit_extender_1_out, bit_extender_2_out, multiplier_1_out;

  assign bit_extender_1_out = {{4{1'b0}}, Y};  // Bit_Extender bit_extender_1
  Multiplier #(.width(12)) multiplier_1 (.a(H), .b(bit_extender_1_out), .out(multiplier_1_out));  // open: cin, cout
  assign bit_extender_2_out = {{4{1'b0}}, X};  // Bit_Extender bit_extender_2
  Adder #(.width(12)) adder_1 (.a(multiplier_1_out), .b(bit_extender_2_out), .out(ELEM));  // open: cin, cout

  // Notes on the sheet:
  //   Переводит координаты ячейки в номер в массиве
  //   H - ширина карты
endmodule

module cond_en_weap (
  input  [1:0] input_char,
  output todisplay,
  output Exit
);

  Multiplexer #(.select(2), .enable("false")) multiplexer_1 (
    .in0(1'b0), .in1(1'b1), .in2(1'b0), .out(todisplay), .sel(input_char));  // open: in3
  Comparator #(.width(2), .mode("unsigned")) comparator_1 (.a(input_char), .b(2'b10), .eq(Exit));  // open: gt, lt
endmodule

module cond_wall_pass (
  input  [7:0] in_1,
  output out
);

  wire comparator_1_eq;

  Comparator comparator_1 (.a(in_1), .b(8'h23), .eq(comparator_1_eq));  // open: gt, lt
  not not_1 (out, comparator_1_eq);
endmodule

module plr_in_cond_of_dir (
  input  [1:0] in_1,
  output [1:0] out_2,
  output [1:0] out_3
);

  Multiplexer #(.select(2), .width(4), .enable("false")) multiplexer_1 (
    .in0(4'b0011), .in1(4'b0101), .in2(4'b1100), .in3(4'b1010), .out({out_3, out_2}), .sel(in_1));
endmodule

module mmap_matrix (
  input  [7:0] Xpp,
  input  [7:0] No_of_map,
  input  [7:0] Ypp,
  output [7:0] out_4,
  output [7:0] out_5,
  output [7:0] out_6,
  output [7:0] out_7,
  output [7:0] out_8,
  output [7:0] out_9,
  output [7:0] out_10,
  output [7:0] out_11,
  output [7:0] out_12,
  output [7:0] out_13,
  output [7:0] out_14,
  output [7:0] out_15,
  output [7:0] out_16,
  output [7:0] out_17,
  output [7:0] out_18,
  output [7:0] out_19,
  output [7:0] out_20,
  output [7:0] out_21,
  output [7:0] out_22,
  output [7:0] out_23,
  output [7:0] out_24,
  output [7:0] out_25,
  output [7:0] out_26,
  output [7:0] out_27,
  output [7:0] out_28,
  output [7:0] out_29,
  output [7:0] out_30,
  output [7:0] out_31,
  output [7:0] out_32,
  output [7:0] out_33,
  output [7:0] out_34,
  output [7:0] out_35,
  output [7:0] out_36,
  output [7:0] out_37,
  output [7:0] out_38,
  output [7:0] out_39,
  output [7:0] out_40,
  output [7:0] out_41,
  output [7:0] out_42,
  output [7:0] out_43,
  output [7:0] out_44,
  output [7:0] out_45,
  output [7:0] out_46,
  output [7:0] out_47,
  output [7:0] out_48,
  output [7:0] out_49,
  output [7:0] out_50,
  output [7:0] out_51,
  output [7:0] out_52
);

  wire [11:0] adder_21_out, adder_29_out, addr0, addr1, addr2, addr3, addr4, addr5, addr6, multiplier_1_out,
       num1, num2, num3, num4, num5, num6, num7, num8, num9, num10, num11, num12, num13, num14, num15, num16,
       num17, num18, num19, num20, num21, num22, num23, num24, num25, num26, num27, num28, num29, num30,
       num31, num32, num33, num34, num35, num36, num37, num38, num39, num40, num41, num42, num43, num44,
       num45, num46, num47, num48, num49, Width;

  Adder #(.width(12)) adder_1 (.a(addr0), .b(Width), .out(addr1));  // open: cin, cout
  Adder #(.width(12)) adder_2 (.a(addr1), .b(Width), .out(addr2));  // open: cin, cout
  Adder #(.width(12)) adder_3 (.a(addr2), .b(Width), .out(addr3));  // open: cin, cout
  Adder #(.width(12)) adder_4 (.a(addr3), .b(Width), .out(addr4));  // open: cin, cout
  Adder #(.width(12)) adder_5 (.a(addr4), .b(Width), .out(addr5));  // open: cin, cout
  Adder #(.width(12)) adder_6 (.a(addr5), .b(Width), .out(addr6));  // open: cin, cout
  Adder #(.width(12)) adder_7 (.a(addr1), .b({12{1'b0}}), .out(num8));  // open: cin, cout
  Adder #(.width(12)) adder_8 (.a(addr1), .b(12'h1), .out(num9));  // open: cin, cout
  Adder #(.width(12)) adder_9 (.a(addr1), .b(12'h2), .out(num10));  // open: cin, cout
  Adder #(.width(12)) adder_10 (.a(addr1), .b(12'h3), .out(num11));  // open: cin, cout
  Adder #(.width(12)) adder_11 (.a(addr1), .b(12'h4), .out(num12));  // open: cin, cout
  Adder #(.width(12)) adder_12 (.a(addr1), .b(12'h5), .out(num13));  // open: cin, cout
  Adder #(.width(12)) adder_13 (.a(addr1), .b(12'h6), .out(num14));  // open: cin, cout
  Adder #(.width(12)) adder_14 (.a(addr0), .b({12{1'b0}}), .out(num1));  // open: cin, cout
  Adder #(.width(12)) adder_15 (.a(addr0), .b(12'h1), .out(num2));  // open: cin, cout
  Adder #(.width(12)) adder_16 (.a(addr0), .b(12'h2), .out(num3));  // open: cin, cout
  Adder #(.width(12)) adder_17 (.a(addr0), .b(12'h3), .out(num4));  // open: cin, cout
  Adder #(.width(12)) adder_18 (.a(addr0), .b(12'h4), .out(num5));  // open: cin, cout
  Adder #(.width(12)) adder_19 (.a(addr0), .b(12'h5), .out(num6));  // open: cin, cout
  Adder #(.width(12)) adder_20 (.a(addr0), .b(12'h6), .out(num7));  // open: cin, cout
  Adder #(.width(12)) adder_21 (.a({4'b0000, Ypp}), .b(12'hffd), .out(adder_21_out));  // open: cin, cout
  Adder #(.width(12)) adder_22 (.a(addr3), .b({12{1'b0}}), .out(num22));  // open: cin, cout
  Adder #(.width(12)) adder_23 (.a(addr3), .b(12'h1), .out(num23));  // open: cin, cout
  Adder #(.width(12)) adder_24 (.a(addr3), .b(12'h2), .out(num24));  // open: cin, cout
  Adder #(.width(12)) adder_25 (.a(addr3), .b(12'h3), .out(num25));  // open: cin, cout
  Adder #(.width(12)) adder_26 (.a(addr3), .b(12'h4), .out(num26));  // open: cin, cout
  Adder #(.width(12)) adder_27 (.a(addr3), .b(12'h5), .out(num27));  // open: cin, cout
  Adder #(.width(12)) adder_28 (.a(addr3), .b(12'h6), .out(num28));  // open: cin, cout
  Adder #(.width(12)) adder_29 (.a({4'b0000, Xpp}), .b(12'hffd), .out(adder_29_out));  // open: cin, cout
  Multiplier #(.width(12)) multiplier_1 (.a(Width), .b(adder_21_out), .out(multiplier_1_out));  // open: cin, cout
  Adder #(.width(12)) adder_30 (.a(addr2), .b({12{1'b0}}), .out(num15));  // open: cin, cout
  Adder #(.width(12)) adder_31 (.a(addr2), .b(12'h1), .out(num16));  // open: cin, cout
  Adder #(.width(12)) adder_32 (.a(addr2), .b(12'h2), .out(num17));  // open: cin, cout
  Adder #(.width(12)) adder_33 (.a(addr2), .b(12'h3), .out(num18));  // open: cin, cout
  Adder #(.width(12)) adder_34 (.a(addr2), .b(12'h4), .out(num19));  // open: cin, cout
  Adder #(.width(12)) adder_35 (.a(addr2), .b(12'h5), .out(num20));  // open: cin, cout
  Adder #(.width(12)) adder_36 (.a(addr2), .b(12'h6), .out(num21));  // open: cin, cout
  Adder #(.width(12)) adder_37 (.a(addr5), .b({12{1'b0}}), .out(num36));  // open: cin, cout
  Adder #(.width(12)) adder_38 (.a(addr5), .b(12'h1), .out(num37));  // open: cin, cout
  Adder #(.width(12)) adder_39 (.a(addr5), .b(12'h2), .out(num38));  // open: cin, cout
  Adder #(.width(12)) adder_40 (.a(addr5), .b(12'h3), .out(num39));  // open: cin, cout
  Adder #(.width(12)) adder_41 (.a(addr5), .b(12'h4), .out(num40));  // open: cin, cout
  Adder #(.width(12)) adder_42 (.a(addr5), .b(12'h5), .out(num41));  // open: cin, cout
  Adder #(.width(12)) adder_43 (.a(addr5), .b(12'h6), .out(num42));  // open: cin, cout
  Adder #(.width(12)) adder_44 (.a(adder_29_out), .b(multiplier_1_out), .out(addr0));  // open: cin, cout
  Adder #(.width(12)) adder_45 (.a(addr4), .b({12{1'b0}}), .out(num29));  // open: cin, cout
  Adder #(.width(12)) adder_46 (.a(addr4), .b(12'h1), .out(num30));  // open: cin, cout
  Adder #(.width(12)) adder_47 (.a(addr4), .b(12'h2), .out(num31));  // open: cin, cout
  Adder #(.width(12)) adder_48 (.a(addr4), .b(12'h3), .out(num32));  // open: cin, cout
  Adder #(.width(12)) adder_49 (.a(addr4), .b(12'h4), .out(num33));  // open: cin, cout
  Adder #(.width(12)) adder_50 (.a(addr4), .b(12'h5), .out(num34));  // open: cin, cout
  Adder #(.width(12)) adder_51 (.a(addr4), .b(12'h6), .out(num35));  // open: cin, cout
  Adder #(.width(12)) adder_52 (.a(addr6), .b({12{1'b0}}), .out(num43));  // open: cin, cout
  Adder #(.width(12)) adder_53 (.a(addr6), .b(12'h1), .out(num44));  // open: cin, cout
  Adder #(.width(12)) adder_54 (.a(addr6), .b(12'h2), .out(num45));  // open: cin, cout
  Adder #(.width(12)) adder_55 (.a(addr6), .b(12'h3), .out(num46));  // open: cin, cout
  Adder #(.width(12)) adder_56 (.a(addr6), .b(12'h4), .out(num47));  // open: cin, cout
  Adder #(.width(12)) adder_57 (.a(addr6), .b(12'h5), .out(num48));  // open: cin, cout
  Adder #(.width(12)) adder_58 (.a(addr6), .b(12'h6), .out(num49));  // open: cin, cout
  maps maps_1 (.ADDR(No_of_map), .ELEM(num3), .DATA(out_18));  // open: Width, Height, Xpp, Ypp, LEN
  maps maps_2 (.ADDR(No_of_map), .ELEM(num4), .DATA(out_25));  // open: Width, Height, Xpp, Ypp, LEN
  maps maps_3 (.ADDR(No_of_map), .ELEM(num5), .DATA(out_32));  // open: Width, Height, Xpp, Ypp, LEN
  maps maps_4 (.ADDR(No_of_map), .ELEM(num6), .DATA(out_39));  // open: Width, Height, Xpp, Ypp, LEN
  maps maps_5 (.ADDR(No_of_map), .ELEM(num7), .DATA(out_46));  // open: Width, Height, Xpp, Ypp, LEN
  maps maps_6 (.ADDR(No_of_map), .ELEM(num1), .Width(Width), .DATA(out_4));  // open: Height, Xpp, Ypp, LEN
  maps maps_7 (.ADDR(No_of_map), .ELEM(num2), .DATA(out_11));  // open: Width, Height, Xpp, Ypp, LEN
  maps maps_8 (.ADDR(No_of_map), .ELEM(num8), .DATA(out_5));  // open: Width, Height, Xpp, Ypp, LEN
  maps maps_9 (.ADDR(No_of_map), .ELEM(num9), .DATA(out_12));  // open: Width, Height, Xpp, Ypp, LEN
  maps maps_10 (.ADDR(No_of_map), .ELEM(num10), .DATA(out_19));  // open: Width, Height, Xpp, Ypp, LEN
  maps maps_11 (.ADDR(No_of_map), .ELEM(num11), .DATA(out_26));  // open: Width, Height, Xpp, Ypp, LEN
  maps maps_12 (.ADDR(No_of_map), .ELEM(num12), .DATA(out_33));  // open: Width, Height, Xpp, Ypp, LEN
  maps maps_13 (.ADDR(No_of_map), .ELEM(num13), .DATA(out_40));  // open: Width, Height, Xpp, Ypp, LEN
  maps maps_14 (.ADDR(No_of_map), .ELEM(num14), .DATA(out_47));  // open: Width, Height, Xpp, Ypp, LEN
  maps maps_15 (.ADDR(No_of_map), .ELEM(num15), .DATA(out_6));  // open: Width, Height, Xpp, Ypp, LEN
  maps maps_16 (.ADDR(No_of_map), .ELEM(num16), .DATA(out_13));  // open: Width, Height, Xpp, Ypp, LEN
  maps maps_17 (.ADDR(No_of_map), .ELEM(num17), .DATA(out_20));  // open: Width, Height, Xpp, Ypp, LEN
  maps maps_18 (.ADDR(No_of_map), .ELEM(num18), .DATA(out_27));  // open: Width, Height, Xpp, Ypp, LEN
  maps maps_19 (.ADDR(No_of_map), .ELEM(num19), .DATA(out_34));  // open: Width, Height, Xpp, Ypp, LEN
  maps maps_20 (.ADDR(No_of_map), .ELEM(num20), .DATA(out_41));  // open: Width, Height, Xpp, Ypp, LEN
  maps maps_21 (.ADDR(No_of_map), .ELEM(num21), .DATA(out_48));  // open: Width, Height, Xpp, Ypp, LEN
  maps maps_22 (.ADDR(No_of_map), .ELEM(num22), .DATA(out_7));  // open: Width, Height, Xpp, Ypp, LEN
  maps maps_23 (.ADDR(No_of_map), .ELEM(num23), .DATA(out_14));  // open: Width, Height, Xpp, Ypp, LEN
  maps maps_24 (.ADDR(No_of_map), .ELEM(num24), .DATA(out_21));  // open: Width, Height, Xpp, Ypp, LEN
  maps maps_25 (.ADDR(No_of_map), .ELEM(num25), .DATA(out_28));  // open: Width, Height, Xpp, Ypp, LEN
  maps maps_26 (.ADDR(No_of_map), .ELEM(num26), .DATA(out_35));  // open: Width, Height, Xpp, Ypp, LEN
  maps maps_27 (.ADDR(No_of_map), .ELEM(num27), .DATA(out_42));  // open: Width, Height, Xpp, Ypp, LEN
  maps maps_28 (.ADDR(No_of_map), .ELEM(num28), .DATA(out_49));  // open: Width, Height, Xpp, Ypp, LEN
  maps maps_29 (.ADDR(No_of_map), .ELEM(num29), .DATA(out_8));  // open: Width, Height, Xpp, Ypp, LEN
  maps maps_30 (.ADDR(No_of_map), .ELEM(num30), .DATA(out_15));  // open: Width, Height, Xpp, Ypp, LEN
  maps maps_31 (.ADDR(No_of_map), .ELEM(num31), .DATA(out_22));  // open: Width, Height, Xpp, Ypp, LEN
  maps maps_32 (.ADDR(No_of_map), .ELEM(num32), .DATA(out_29));  // open: Width, Height, Xpp, Ypp, LEN
  maps maps_33 (.ADDR(No_of_map), .ELEM(num33), .DATA(out_36));  // open: Width, Height, Xpp, Ypp, LEN
  maps maps_34 (.ADDR(No_of_map), .ELEM(num34), .DATA(out_43));  // open: Width, Height, Xpp, Ypp, LEN
  maps maps_35 (.ADDR(No_of_map), .ELEM(num35), .DATA(out_50));  // open: Width, Height, Xpp, Ypp, LEN
  maps maps_36 (.ADDR(No_of_map), .ELEM(num36), .DATA(out_9));  // open: Width, Height, Xpp, Ypp, LEN
  maps maps_37 (.ADDR(No_of_map), .ELEM(num37), .DATA(out_16));  // open: Width, Height, Xpp, Ypp, LEN
  maps maps_38 (.ADDR(No_of_map), .ELEM(num38), .DATA(out_23));  // open: Width, Height, Xpp, Ypp, LEN
  maps maps_39 (.ADDR(No_of_map), .ELEM(num39), .DATA(out_30));  // open: Width, Height, Xpp, Ypp, LEN
  maps maps_40 (.ADDR(No_of_map), .ELEM(num40), .DATA(out_37));  // open: Width, Height, Xpp, Ypp, LEN
  maps maps_41 (.ADDR(No_of_map), .ELEM(num41), .DATA(out_44));  // open: Width, Height, Xpp, Ypp, LEN
  maps maps_42 (.ADDR(No_of_map), .ELEM(num42), .DATA(out_51));  // open: Width, Height, Xpp, Ypp, LEN
  maps maps_43 (.ADDR(No_of_map), .ELEM(num43), .DATA(out_10));  // open: Width, Height, Xpp, Ypp, LEN
  maps maps_44 (.ADDR(No_of_map), .ELEM(num44), .DATA(out_17));  // open: Width, Height, Xpp, Ypp, LEN
  maps maps_45 (.ADDR(No_of_map), .ELEM(num45), .DATA(out_24));  // open: Width, Height, Xpp, Ypp, LEN
  maps maps_46 (.ADDR(No_of_map), .ELEM(num46), .DATA(out_31));  // open: Width, Height, Xpp, Ypp, LEN
  maps maps_47 (.ADDR(No_of_map), .ELEM(num47), .DATA(out_38));  // open: Width, Height, Xpp, Ypp, LEN
  maps maps_48 (.ADDR(No_of_map), .ELEM(num48), .DATA(out_45));  // open: Width, Height, Xpp, Ypp, LEN
  maps maps_49 (.ADDR(No_of_map), .ELEM(num49), .DATA(out_52));  // open: Width, Height, Xpp, Ypp, LEN

  // Other names for the same wires on the sheet: No[7:0] = No_of_map
endmodule

module driver_mm (
  input  [25:0] Bus1,
  input  [16:0] Bus2,
  output [17:0] out_3,
  output [17:0] out_4,
  output [17:0] out_5,
  output [17:0] out_6,
  output [17:0] out_7,
  output [17:0] out_8,
  output [15:0] out_9,
  output [13:0] out_10,
  output [15:0] out_11,
  output [17:0] out_12,
  output [15:0] out_13,
  output [13:0] out_14,
  output [15:0] out_15,
  output [17:0] out_16,
  output [13:0] out_17,
  output [15:0] out_18,
  output [13:0] out_19,
  output [17:0] out_20,
  output [15:0] out_21,
  output [13:0] out_22,
  output [17:0] out_23,
  output [15:0] out_24,
  output [13:0] out_25,
  output [15:0] out_26,
  output [13:0] out_27,
  output [17:0] out_28,
  output [13:0] out_29,
  output [15:0] out_30,
  output [17:0] out_31,
  output [13:0] out_32,
  output [15:0] out_33,
  output [13:0] out_34,
  output [17:0] out_35,
  output [15:0] out_36,
  output [13:0] out_37,
  output [15:0] out_38,
  output [17:0] out_39,
  output [13:0] out_40,
  output [15:0] out_41,
  output [13:0] out_42,
  output [17:0] out_43,
  output [15:0] out_44,
  output [13:0] out_45,
  output [1:0] out_46,
  output [1:0] out_47,
  output [17:0] out_48,
  output [15:0] out_49,
  output [15:0] out_50,
  output [17:0] out_51,
  output [17:0] out_52,
  output [8:0] To_print3D_walls
);

  wire _1_3, _1_exit, _2_3, _2_exit, _3_1, _3_2, _3_4, _3_5, _3_exit, _4_3, _4_exit, _5_3, _5_exit, _6_exit,
       _7_exit, _8_exit, m_1_0, m_1_1, m_1_2, m_1_3, m_1_4, m_1_5, m_1_6, m_2_0, m_2_1, m_2_2, m_2_3, m_2_4,
       m_2_5, m_2_6, m_3_0, m_3_1, m_3_2, m_3_3, m_3_4, m_3_5, m_3_6, m_4_0, m_4_1, m_4_2, m_4_3, m_4_4,
       m_4_5, m_4_6, m_5_0, m_5_1, m_5_2, m_5_3, m_5_4, m_5_5, m_5_6, m_6_0, m_6_1, m_6_2, m_6_3, m_6_4,
       m_6_5, m_6_6, m__0_0, m__0_1, m__0_2, m__0_3, m__0_4, m__0_5, m__0_6;
  wire [7:0] char1, char2, char3, char4, char5, char6, char7, char8, char9, char10, char11, char12, char13,
       char14, char15, char16, char17, char18, char19, char20, char21, char22, char23, char24, char25,
       char26, char27, char28, char29, char30, char31, char32, char33, char34, char35, char36, char37,
       char38, char39, char40, char41, char42, char43, char44, char45, char46, char47, char48, char49;
  wire [8:0] multiplexer_8_out;

  plr_in_cond_of_dir plr_in_cond_of_dir_1 (.in_1(Bus1[25:24]), .out_2(out_46), .out_3(out_47));
  mmap_matrix mmap_matrix_1 (
    .Xpp(Bus1[7:0]), .Ypp(Bus1[15:8]), .out_4(char1), .out_5(char8), .out_6(char15), .out_7(char22),
    .out_8(char29), .out_9(char36), .out_10(char43), .out_11(char2), .out_12(char9), .out_13(char16),
    .out_14(char23), .out_15(char30), .out_16(char37), .out_17(char44), .out_18(char3), .out_19(char10),
    .out_20(char17), .out_21(char24), .out_22(char31), .out_23(char38), .out_24(char45), .out_25(char4),
    .out_26(char11), .out_27(char18), .out_28(char25), .out_29(char32), .out_30(char39), .out_31(char46),
    .out_32(char5), .out_33(char12), .out_34(char19), .out_35(char26), .out_36(char33), .out_37(char40),
    .out_38(char47), .out_39(char6), .out_40(char13), .out_41(char20), .out_42(char27), .out_43(char34),
    .out_44(char41), .out_45(char48), .out_46(char7), .out_47(char14), .out_48(char21), .out_49(char28),
    .out_50(char35), .out_51(char42), .out_52(char49), .No_of_map(Bus1[23:16]));
  cond_en_weap cond_en_weap_1 (.input_char(Bus2[1:0]), .todisplay(_3_4), .Exit(_7_exit));
  cond_en_weap cond_en_weap_2 (.input_char(Bus2[3:2]), .todisplay(_3_2), .Exit(_2_exit));
  cond_en_weap cond_en_weap_3 (.input_char(Bus2[5:4]), .todisplay(_2_3), .Exit(_4_exit));
  cond_en_weap cond_en_weap_4 (.input_char(Bus2[7:6]), .todisplay(_4_3), .Exit(_5_exit));
  cond_en_weap cond_en_weap_5 (.input_char(Bus2[9:8]), .todisplay(_5_3), .Exit(_6_exit));
  cond_en_weap cond_en_weap_6 (.input_char(Bus2[11:10]), .todisplay(_1_3), .Exit(_3_exit));
  cond_en_weap cond_en_weap_7 (.input_char(Bus2[13:12]), .todisplay(_3_5), .Exit(_8_exit));
  cond_en_weap cond_en_weap_8 (.input_char(Bus2[15:14]), .todisplay(_3_1), .Exit(_1_exit));
  Multiplexer #(.width(18), .enable("false")) multiplexer_1 (
    .in0({18{1'b0}}), .in1({18{1'b0}}), .out(out_6), .sel(Bus2[16]));
  Multiplexer #(.width(18), .enable("false")) multiplexer_2 (
    .in0({18{1'b0}}), .in1({{8{1'b0}}, {2{_3_5}}, {8{1'b0}}}), .out(out_12), .sel(Bus2[16]));
  Multiplexer #(.width(18), .enable("false")) multiplexer_3 (
    .in0({18{1'b0}}), .in1({{8{1'b0}}, {2{_3_4}}, {8{1'b0}}}), .out(out_20), .sel(Bus2[16]));
  Multiplexer #(.width(18), .enable("false")) multiplexer_4 (
    .in0({18{1'b0}}), .in1({4'b0000, {2{_1_3}}, {2{_2_3}}, 2'b00, {2{_4_3}}, {2{_5_3}}, 4'b0000}),
    .out(out_28), .sel(Bus2[16]));
  Multiplexer #(.width(18), .enable("false")) multiplexer_5 (
    .in0({18{1'b0}}), .in1({{8{1'b0}}, {2{_3_2}}, {8{1'b0}}}), .out(out_35), .sel(Bus2[16]));
  Multiplexer #(.width(18), .enable("false")) multiplexer_6 (
    .in0({18{1'b0}}), .in1({{8{1'b0}}, {2{_3_1}}, {8{1'b0}}}), .out(out_43), .sel(Bus2[16]));
  Multiplexer #(.width(18), .enable("false")) multiplexer_7 (
    .in0({18{1'b0}}), .in1({18{1'b0}}), .out(out_51), .sel(Bus2[16]));
  Multiplexer #(.select(2), .width(9), .enable("false")) multiplexer_8 (
    .in0({m_3_2, m_3_4, m_2_2, m_2_4, m_1_2, m_1_4, m__0_2, m__0_3, m__0_4}),
    .in1({m_4_3, m_2_3, m_4_2, m_2_2, m_4_1, m_2_1, m_4_0, m_3_0, m_2_0}),
    .in2({m_3_4, m_3_2, m_4_4, m_4_2, m_5_4, m_5_2, m_6_4, m_6_3, m_6_2}),
    .in3({m_2_3, m_4_3, m_2_4, m_4_4, m_2_5, m_4_5, m_2_6, m_3_6, m_4_6}), .out(multiplexer_8_out),
    .sel(Bus1[25:24]));
  assign To_print3D_walls = ~multiplexer_8_out;  // NOT_Gate not_1, 9 bits wide
  cond_wall_pass cond_wall_pass_1 (.in_1(char1), .out(m__0_6));
  cond_wall_pass cond_wall_pass_2 (.in_1(char2), .out(m__0_5));
  cond_wall_pass cond_wall_pass_3 (.in_1(char3), .out(m__0_4));
  cond_wall_pass cond_wall_pass_4 (.in_1(char4), .out(m__0_3));
  cond_wall_pass cond_wall_pass_5 (.in_1(char5), .out(m__0_2));
  cond_wall_pass cond_wall_pass_6 (.in_1(char6), .out(m__0_1));
  cond_wall_pass cond_wall_pass_7 (.in_1(char7), .out(m__0_0));
  cond_wall_pass cond_wall_pass_8 (.in_1(char8), .out(m_1_6));
  cond_wall_pass cond_wall_pass_9 (.in_1(char9), .out(m_1_5));
  cond_wall_pass cond_wall_pass_10 (.in_1(char10), .out(m_1_4));
  cond_wall_pass cond_wall_pass_11 (.in_1(char11), .out(m_1_3));
  cond_wall_pass cond_wall_pass_12 (.in_1(char12), .out(m_1_2));
  cond_wall_pass cond_wall_pass_13 (.in_1(char13), .out(m_1_1));
  cond_wall_pass cond_wall_pass_14 (.in_1(char14), .out(m_1_0));
  cond_wall_pass cond_wall_pass_15 (.in_1(char15), .out(m_2_6));
  cond_wall_pass cond_wall_pass_16 (.in_1(char16), .out(m_2_5));
  cond_wall_pass cond_wall_pass_17 (.in_1(char17), .out(m_2_4));
  cond_wall_pass cond_wall_pass_18 (.in_1(char18), .out(m_2_3));
  cond_wall_pass cond_wall_pass_19 (.in_1(char19), .out(m_2_2));
  cond_wall_pass cond_wall_pass_20 (.in_1(char20), .out(m_2_1));
  cond_wall_pass cond_wall_pass_21 (.in_1(char21), .out(m_2_0));
  cond_wall_pass cond_wall_pass_22 (.in_1(char22), .out(m_3_6));
  cond_wall_pass cond_wall_pass_23 (.in_1(char23), .out(m_3_5));
  cond_wall_pass cond_wall_pass_24 (.in_1(char24), .out(m_3_4));
  cond_wall_pass cond_wall_pass_25 (.in_1(char25), .out(m_3_3));
  cond_wall_pass cond_wall_pass_26 (.in_1(char26), .out(m_3_2));
  cond_wall_pass cond_wall_pass_27 (.in_1(char27), .out(m_3_1));
  cond_wall_pass cond_wall_pass_28 (.in_1(char28), .out(m_3_0));
  cond_wall_pass cond_wall_pass_29 (.in_1(char29), .out(m_4_6));
  cond_wall_pass cond_wall_pass_30 (.in_1(char30), .out(m_4_5));
  cond_wall_pass cond_wall_pass_31 (.in_1(char31), .out(m_4_4));
  cond_wall_pass cond_wall_pass_32 (.in_1(char32), .out(m_4_3));
  cond_wall_pass cond_wall_pass_33 (.in_1(char33), .out(m_4_2));
  cond_wall_pass cond_wall_pass_34 (.in_1(char34), .out(m_4_1));
  cond_wall_pass cond_wall_pass_35 (.in_1(char35), .out(m_4_0));
  cond_wall_pass cond_wall_pass_36 (.in_1(char36), .out(m_5_6));
  cond_wall_pass cond_wall_pass_37 (.in_1(char37), .out(m_5_5));
  cond_wall_pass cond_wall_pass_38 (.in_1(char38), .out(m_5_4));
  cond_wall_pass cond_wall_pass_39 (.in_1(char39), .out(m_5_3));
  cond_wall_pass cond_wall_pass_40 (.in_1(char40), .out(m_5_2));
  cond_wall_pass cond_wall_pass_41 (.in_1(char41), .out(m_5_1));
  cond_wall_pass cond_wall_pass_42 (.in_1(char42), .out(m_5_0));
  cond_wall_pass cond_wall_pass_43 (.in_1(char43), .out(m_6_6));
  cond_wall_pass cond_wall_pass_44 (.in_1(char44), .out(m_6_5));
  cond_wall_pass cond_wall_pass_45 (.in_1(char45), .out(m_6_4));
  cond_wall_pass cond_wall_pass_46 (.in_1(char46), .out(m_6_3));
  cond_wall_pass cond_wall_pass_47 (.in_1(char47), .out(m_6_2));
  cond_wall_pass cond_wall_pass_48 (.in_1(char48), .out(m_6_1));
  cond_wall_pass cond_wall_pass_49 (.in_1(char49), .out(m_6_0));
  Multiplexer #(.width(14), .enable("false")) multiplexer_9 (
    .in0({14{1'b1}}),
    .in1({{2{m__0_6}}, {2{m__0_5}}, {2{m__0_4}}, {2{m__0_3}}, {2{m__0_2}}, {2{m__0_1}}, {2{m__0_0}}}),
    .out(out_10), .sel(Bus2[16]));
  Multiplexer #(.width(14), .enable("false")) multiplexer_10 (
    .in0({14{1'b1}}),
    .in1({{2{m_1_6}}, {2{m_1_5}}, {2{m_1_4}}, {2{m_1_3}}, {2{m_1_2}}, {2{m_1_1}}, {2{m_1_0}}}), .out(out_17),
    .sel(Bus2[16]));
  Multiplexer #(.width(14), .enable("false")) multiplexer_11 (
    .in0({14{1'b1}}),
    .in1({{2{m_2_6}}, {2{m_2_5}}, {2{m_2_4}}, {2{m_2_3}}, {2{m_2_2}}, {2{m_2_1}}, {2{m_2_0}}}), .out(out_22),
    .sel(Bus2[16]));
  Multiplexer #(.width(14), .enable("false")) multiplexer_12 (
    .in0({14{1'b1}}),
    .in1({{2{m_3_6}}, {2{m_3_5}}, {2{m_3_4}}, {2{m_3_3}}, {2{m_3_2}}, {2{m_3_1}}, {2{m_3_0}}}), .out(out_27),
    .sel(Bus2[16]));
  Multiplexer #(.width(14), .enable("false")) multiplexer_13 (
    .in0({14{1'b1}}),
    .in1({{2{m_4_6}}, {2{m_4_5}}, {2{m_4_4}}, {2{m_4_3}}, {2{m_4_2}}, {2{m_4_1}}, {2{m_4_0}}}), .out(out_32),
    .sel(Bus2[16]));
  Multiplexer #(.width(14), .enable("false")) multiplexer_14 (
    .in0({14{1'b1}}),
    .in1({{2{m_5_6}}, {2{m_5_5}}, {2{m_5_4}}, {2{m_5_3}}, {2{m_5_2}}, {2{m_5_1}}, {2{m_5_0}}}), .out(out_37),
    .sel(Bus2[16]));
  Multiplexer #(.width(14), .enable("false")) multiplexer_15 (
    .in0({14{1'b1}}),
    .in1({{2{m_6_6}}, {2{m_6_5}}, {2{m_6_4}}, {2{m_6_3}}, {2{m_6_2}}, {2{m_6_1}}, {2{m_6_0}}}), .out(out_42),
    .sel(Bus2[16]));
  Multiplexer #(.width(16), .enable("false")) multiplexer_16 (
    .in0({16{1'b0}}), .in1({16{1'b0}}), .out(out_13), .sel(Bus2[16]));
  Multiplexer #(.width(16), .enable("false")) multiplexer_17 (
    .in0({16{1'b0}}), .in1({{7{1'b0}}, {2{_8_exit}}, {7{1'b0}}}), .out(out_18), .sel(Bus2[16]));
  Multiplexer #(.width(16), .enable("false")) multiplexer_18 (
    .in0({16{1'b0}}), .in1({{7{1'b0}}, {2{_7_exit}}, {7{1'b0}}}), .out(out_24), .sel(Bus2[16]));
  Multiplexer #(.width(16), .enable("false")) multiplexer_19 (
    .in0({16{1'b0}}), .in1({3'b000, {2{_3_exit}}, {2{_4_exit}}, 2'b00, {2{_5_exit}}, {2{_6_exit}}, 3'b000}),
    .out(out_30), .sel(Bus2[16]));
  Multiplexer #(.width(16), .enable("false")) multiplexer_20 (
    .in0({16{1'b0}}), .in1({{7{1'b0}}, {2{_2_exit}}, {7{1'b0}}}), .out(out_36), .sel(Bus2[16]));
  Multiplexer #(.width(16), .enable("false")) multiplexer_21 (
    .in0({16{1'b0}}), .in1({{7{1'b0}}, {2{_1_exit}}, {7{1'b0}}}), .out(out_41), .sel(Bus2[16]));
  Multiplexer #(.width(16), .enable("false")) multiplexer_22 (
    .in0({16{1'b0}}), .in1({16{1'b0}}), .out(out_49), .sel(Bus2[16]));

  assign out_3 = {18{1'b0}};
  assign out_4 = {18{1'b0}};
  assign out_5 = {18{1'b0}};
  assign out_7 = {18{1'b0}};
  assign out_8 = out_6;
  assign out_9 = {16{1'b0}};
  assign out_11 = {16{1'b0}};
  assign out_14 = out_10;
  assign out_15 = out_13;
  assign out_16 = out_12;
  assign out_19 = out_17;
  assign out_21 = out_18;
  assign out_23 = out_20;
  assign out_25 = out_22;
  assign out_26 = out_24;
  assign out_29 = out_27;
  assign out_31 = out_28;
  assign out_33 = out_30;
  assign out_34 = out_32;
  assign out_38 = out_36;
  assign out_39 = out_35;
  assign out_40 = out_37;
  assign out_44 = out_41;
  assign out_45 = out_42;
  assign out_48 = out_43;
  assign out_50 = out_49;
  assign out_52 = out_51;

  // Other names for the same wires on the sheet: p_x_y_1[1:0] = Bus2[1:0]; p_x__y_1[1:0] = Bus2[3:2];
  //   p_x_1__y_t[1:0] = Bus2[5:4]; p_x_1__y[1:0] = Bus2[7:6]; p_x_2__y[1:0] = Bus2[9:8];
  //   p_x_2__y_t[1:0] = Bus2[11:10]; p_x__y_2_t[1:0] = Bus2[13:12]; p_x__y_2[1:0] = Bus2[15:14]; gs1 = Bus2[16];
  //   Direction[1:0] = Bus1[25:24]; mapLevelCurrent[7:0] = Bus1[23:16]; X[7:0] = Bus1[7:0]; Y[7:0] = Bus1[15:8]

  // Notes on the sheet:
  //   0 dir
  //   Big matrix(enemy/weapon)
  //   1 dir
  //   2 dir
  //   3 dir
  //   Small Matrix(wall/pass)
  //   Exit_Matrix
endmodule

module cond_dir_to3d (
  input  [1:0] dir,
  output _0,
  output _1,
  output _2,
  output _3
);

  Demultiplexer #(.select(2), .enable("false")) demultiplexer_1 (
    .out0(_0), .out1(_1), .out2(_2), .out3(_3), .in(1'b1), .sel(dir));
endmodule

module lookup_onMMap (
  input  [16:0] in_1,
  input  [25:0] in_2,
  input  [16:0] in_3,
  input  [25:0] in_4,
  input  [16:0] in_5,
  input  [25:0] in_6,
  input  [16:0] in_7,
  input  [25:0] in_8
);

  wire [8:0] b, driver_mm_3_to_print3d_walls;
  wire [15:0] driver_mm_2_out_9, driver_mm_2_out_11, driver_mm_2_out_13, driver_mm_2_out_15,
       driver_mm_2_out_18, driver_mm_2_out_21, driver_mm_2_out_24, driver_mm_2_out_26, driver_mm_2_out_30,
       driver_mm_2_out_33, driver_mm_2_out_36, driver_mm_2_out_38, driver_mm_2_out_41, driver_mm_2_out_44,
       driver_mm_2_out_49, driver_mm_2_out_50, driver_mm_3_out_9, driver_mm_3_out_11, driver_mm_3_out_13,
       driver_mm_3_out_15, driver_mm_3_out_18, driver_mm_3_out_21, driver_mm_3_out_24, driver_mm_3_out_26,
       driver_mm_3_out_30, driver_mm_3_out_33, driver_mm_3_out_36, driver_mm_3_out_38, driver_mm_3_out_41,
       driver_mm_3_out_44, driver_mm_3_out_49, driver_mm_3_out_50;
  wire [17:0] driver_mm_2_out_3, driver_mm_2_out_4, driver_mm_2_out_5, driver_mm_2_out_6, driver_mm_2_out_7,
       driver_mm_2_out_8, driver_mm_2_out_12, driver_mm_2_out_16, driver_mm_2_out_20, driver_mm_2_out_23,
       driver_mm_2_out_28, driver_mm_2_out_31, driver_mm_2_out_35, driver_mm_2_out_39, driver_mm_2_out_43,
       driver_mm_2_out_48, driver_mm_2_out_51, driver_mm_2_out_52, driver_mm_3_out_3, driver_mm_3_out_4,
       driver_mm_3_out_5, driver_mm_3_out_6, driver_mm_3_out_7, driver_mm_3_out_8, driver_mm_3_out_12,
       driver_mm_3_out_16, driver_mm_3_out_20, driver_mm_3_out_23, driver_mm_3_out_28, driver_mm_3_out_31,
       driver_mm_3_out_35, driver_mm_3_out_39, driver_mm_3_out_43, driver_mm_3_out_48, driver_mm_3_out_51,
       driver_mm_3_out_52, driver_mm_4_out_3, driver_mm_4_out_4, driver_mm_4_out_5, driver_mm_4_out_6,
       driver_mm_4_out_7, driver_mm_4_out_8, driver_mm_4_out_12, driver_mm_4_out_16, driver_mm_4_out_20,
       driver_mm_4_out_23, driver_mm_4_out_28, driver_mm_4_out_31, driver_mm_4_out_35, driver_mm_4_out_39,
       driver_mm_4_out_43, driver_mm_4_out_48, driver_mm_4_out_51, driver_mm_4_out_52;

  DotMatrix #(.inputtype("row"), .matrixcols(16), .matrixrows(16)) dotmatrix_1 (
    .row0({16{1'b1}}), .row1({16{1'b1}}), .row2({16{1'b1}}), .row3({16{1'b1}}), .row4({16{1'b1}}),
    .row5({16{1'b1}}), .row6({16{1'b1}}), .row7({16{1'b1}}), .row8({16{1'b1}}), .row9({16{1'b1}}),
    .row10({16{1'b1}}), .row11({16{1'b1}}), .row12({16{1'b1}}), .row13({16{1'b1}}), .row14({16{1'b1}}),
    .row15({16{1'b0}}));
  DotMatrix #(.inputtype("row"), .matrixcols(18), .matrixrows(18)) dotmatrix_2 (
    .row0({18{1'b1}}), .row1({18{1'b1}}), .row2({18{1'b1}}), .row3({18{1'b1}}), .row4({18{1'b1}}),
    .row5({18{1'b1}}), .row6({18{1'b1}}), .row7({18{1'b1}}), .row8({18{1'b1}}), .row9({18{1'b1}}),
    .row10({18{1'b1}}), .row11({18{1'b1}}), .row12({18{1'b1}}), .row13({18{1'b1}}), .row14({18{1'b1}}),
    .row15({18{1'b1}}), .row16({18{1'b1}}), .row17({18{1'b0}}));
  driver_mm driver_mm_1 ();  // open: Bus1, Bus2, out_3, out_4, out_5, out_7, out_6, out_8, out_10, out_12, out_14, out_16, out_17, out_19, out_20, out_22, out_23, out_25, out_46, out_27, out_47, out_28, out_29, out_31, out_32, out_34, out_35, out_37, out_39, out_40, out_42, out_43, out_45, out_48, out_51, out_52, To_print3D_walls, out_13, out_15, out_18, out_21, out_24, out_26, out_30, out_33, out_36, out_38, out_41, out_44, out_49, out_50, out_9, out_11
  DotMatrix #(.inputtype("row"), .matrixcols(2), .matrixrows(2)) dotmatrix_3 (.row0(2'b11), .row1(2'b00));
  DotMatrix #(.inputtype("row"), .matrixcols(14), .matrixrows(14)) dotmatrix_4 (
    .row0({14{1'b1}}), .row1({14{1'b1}}), .row2({14{1'b1}}), .row3({14{1'b1}}), .row4({14{1'b1}}),
    .row5({14{1'b1}}), .row6({14{1'b1}}), .row7({14{1'b1}}), .row8({14{1'b1}}), .row9({14{1'b1}}),
    .row10({14{1'b1}}), .row11({14{1'b1}}), .row12({14{1'b1}}), .row13({14{1'b0}}));
  DotMatrix #(.inputtype("row"), .matrixcols(18), .matrixrows(18)) dotmatrix_5 (
    .row0(driver_mm_2_out_3), .row1(driver_mm_2_out_4), .row2(driver_mm_2_out_6), .row3(driver_mm_2_out_8),
    .row4(driver_mm_2_out_12), .row5(driver_mm_2_out_16), .row6(driver_mm_2_out_20),
    .row7(driver_mm_2_out_23), .row8(driver_mm_2_out_28), .row9(driver_mm_2_out_31),
    .row10(driver_mm_2_out_35), .row11(driver_mm_2_out_39), .row12(driver_mm_2_out_43),
    .row13(driver_mm_2_out_48), .row14(driver_mm_2_out_51), .row15(driver_mm_2_out_52),
    .row16(driver_mm_2_out_5), .row17(driver_mm_2_out_7));
  driver_mm driver_mm_2 (
    .Bus1(in_2), .Bus2(in_1), .out_3(driver_mm_2_out_3), .out_4(driver_mm_2_out_4),
    .out_5(driver_mm_2_out_5), .out_7(driver_mm_2_out_7), .out_6(driver_mm_2_out_6),
    .out_8(driver_mm_2_out_8), .out_12(driver_mm_2_out_12), .out_16(driver_mm_2_out_16),
    .out_20(driver_mm_2_out_20), .out_23(driver_mm_2_out_23), .out_28(driver_mm_2_out_28),
    .out_31(driver_mm_2_out_31), .out_35(driver_mm_2_out_35), .out_39(driver_mm_2_out_39),
    .out_43(driver_mm_2_out_43), .out_48(driver_mm_2_out_48), .out_51(driver_mm_2_out_51),
    .out_52(driver_mm_2_out_52), .To_print3D_walls(b), .out_13(driver_mm_2_out_13),
    .out_15(driver_mm_2_out_15), .out_18(driver_mm_2_out_18), .out_21(driver_mm_2_out_21),
    .out_24(driver_mm_2_out_24), .out_26(driver_mm_2_out_26), .out_30(driver_mm_2_out_30),
    .out_33(driver_mm_2_out_33), .out_36(driver_mm_2_out_36), .out_38(driver_mm_2_out_38),
    .out_41(driver_mm_2_out_41), .out_44(driver_mm_2_out_44), .out_49(driver_mm_2_out_49),
    .out_50(driver_mm_2_out_50), .out_9(driver_mm_2_out_9), .out_11(driver_mm_2_out_11));  // open: out_10, out_14, out_17, out_19, out_22, out_25, out_46, out_27, out_47, out_29, out_32, out_34, out_37, out_40, out_42, out_45
  DotMatrix #(.inputtype("row"), .matrixcols(16), .matrixrows(16)) dotmatrix_6 (
    .row0(driver_mm_2_out_9), .row1(driver_mm_2_out_13), .row2(driver_mm_2_out_15),
    .row3(driver_mm_2_out_18), .row4(driver_mm_2_out_21), .row5(driver_mm_2_out_24),
    .row6(driver_mm_2_out_26), .row7(driver_mm_2_out_30), .row8(driver_mm_2_out_33),
    .row9(driver_mm_2_out_36), .row10(driver_mm_2_out_38), .row11(driver_mm_2_out_41),
    .row12(driver_mm_2_out_44), .row13(driver_mm_2_out_49), .row14(driver_mm_2_out_50),
    .row15(driver_mm_2_out_11));
  driver_mm driver_mm_3 (
    .Bus1(in_6), .Bus2(in_5), .out_3(driver_mm_3_out_3), .out_4(driver_mm_3_out_4),
    .out_5(driver_mm_3_out_5), .out_7(driver_mm_3_out_7), .out_6(driver_mm_3_out_6),
    .out_8(driver_mm_3_out_8), .out_12(driver_mm_3_out_12), .out_16(driver_mm_3_out_16),
    .out_20(driver_mm_3_out_20), .out_23(driver_mm_3_out_23), .out_28(driver_mm_3_out_28),
    .out_31(driver_mm_3_out_31), .out_35(driver_mm_3_out_35), .out_39(driver_mm_3_out_39),
    .out_43(driver_mm_3_out_43), .out_48(driver_mm_3_out_48), .out_51(driver_mm_3_out_51),
    .out_52(driver_mm_3_out_52), .To_print3D_walls(driver_mm_3_to_print3d_walls),
    .out_13(driver_mm_3_out_13), .out_15(driver_mm_3_out_15), .out_18(driver_mm_3_out_18),
    .out_21(driver_mm_3_out_21), .out_24(driver_mm_3_out_24), .out_26(driver_mm_3_out_26),
    .out_30(driver_mm_3_out_30), .out_33(driver_mm_3_out_33), .out_36(driver_mm_3_out_36),
    .out_38(driver_mm_3_out_38), .out_41(driver_mm_3_out_41), .out_44(driver_mm_3_out_44),
    .out_49(driver_mm_3_out_49), .out_50(driver_mm_3_out_50), .out_9(driver_mm_3_out_9),
    .out_11(driver_mm_3_out_11));  // open: out_10, out_14, out_17, out_19, out_22, out_25, out_46, out_27, out_47, out_29, out_32, out_34, out_37, out_40, out_42, out_45
  DotMatrix #(.inputtype("row"), .matrixcols(18), .matrixrows(18)) dotmatrix_7 (
    .row0(driver_mm_3_out_3), .row1(driver_mm_3_out_4), .row2(driver_mm_3_out_6), .row3(driver_mm_3_out_8),
    .row4(driver_mm_3_out_12), .row5(driver_mm_3_out_16), .row6(driver_mm_3_out_20),
    .row7(driver_mm_3_out_23), .row8(driver_mm_3_out_28), .row9(driver_mm_3_out_31),
    .row10(driver_mm_3_out_35), .row11(driver_mm_3_out_39), .row12(driver_mm_3_out_43),
    .row13(driver_mm_3_out_48), .row14(driver_mm_3_out_51), .row15(driver_mm_3_out_52),
    .row16(driver_mm_3_out_5), .row17(driver_mm_3_out_7));
  DotMatrix #(.inputtype("row"), .matrixcols(16), .matrixrows(16)) dotmatrix_8 (
    .row0(driver_mm_3_out_9), .row1(driver_mm_3_out_13), .row2(driver_mm_3_out_15),
    .row3(driver_mm_3_out_18), .row4(driver_mm_3_out_21), .row5(driver_mm_3_out_24),
    .row6(driver_mm_3_out_26), .row7(driver_mm_3_out_30), .row8(driver_mm_3_out_33),
    .row9(driver_mm_3_out_36), .row10(driver_mm_3_out_38), .row11(driver_mm_3_out_41),
    .row12(driver_mm_3_out_44), .row13(driver_mm_3_out_49), .row14(driver_mm_3_out_50),
    .row15(driver_mm_3_out_11));
  DotMatrix #(.inputtype("row"), .matrixcols(18), .matrixrows(18)) dotmatrix_9 (
    .row0(driver_mm_4_out_3), .row1(driver_mm_4_out_4), .row2(driver_mm_4_out_6), .row3(driver_mm_4_out_8),
    .row4(driver_mm_4_out_12), .row5(driver_mm_4_out_16), .row6(driver_mm_4_out_20),
    .row7(driver_mm_4_out_23), .row8(driver_mm_4_out_28), .row9(driver_mm_4_out_31),
    .row10(driver_mm_4_out_35), .row11(driver_mm_4_out_39), .row12(driver_mm_4_out_43),
    .row13(driver_mm_4_out_48), .row14(driver_mm_4_out_51), .row15(driver_mm_4_out_52),
    .row16(driver_mm_4_out_5), .row17(driver_mm_4_out_7));
  driver_mm driver_mm_4 (
    .Bus1(in_4), .Bus2(in_3), .out_3(driver_mm_4_out_3), .out_4(driver_mm_4_out_4),
    .out_5(driver_mm_4_out_5), .out_7(driver_mm_4_out_7), .out_6(driver_mm_4_out_6),
    .out_8(driver_mm_4_out_8), .out_12(driver_mm_4_out_12), .out_16(driver_mm_4_out_16),
    .out_20(driver_mm_4_out_20), .out_23(driver_mm_4_out_23), .out_28(driver_mm_4_out_28),
    .out_31(driver_mm_4_out_31), .out_35(driver_mm_4_out_35), .out_39(driver_mm_4_out_39),
    .out_43(driver_mm_4_out_43), .out_48(driver_mm_4_out_48), .out_51(driver_mm_4_out_51),
    .out_52(driver_mm_4_out_52), .To_print3D_walls(b));  // open: out_10, out_14, out_17, out_19, out_22, out_25, out_46, out_27, out_47, out_29, out_32, out_34, out_37, out_40, out_42, out_45, out_13, out_15, out_18, out_21, out_24, out_26, out_30, out_33, out_36, out_38, out_41, out_44, out_49, out_50, out_9, out_11
  driver_mm driver_mm_5 (
    .Bus1(in_8), .Bus2(in_7), .To_print3D_walls(b));  // open: out_3, out_4, out_5, out_7, out_6, out_8, out_10, out_12, out_14, out_16, out_17, out_19, out_20, out_22, out_23, out_25, out_46, out_27, out_47, out_28, out_29, out_31, out_32, out_34, out_35, out_37, out_39, out_40, out_42, out_43, out_45, out_48, out_51, out_52, out_13, out_15, out_18, out_21, out_24, out_26, out_30, out_33, out_36, out_38, out_41, out_44, out_49, out_50, out_9, out_11
endmodule
