// Logisim project print3D.circ as structural Verilog
module matrix (
  input  [15:0] in_1,
  input  [8:0] in_2,
  input  [1:0] in_3,
  input  [1:0] GS
);

  wire [1:0] ATCcurEN, gameState;
  wire [8:0] b;
  wire [15:0] ASSH;
  wire [27:0] driver_l_1_out_8, driver_l_1_out_12, driver_l_1_out_16, driver_l_1_out_20, driver_l_1_out_24,
       driver_l_1_out_28, driver_l_1_out_32, driver_l_1_out_36, driver_l_1_out_40, driver_l_1_out_44,
       driver_l_1_out_48, driver_l_1_out_52, driver_l_1_out_56, driver_l_1_out_60, driver_l_1_out_64,
       driver_l_1_out_68, driver_l_1_out_72, driver_l_1_out_76, driver_l_1_out_80, driver_l_1_out_84,
       driver_l_1_out_88, driver_l_1_out_92, driver_l_1_out_96, driver_l_1_out_100, driver_l_1_out_104,
       driver_l_1_out_108, driver_l_1_out_112, driver_l_1_out_116, driver_l_1_out_120, driver_l_1_out_124,
       driver_l_1_out_128, driver_l_1_out_132, driver_l_2_out_8, driver_l_2_out_12, driver_l_2_out_16,
       driver_l_2_out_20, driver_l_2_out_24, driver_l_2_out_28, driver_l_2_out_32, driver_l_2_out_36,
       driver_l_2_out_40, driver_l_2_out_44, driver_l_2_out_48, driver_l_2_out_52, driver_l_2_out_56,
       driver_l_2_out_60, driver_l_2_out_64, driver_l_2_out_68, driver_l_2_out_72, driver_l_2_out_76,
       driver_l_2_out_80, driver_l_2_out_84, driver_l_2_out_88, driver_l_2_out_92, driver_l_2_out_96,
       driver_l_2_out_100, driver_l_2_out_104, driver_l_2_out_108, driver_l_2_out_112, driver_l_2_out_116,
       driver_l_2_out_120, driver_l_2_out_124, driver_l_2_out_128, driver_l_2_out_132;
  wire [28:0] driver_l_1_out_7, driver_l_1_out_11, driver_l_1_out_15, driver_l_1_out_19, driver_l_1_out_23,
       driver_l_1_out_27, driver_l_1_out_31, driver_l_1_out_35, driver_l_1_out_39, driver_l_1_out_43,
       driver_l_1_out_47, driver_l_1_out_51, driver_l_1_out_55, driver_l_1_out_59, driver_l_1_out_63,
       driver_l_1_out_67, driver_l_1_out_71, driver_l_1_out_75, driver_l_1_out_79, driver_l_1_out_83,
       driver_l_1_out_87, driver_l_1_out_91, driver_l_1_out_95, driver_l_1_out_99, driver_l_1_out_103,
       driver_l_1_out_107, driver_l_1_out_111, driver_l_1_out_115, driver_l_1_out_119, driver_l_1_out_123,
       driver_l_1_out_127, driver_l_1_out_131, driver_l_2_out_7, driver_l_2_out_11, driver_l_2_out_15,
       driver_l_2_out_19, driver_l_2_out_23, driver_l_2_out_27, driver_l_2_out_31, driver_l_2_out_35,
       driver_l_2_out_39, driver_l_2_out_43, driver_l_2_out_47, driver_l_2_out_51, driver_l_2_out_55,
       driver_l_2_out_59, driver_l_2_out_63, driver_l_2_out_67, driver_l_2_out_71, driver_l_2_out_75,
       driver_l_2_out_79, driver_l_2_out_83, driver_l_2_out_87, driver_l_2_out_91, driver_l_2_out_95,
       driver_l_2_out_99, driver_l_2_out_103, driver_l_2_out_107, driver_l_2_out_111, driver_l_2_out_115,
       driver_l_2_out_119, driver_l_2_out_123, driver_l_2_out_127, driver_l_2_out_131, driver_r_1_out_8,
       driver_r_1_out_12, driver_r_1_out_16, driver_r_1_out_20, driver_r_1_out_24, driver_r_1_out_28,
       driver_r_1_out_32, driver_r_1_out_36, driver_r_1_out_40, driver_r_1_out_44, driver_r_1_out_48,
       driver_r_1_out_52, driver_r_1_out_56, driver_r_1_out_60, driver_r_1_out_64, driver_r_1_out_68,
       driver_r_1_out_72, driver_r_1_out_76, driver_r_1_out_80, driver_r_1_out_84, driver_r_1_out_88,
       driver_r_1_out_92, driver_r_1_out_96, driver_r_1_out_100, driver_r_1_out_104, driver_r_1_out_108,
       driver_r_1_out_112, driver_r_1_out_116, driver_r_1_out_120, driver_r_1_out_124, driver_r_1_out_128,
       driver_r_1_out_132, driver_r_2_out_8, driver_r_2_out_12, driver_r_2_out_16, driver_r_2_out_20,
       driver_r_2_out_24, driver_r_2_out_28, driver_r_2_out_32, driver_r_2_out_36, driver_r_2_out_40,
       driver_r_2_out_44, driver_r_2_out_48, driver_r_2_out_52, driver_r_2_out_56, driver_r_2_out_60,
       driver_r_2_out_64, driver_r_2_out_68, driver_r_2_out_72, driver_r_2_out_76, driver_r_2_out_80,
       driver_r_2_out_84, driver_r_2_out_88, driver_r_2_out_92, driver_r_2_out_96, driver_r_2_out_100,
       driver_r_2_out_104, driver_r_2_out_108, driver_r_2_out_112, driver_r_2_out_116, driver_r_2_out_120,
       driver_r_2_out_124, driver_r_2_out_128, driver_r_2_out_132;
  wire [29:0] driver_l_1_out_6, driver_l_1_out_10, driver_l_1_out_14, driver_l_1_out_18, driver_l_1_out_22,
       driver_l_1_out_26, driver_l_1_out_30, driver_l_1_out_34, driver_l_1_out_38, driver_l_1_out_42,
       driver_l_1_out_46, driver_l_1_out_50, driver_l_1_out_54, driver_l_1_out_58, driver_l_1_out_62,
       driver_l_1_out_66, driver_l_1_out_70, driver_l_1_out_74, driver_l_1_out_78, driver_l_1_out_82,
       driver_l_1_out_86, driver_l_1_out_90, driver_l_1_out_94, driver_l_1_out_98, driver_l_1_out_102,
       driver_l_1_out_106, driver_l_1_out_110, driver_l_1_out_114, driver_l_1_out_118, driver_l_1_out_122,
       driver_l_1_out_126, driver_l_1_out_130, driver_l_2_out_6, driver_l_2_out_10, driver_l_2_out_14,
       driver_l_2_out_18, driver_l_2_out_22, driver_l_2_out_26, driver_l_2_out_30, driver_l_2_out_34,
       driver_l_2_out_38, driver_l_2_out_42, driver_l_2_out_46, driver_l_2_out_50, driver_l_2_out_54,
       driver_l_2_out_58, driver_l_2_out_62, driver_l_2_out_66, driver_l_2_out_70, driver_l_2_out_74,
       driver_l_2_out_78, driver_l_2_out_82, driver_l_2_out_86, driver_l_2_out_90, driver_l_2_out_94,
       driver_l_2_out_98, driver_l_2_out_102, driver_l_2_out_106, driver_l_2_out_110, driver_l_2_out_114,
       driver_l_2_out_118, driver_l_2_out_122, driver_l_2_out_126, driver_l_2_out_130, driver_r_1_out_7,
       driver_r_1_out_11, driver_r_1_out_15, driver_r_1_out_19, driver_r_1_out_23, driver_r_1_out_27,
       driver_r_1_out_31, driver_r_1_out_35, driver_r_1_out_39, driver_r_1_out_43, driver_r_1_out_47,
       driver_r_1_out_51, driver_r_1_out_55, driver_r_1_out_59, driver_r_1_out_63, driver_r_1_out_67,
       driver_r_1_out_71, driver_r_1_out_75, driver_r_1_out_79, driver_r_1_out_83, driver_r_1_out_87,
       driver_r_1_out_91, driver_r_1_out_95, driver_r_1_out_99, driver_r_1_out_103, driver_r_1_out_107,
       driver_r_1_out_111, driver_r_1_out_115, driver_r_1_out_119, driver_r_1_out_123, driver_r_1_out_127,
       driver_r_1_out_131, driver_r_2_out_7, driver_r_2_out_11, driver_r_2_out_15, driver_r_2_out_19,
       driver_r_2_out_23, driver_r_2_out_27, driver_r_2_out_31, driver_r_2_out_35, driver_r_2_out_39,
       driver_r_2_out_43, driver_r_2_out_47, driver_r_2_out_51, driver_r_2_out_55, driver_r_2_out_59,
       driver_r_2_out_63, driver_r_2_out_67, driver_r_2_out_71, driver_r_2_out_75, driver_r_2_out_79,
       driver_r_2_out_83, driver_r_2_out_87, driver_r_2_out_91, driver_r_2_out_95, driver_r_2_out_99,
       driver_r_2_out_103, driver_r_2_out_107, driver_r_2_out_111, driver_r_2_out_115, driver_r_2_out_119,
       driver_r_2_out_123, driver_r_2_out_127, driver_r_2_out_131;
  wire [30:0] driver_l_1_out_5, driver_l_1_out_9, driver_l_1_out_13, driver_l_1_out_17, driver_l_1_out_21,
       driver_l_1_out_25, driver_l_1_out_29, driver_l_1_out_33, driver_l_1_out_37, driver_l_1_out_41,
       driver_l_1_out_45, driver_l_1_out_49, driver_l_1_out_53, driver_l_1_out_57, driver_l_1_out_61,
       driver_l_1_out_65, driver_l_1_out_69, driver_l_1_out_73, driver_l_1_out_77, driver_l_1_out_81,
       driver_l_1_out_85, driver_l_1_out_89, driver_l_1_out_93, driver_l_1_out_97, driver_l_1_out_101,
       driver_l_1_out_105, driver_l_1_out_109, driver_l_1_out_113, driver_l_1_out_117, driver_l_1_out_121,
       driver_l_1_out_125, driver_l_1_out_129, driver_l_2_out_5, driver_l_2_out_9, driver_l_2_out_13,
       driver_l_2_out_17, driver_l_2_out_21, driver_l_2_out_25, driver_l_2_out_29, driver_l_2_out_33,
       driver_l_2_out_37, driver_l_2_out_41, driver_l_2_out_45, driver_l_2_out_49, driver_l_2_out_53,
       driver_l_2_out_57, driver_l_2_out_61, driver_l_2_out_65, driver_l_2_out_69, driver_l_2_out_73,
       driver_l_2_out_77, driver_l_2_out_81, driver_l_2_out_85, driver_l_2_out_89, driver_l_2_out_93,
       driver_l_2_out_97, driver_l_2_out_101, driver_l_2_out_105, driver_l_2_out_109, driver_l_2_out_113,
       driver_l_2_out_117, driver_l_2_out_121, driver_l_2_out_125, driver_l_2_out_129, driver_r_1_out_6,
       driver_r_1_out_10, driver_r_1_out_14, driver_r_1_out_18, driver_r_1_out_22, driver_r_1_out_26,
       driver_r_1_out_30, driver_r_1_out_34, driver_r_1_out_38, driver_r_1_out_42, driver_r_1_out_46,
       driver_r_1_out_50, driver_r_1_out_54, driver_r_1_out_58, driver_r_1_out_62, driver_r_1_out_66,
       driver_r_1_out_70, driver_r_1_out_74, driver_r_1_out_78, driver_r_1_out_82, driver_r_1_out_86,
       driver_r_1_out_90, driver_r_1_out_94, driver_r_1_out_98, driver_r_1_out_102, driver_r_1_out_106,
       driver_r_1_out_110, driver_r_1_out_114, driver_r_1_out_118, driver_r_1_out_122, driver_r_1_out_126,
       driver_r_1_out_130, driver_r_2_out_6, driver_r_2_out_10, driver_r_2_out_14, driver_r_2_out_18,
       driver_r_2_out_22, driver_r_2_out_26, driver_r_2_out_30, driver_r_2_out_34, driver_r_2_out_38,
       driver_r_2_out_42, driver_r_2_out_46, driver_r_2_out_50, driver_r_2_out_54, driver_r_2_out_58,
       driver_r_2_out_62, driver_r_2_out_66, driver_r_2_out_70, driver_r_2_out_74, driver_r_2_out_78,
       driver_r_2_out_82, driver_r_2_out_86, driver_r_2_out_90, driver_r_2_out_94, driver_r_2_out_98,
       driver_r_2_out_102, driver_r_2_out_106, driver_r_2_out_110, driver_r_2_out_114, driver_r_2_out_118,
       driver_r_2_out_122, driver_r_2_out_126, driver_r_2_out_130;
  wire [31:0] driver_r_1_out_5, driver_r_1_out_9, driver_r_1_out_13, driver_r_1_out_17, driver_r_1_out_21,
       driver_r_1_out_25, driver_r_1_out_29, driver_r_1_out_33, driver_r_1_out_37, driver_r_1_out_41,
       driver_r_1_out_45, driver_r_1_out_49, driver_r_1_out_53, driver_r_1_out_57, driver_r_1_out_61,
       driver_r_1_out_65, driver_r_1_out_69, driver_r_1_out_73, driver_r_1_out_77, driver_r_1_out_81,
       driver_r_1_out_85, driver_r_1_out_89, driver_r_1_out_93, driver_r_1_out_97, driver_r_1_out_101,
       driver_r_1_out_105, driver_r_1_out_109, driver_r_1_out_113, driver_r_1_out_117, driver_r_1_out_121,
       driver_r_1_out_125, driver_r_1_out_129, driver_r_2_out_5, driver_r_2_out_9, driver_r_2_out_13,
       driver_r_2_out_17, driver_r_2_out_21, driver_r_2_out_25, driver_r_2_out_29, driver_r_2_out_33,
       driver_r_2_out_37, driver_r_2_out_41, driver_r_2_out_45, driver_r_2_out_49, driver_r_2_out_53,
       driver_r_2_out_57, driver_r_2_out_61, driver_r_2_out_65, driver_r_2_out_69, driver_r_2_out_73,
       driver_r_2_out_77, driver_r_2_out_81, driver_r_2_out_85, driver_r_2_out_89, driver_r_2_out_93,
       driver_r_2_out_97, driver_r_2_out_101, driver_r_2_out_105, driver_r_2_out_109, driver_r_2_out_113,
       driver_r_2_out_117, driver_r_2_out_121, driver_r_2_out_125, driver_r_2_out_129;

  driver_l driver_l_1 (
    .b(in_2), .ASSH(in_1), .out_5(driver_l_1_out_5), .out_6(driver_l_1_out_6), .out_7(driver_l_1_out_7),
    .out_8(driver_l_1_out_8), .out_9(driver_l_1_out_9), .out_10(driver_l_1_out_10),
    .out_11(driver_l_1_out_11), .out_12(driver_l_1_out_12), .out_13(driver_l_1_out_13),
    .out_14(driver_l_1_out_14), .out_15(driver_l_1_out_15), .out_16(driver_l_1_out_16),
    .out_17(driver_l_1_out_17), .out_18(driver_l_1_out_18), .out_19(driver_l_1_out_19),
    .out_20(driver_l_1_out_20), .out_21(driver_l_1_out_21), .out_22(driver_l_1_out_22),
    .out_23(driver_l_1_out_23), .out_24(driver_l_1_out_24), .out_25(driver_l_1_out_25),
    .out_26(driver_l_1_out_26), .out_27(driver_l_1_out_27), .out_28(driver_l_1_out_28),
    .out_29(driver_l_1_out_29), .out_30(driver_l_1_out_30), .out_31(driver_l_1_out_31),
    .out_32(driver_l_1_out_32), .out_33(driver_l_1_out_33), .out_34(driver_l_1_out_34),
    .out_35(driver_l_1_out_35), .out_36(driver_l_1_out_36), .out_37(driver_l_1_out_37),
    .out_38(driver_l_1_out_38), .out_39(driver_l_1_out_39), .out_40(driver_l_1_out_40),
    .out_41(driver_l_1_out_41), .out_42(driver_l_1_out_42), .out_43(driver_l_1_out_43),
    .out_44(driver_l_1_out_44), .out_45(driver_l_1_out_45), .out_46(driver_l_1_out_46),
    .out_47(driver_l_1_out_47), .out_48(driver_l_1_out_48), .out_49(driver_l_1_out_49),
    .out_50(driver_l_1_out_50), .out_51(driver_l_1_out_51), .out_52(driver_l_1_out_52),
    .out_53(driver_l_1_out_53), .out_54(driver_l_1_out_54), .out_55(driver_l_1_out_55),
    .out_56(driver_l_1_out_56), .out_57(driver_l_1_out_57), .out_58(driver_l_1_out_58),
    .out_59(driver_l_1_out_59), .out_60(driver_l_1_out_60), .out_61(driver_l_1_out_61),
    .out_62(driver_l_1_out_62), .out_63(driver_l_1_out_63), .out_64(driver_l_1_out_64),
    .out_65(driver_l_1_out_65), .out_66(driver_l_1_out_66), .out_67(driver_l_1_out_67),
    .out_68(driver_l_1_out_68), .out_69(driver_l_1_out_69), .out_70(driver_l_1_out_70),
    .out_71(driver_l_1_out_71), .out_72(driver_l_1_out_72), .out_73(driver_l_1_out_73),
    .out_74(driver_l_1_out_74), .out_75(driver_l_1_out_75), .out_76(driver_l_1_out_76),
    .out_77(driver_l_1_out_77), .out_78(driver_l_1_out_78), .out_79(driver_l_1_out_79),
    .out_80(driver_l_1_out_80), .out_81(driver_l_1_out_81), .out_82(driver_l_1_out_82),
    .out_83(driver_l_1_out_83), .out_84(driver_l_1_out_84), .out_85(driver_l_1_out_85),
    .out_86(driver_l_1_out_86), .out_87(driver_l_1_out_87), .out_88(driver_l_1_out_88),
    .out_89(driver_l_1_out_89), .out_90(driver_l_1_out_90), .out_91(driver_l_1_out_91),
    .out_92(driver_l_1_out_92), .out_93(driver_l_1_out_93), .out_94(driver_l_1_out_94),
    .out_95(driver_l_1_out_95), .out_96(driver_l_1_out_96), .out_97(driver_l_1_out_97),
    .out_98(driver_l_1_out_98), .out_99(driver_l_1_out_99), .out_100(driver_l_1_out_100),
    .out_101(driver_l_1_out_101), .out_102(driver_l_1_out_102), .out_103(driver_l_1_out_103),
    .out_104(driver_l_1_out_104), .out_105(driver_l_1_out_105), .out_106(driver_l_1_out_106),
    .out_107(driver_l_1_out_107), .out_108(driver_l_1_out_108), .out_109(driver_l_1_out_109),
    .out_110(driver_l_1_out_110), .out_111(driver_l_1_out_111), .out_112(driver_l_1_out_112),
    .out_113(driver_l_1_out_113), .out_114(driver_l_1_out_114), .out_115(driver_l_1_out_115),
    .out_116(driver_l_1_out_116), .out_117(driver_l_1_out_117), .out_118(driver_l_1_out_118),
    .out_119(driver_l_1_out_119), .out_120(driver_l_1_out_120), .out_121(driver_l_1_out_121),
    .out_122(driver_l_1_out_122), .out_123(driver_l_1_out_123), .out_124(driver_l_1_out_124),
    .out_125(driver_l_1_out_125), .out_126(driver_l_1_out_126), .out_127(driver_l_1_out_127),
    .out_128(driver_l_1_out_128), .out_129(driver_l_1_out_129), .out_130(driver_l_1_out_130),
    .out_131(driver_l_1_out_131), .out_132(driver_l_1_out_132), .gamestate(in_3), .curr_enemy(GS));
  DotMatrix #(.inputtype("row"), .matrixcols(30), .matrixrows(32)) dotmatrix_1 (
    .row0(driver_l_1_out_6), .row1(driver_l_1_out_10), .row2(driver_l_1_out_14), .row3(driver_l_1_out_18),
    .row4(driver_l_1_out_22), .row5(driver_l_1_out_26), .row6(driver_l_1_out_30), .row7(driver_l_1_out_34),
    .row8(driver_l_1_out_38), .row9(driver_l_1_out_42), .row10(driver_l_1_out_46), .row11(driver_l_1_out_50),
    .row12(driver_l_1_out_54), .row13(driver_l_1_out_58), .row14(driver_l_1_out_62),
    .row15(driver_l_1_out_66), .row16(driver_l_1_out_70), .row17(driver_l_1_out_74),
    .row18(driver_l_1_out_78), .row19(driver_l_1_out_82), .row20(driver_l_1_out_86),
    .row21(driver_l_1_out_90), .row22(driver_l_1_out_94), .row23(driver_l_1_out_98),
    .row24(driver_l_1_out_102), .row25(driver_l_1_out_106), .row26(driver_l_1_out_110),
    .row27(driver_l_1_out_114), .row28(driver_l_1_out_118), .row29(driver_l_1_out_122),
    .row30(driver_l_1_out_126), .row31(driver_l_1_out_130));
  DotMatrix #(.inputtype("row"), .matrixcols(31), .matrixrows(32)) dotmatrix_2 (
    .row0(driver_l_1_out_5), .row1(driver_l_1_out_9), .row2(driver_l_1_out_13), .row3(driver_l_1_out_17),
    .row4(driver_l_1_out_21), .row5(driver_l_1_out_25), .row6(driver_l_1_out_29), .row7(driver_l_1_out_33),
    .row8(driver_l_1_out_37), .row9(driver_l_1_out_41), .row10(driver_l_1_out_45), .row11(driver_l_1_out_49),
    .row12(driver_l_1_out_53), .row13(driver_l_1_out_57), .row14(driver_l_1_out_61),
    .row15(driver_l_1_out_65), .row16(driver_l_1_out_69), .row17(driver_l_1_out_73),
    .row18(driver_l_1_out_77), .row19(driver_l_1_out_81), .row20(driver_l_1_out_85),
    .row21(driver_l_1_out_89), .row22(driver_l_1_out_93), .row23(driver_l_1_out_97),
    .row24(driver_l_1_out_101), .row25(driver_l_1_out_105), .row26(driver_l_1_out_109),
    .row27(driver_l_1_out_113), .row28(driver_l_1_out_117), .row29(driver_l_1_out_121),
    .row30(driver_l_1_out_125), .row31(driver_l_1_out_129));
  DotMatrix #(.inputtype("row"), .matrixcols(28), .matrixrows(32)) dotmatrix_3 (
    .row0(driver_l_1_out_8), .row1(driver_l_1_out_12), .row2(driver_l_1_out_16), .row3(driver_l_1_out_20),
    .row4(driver_l_1_out_24), .row5(driver_l_1_out_28), .row6(driver_l_1_out_32), .row7(driver_l_1_out_36),
    .row8(driver_l_1_out_40), .row9(driver_l_1_out_44), .row10(driver_l_1_out_48), .row11(driver_l_1_out_52),
    .row12(driver_l_1_out_56), .row13(driver_l_1_out_60), .row14(driver_l_1_out_64),
    .row15(driver_l_1_out_68), .row16(driver_l_1_out_72), .row17(driver_l_1_out_76),
    .row18(driver_l_1_out_80), .row19(driver_l_1_out_84), .row20(driver_l_1_out_88),
    .row21(driver_l_1_out_92), .row22(driver_l_1_out_96), .row23(driver_l_1_out_100),
    .row24(driver_l_1_out_104), .row25(driver_l_1_out_108), .row26(driver_l_1_out_112),
    .row27(driver_l_1_out_116), .row28(driver_l_1_out_120), .row29(driver_l_1_out_124),
    .row30(driver_l_1_out_128), .row31(driver_l_1_out_132));
  DotMatrix #(.inputtype("row"), .matrixcols(29), .matrixrows(32)) dotmatrix_4 (
    .row0(driver_l_1_out_7), .row1(driver_l_1_out_11), .row2(driver_l_1_out_15), .row3(driver_l_1_out_19),
    .row4(driver_l_1_out_23), .row5(driver_l_1_out_27), .row6(driver_l_1_out_31), .row7(driver_l_1_out_35),
    .row8(driver_l_1_out_39), .row9(driver_l_1_out_43), .row10(driver_l_1_out_47), .row11(driver_l_1_out_51),
    .row12(driver_l_1_out_55), .row13(driver_l_1_out_59), .row14(driver_l_1_out_63),
    .row15(driver_l_1_out_67), .row16(driver_l_1_out_71), .row17(driver_l_1_out_75),
    .row18(driver_l_1_out_79), .row19(driver_l_1_out_83), .row20(driver_l_1_out_87),
    .row21(driver_l_1_out_91), .row22(driver_l_1_out_95), .row23(driver_l_1_out_99),
    .row24(driver_l_1_out_103), .row25(driver_l_1_out_107), .row26(driver_l_1_out_111),
    .row27(driver_l_1_out_115), .row28(driver_l_1_out_119), .row29(driver_l_1_out_123),
    .row30(driver_l_1_out_127), .row31(driver_l_1_out_131));
  driver_r driver_r_1 (
    .out_5(driver_r_1_out_5), .out_6(driver_r_1_out_6), .out_7(driver_r_1_out_7), .out_8(driver_r_1_out_8),
    .out_9(driver_r_1_out_9), .out_10(driver_r_1_out_10), .out_11(driver_r_1_out_11),
    .out_12(driver_r_1_out_12), .out_13(driver_r_1_out_13), .out_14(driver_r_1_out_14),
    .out_15(driver_r_1_out_15), .out_16(driver_r_1_out_16), .out_17(driver_r_1_out_17),
    .out_18(driver_r_1_out_18), .out_19(driver_r_1_out_19), .out_20(driver_r_1_out_20),
    .out_21(driver_r_1_out_21), .out_22(driver_r_1_out_22), .out_23(driver_r_1_out_23),
    .out_24(driver_r_1_out_24), .out_25(driver_r_1_out_25), .out_26(driver_r_1_out_26),
    .out_27(driver_r_1_out_27), .out_28(driver_r_1_out_28), .out_29(driver_r_1_out_29),
    .out_30(driver_r_1_out_30), .out_31(driver_r_1_out_31), .out_32(driver_r_1_out_32),
    .out_33(driver_r_1_out_33), .out_34(driver_r_1_out_34), .out_35(driver_r_1_out_35),
    .out_36(driver_r_1_out_36), .out_37(driver_r_1_out_37), .out_38(driver_r_1_out_38),
    .out_39(driver_r_1_out_39), .out_40(driver_r_1_out_40), .out_41(driver_r_1_out_41),
    .out_42(driver_r_1_out_42), .out_43(driver_r_1_out_43), .out_44(driver_r_1_out_44),
    .out_45(driver_r_1_out_45), .out_46(driver_r_1_out_46), .out_47(driver_r_1_out_47),
    .out_48(driver_r_1_out_48), .out_49(driver_r_1_out_49), .out_50(driver_r_1_out_50),
    .out_51(driver_r_1_out_51), .out_52(driver_r_1_out_52), .out_53(driver_r_1_out_53),
    .out_54(driver_r_1_out_54), .out_55(driver_r_1_out_55), .out_56(driver_r_1_out_56),
    .out_57(driver_r_1_out_57), .out_58(driver_r_1_out_58), .out_59(driver_r_1_out_59),
    .out_60(driver_r_1_out_60), .out_61(driver_r_1_out_61), .out_62(driver_r_1_out_62),
    .out_63(driver_r_1_out_63), .out_64(driver_r_1_out_64), .out_65(driver_r_1_out_65),
    .out_66(driver_r_1_out_66), .out_67(driver_r_1_out_67), .out_68(driver_r_1_out_68),
    .out_69(driver_r_1_out_69), .out_70(driver_r_1_out_70), .out_71(driver_r_1_out_71),
    .out_72(driver_r_1_out_72), .out_73(driver_r_1_out_73), .out_74(driver_r_1_out_74),
    .out_75(driver_r_1_out_75), .out_76(driver_r_1_out_76), .out_77(driver_r_1_out_77),
    .out_78(driver_r_1_out_78), .out_79(driver_r_1_out_79), .out_80(driver_r_1_out_80),
    .out_81(driver_r_1_out_81), .out_82(driver_r_1_out_82), .out_83(driver_r_1_out_83),
    .out_84(driver_r_1_out_84), .out_85(driver_r_1_out_85), .out_86(driver_r_1_out_86),
    .out_87(driver_r_1_out_87), .out_88(driver_r_1_out_88), .out_89(driver_r_1_out_89),
    .out_90(driver_r_1_out_90), .out_91(driver_r_1_out_91), .out_92(driver_r_1_out_92),
    .out_93(driver_r_1_out_93), .out_94(driver_r_1_out_94), .out_95(driver_r_1_out_95),
    .out_96(driver_r_1_out_96), .out_97(driver_r_1_out_97), .out_98(driver_r_1_out_98),
    .out_99(driver_r_1_out_99), .out_100(driver_r_1_out_100), .out_101(driver_r_1_out_101),
    .out_102(driver_r_1_out_102), .out_103(driver_r_1_out_103), .out_104(driver_r_1_out_104),
    .out_105(driver_r_1_out_105), .out_106(driver_r_1_out_106), .out_107(driver_r_1_out_107),
    .out_108(driver_r_1_out_108), .out_109(driver_r_1_out_109), .out_110(driver_r_1_out_110),
    .out_111(driver_r_1_out_111), .out_112(driver_r_1_out_112), .out_113(driver_r_1_out_113),
    .out_114(driver_r_1_out_114), .out_115(driver_r_1_out_115), .out_116(driver_r_1_out_116),
    .out_117(driver_r_1_out_117), .out_118(driver_r_1_out_118), .out_119(driver_r_1_out_119),
    .out_120(driver_r_1_out_120), .out_121(driver_r_1_out_121), .out_122(driver_r_1_out_122),
    .out_123(driver_r_1_out_123), .out_124(driver_r_1_out_124), .out_125(driver_r_1_out_125),
    .out_126(driver_r_1_out_126), .out_127(driver_r_1_out_127), .out_128(driver_r_1_out_128),
    .out_129(driver_r_1_out_129), .out_130(driver_r_1_out_130), .out_131(driver_r_1_out_131),
    .out_132(driver_r_1_out_132), .ASSH(in_1), .b(in_2), .curr_enem(in_3), .gameState(GS));
  DotMatrix #(.inputtype("row"), .matrixcols(30), .matrixrows(32)) dotmatrix_5 (
    .row0(driver_r_1_out_7), .row1(driver_r_1_out_11), .row2(driver_r_1_out_15), .row3(driver_r_1_out_19),
    .row4(driver_r_1_out_23), .row5(driver_r_1_out_27), .row6(driver_r_1_out_31), .row7(driver_r_1_out_35),
    .row8(driver_r_1_out_39), .row9(driver_r_1_out_43), .row10(driver_r_1_out_47), .row11(driver_r_1_out_51),
    .row12(driver_r_1_out_55), .row13(driver_r_1_out_59), .row14(driver_r_1_out_63),
    .row15(driver_r_1_out_67), .row16(driver_r_1_out_71), .row17(driver_r_1_out_75),
    .row18(driver_r_1_out_79), .row19(driver_r_1_out_83), .row20(driver_r_1_out_87),
    .row21(driver_r_1_out_91), .row22(driver_r_1_out_95), .row23(driver_r_1_out_99),
    .row24(driver_r_1_out_103), .row25(driver_r_1_out_107), .row26(driver_r_1_out_111),
    .row27(driver_r_1_out_115), .row28(driver_r_1_out_119), .row29(driver_r_1_out_123),
    .row30(driver_r_1_out_127), .row31(driver_r_1_out_131));
  DotMatrix #(.inputtype("row"), .matrixcols(29), .matrixrows(32)) dotmatrix_6 (
    .row0(driver_r_1_out_8), .row1(driver_r_1_out_12), .row2(driver_r_1_out_16), .row3(driver_r_1_out_20),
    .row4(driver_r_1_out_24), .row5(driver_r_1_out_28), .row6(driver_r_1_out_32), .row7(driver_r_1_out_36),
    .row8(driver_r_1_out_40), .row9(driver_r_1_out_44), .row10(driver_r_1_out_48), .row11(driver_r_1_out_52),
    .row12(driver_r_1_out_56), .row13(driver_r_1_out_60), .row14(driver_r_1_out_64),
    .row15(driver_r_1_out_68), .row16(driver_r_1_out_72), .row17(driver_r_1_out_76),
    .row18(driver_r_1_out_80), .row19(driver_r_1_out_84), .row20(driver_r_1_out_88),
    .row21(driver_r_1_out_92), .row22(driver_r_1_out_96), .row23(driver_r_1_out_100),
    .row24(driver_r_1_out_104), .row25(driver_r_1_out_108), .row26(driver_r_1_out_112),
    .row27(driver_r_1_out_116), .row28(driver_r_1_out_120), .row29(driver_r_1_out_124),
    .row30(driver_r_1_out_128), .row31(driver_r_1_out_132));
  DotMatrix #(.inputtype("row"), .matrixcols(32), .matrixrows(32)) dotmatrix_7 (
    .row0(driver_r_1_out_5), .row1(driver_r_1_out_9), .row2(driver_r_1_out_13), .row3(driver_r_1_out_17),
    .row4(driver_r_1_out_21), .row5(driver_r_1_out_25), .row6(driver_r_1_out_29), .row7(driver_r_1_out_33),
    .row8(driver_r_1_out_37), .row9(driver_r_1_out_41), .row10(driver_r_1_out_45), .row11(driver_r_1_out_49),
    .row12(driver_r_1_out_53), .row13(driver_r_1_out_57), .row14(driver_r_1_out_61),
    .row15(driver_r_1_out_65), .row16(driver_r_1_out_69), .row17(driver_r_1_out_73),
    .row18(driver_r_1_out_77), .row19(driver_r_1_out_81), .row20(driver_r_1_out_85),
    .row21(driver_r_1_out_89), .row22(driver_r_1_out_93), .row23(driver_r_1_out_97),
    .row24(driver_r_1_out_101), .row25(driver_r_1_out_105), .row26(driver_r_1_out_109),
    .row27(driver_r_1_out_113), .row28(driver_r_1_out_117), .row29(driver_r_1_out_121),
    .row30(driver_r_1_out_125), .row31(driver_r_1_out_129));
  DotMatrix #(.inputtype("row"), .matrixcols(31), .matrixrows(32)) dotmatrix_8 (
    .row0(driver_r_1_out_6), .row1(driver_r_1_out_10), .row2(driver_r_1_out_14), .row3(driver_r_1_out_18),
    .row4(driver_r_1_out_22), .row5(driver_r_1_out_26), .row6(driver_r_1_out_30), .row7(driver_r_1_out_34),
    .row8(driver_r_1_out_38), .row9(driver_r_1_out_42), .row10(driver_r_1_out_46), .row11(driver_r_1_out_50),
    .row12(driver_r_1_out_54), .row13(driver_r_1_out_58), .row14(driver_r_1_out_62),
    .row15(driver_r_1_out_66), .row16(driver_r_1_out_70), .row17(driver_r_1_out_74),
    .row18(driver_r_1_out_78), .row19(driver_r_1_out_82), .row20(driver_r_1_out_86),
    .row21(driver_r_1_out_90), .row22(driver_r_1_out_94), .row23(driver_r_1_out_98),
    .row24(driver_r_1_out_102), .row25(driver_r_1_out_106), .row26(driver_r_1_out_110),
    .row27(driver_r_1_out_114), .row28(driver_r_1_out_118), .row29(driver_r_1_out_122),
    .row30(driver_r_1_out_126), .row31(driver_r_1_out_130));
  driver_l driver_l_2 (
    .b(b), .ASSH(ASSH), .out_5(driver_l_2_out_5), .out_6(driver_l_2_out_6), .out_7(driver_l_2_out_7),
    .out_8(driver_l_2_out_8), .out_9(driver_l_2_out_9), .out_10(driver_l_2_out_10),
    .out_11(driver_l_2_out_11), .out_12(driver_l_2_out_12), .out_13(driver_l_2_out_13),
    .out_14(driver_l_2_out_14), .out_15(driver_l_2_out_15), .out_16(driver_l_2_out_16),
    .out_17(driver_l_2_out_17), .out_18(driver_l_2_out_18), .out_19(driver_l_2_out_19),
    .out_20(driver_l_2_out_20), .out_21(driver_l_2_out_21), .out_22(driver_l_2_out_22),
    .out_23(driver_l_2_out_23), .out_24(driver_l_2_out_24), .out_25(driver_l_2_out_25),
    .out_26(driver_l_2_out_26), .out_27(driver_l_2_out_27), .out_28(driver_l_2_out_28),
    .out_29(driver_l_2_out_29), .out_30(driver_l_2_out_30), .out_31(driver_l_2_out_31),
    .out_32(driver_l_2_out_32), .out_33(driver_l_2_out_33), .out_34(driver_l_2_out_34),
    .out_35(driver_l_2_out_35), .out_36(driver_l_2_out_36), .out_37(driver_l_2_out_37),
    .out_38(driver_l_2_out_38), .out_39(driver_l_2_out_39), .out_40(driver_l_2_out_40),
    .out_41(driver_l_2_out_41), .out_42(driver_l_2_out_42), .out_43(driver_l_2_out_43),
    .out_44(driver_l_2_out_44), .out_45(driver_l_2_out_45), .out_46(driver_l_2_out_46),
    .out_47(driver_l_2_out_47), .out_48(driver_l_2_out_48), .out_49(driver_l_2_out_49),
    .out_50(driver_l_2_out_50), .out_51(driver_l_2_out_51), .out_52(driver_l_2_out_52),
    .out_53(driver_l_2_out_53), .out_54(driver_l_2_out_54), .out_55(driver_l_2_out_55),
    .out_56(driver_l_2_out_56), .out_57(driver_l_2_out_57), .out_58(driver_l_2_out_58),
    .out_59(driver_l_2_out_59), .out_60(driver_l_2_out_60), .out_61(driver_l_2_out_61),
    .out_62(driver_l_2_out_62), .out_63(driver_l_2_out_63), .out_64(driver_l_2_out_64),
    .out_65(driver_l_2_out_65), .out_66(driver_l_2_out_66), .out_67(driver_l_2_out_67),
    .out_68(driver_l_2_out_68), .out_69(driver_l_2_out_69), .out_70(driver_l_2_out_70),
    .out_71(driver_l_2_out_71), .out_72(driver_l_2_out_72), .out_73(driver_l_2_out_73),
    .out_74(driver_l_2_out_74), .out_75(driver_l_2_out_75), .out_76(driver_l_2_out_76),
    .out_77(driver_l_2_out_77), .out_78(driver_l_2_out_78), .out_79(driver_l_2_out_79),
    .out_80(driver_l_2_out_80), .out_81(driver_l_2_out_81), .out_82(driver_l_2_out_82),
    .out_83(driver_l_2_out_83), .out_84(driver_l_2_out_84), .out_85(driver_l_2_out_85),
    .out_86(driver_l_2_out_86), .out_87(driver_l_2_out_87), .out_88(driver_l_2_out_88),
    .out_89(driver_l_2_out_89), .out_90(driver_l_2_out_90), .out_91(driver_l_2_out_91),
    .out_92(driver_l_2_out_92), .out_93(driver_l_2_out_93), .out_94(driver_l_2_out_94),
    .out_95(driver_l_2_out_95), .out_96(driver_l_2_out_96), .out_97(driver_l_2_out_97),
    .out_98(driver_l_2_out_98), .out_99(driver_l_2_out_99), .out_100(driver_l_2_out_100),
    .out_101(driver_l_2_out_101), .out_102(driver_l_2_out_102), .out_103(driver_l_2_out_103),
    .out_104(driver_l_2_out_104), .out_105(driver_l_2_out_105), .out_106(driver_l_2_out_106),
    .out_107(driver_l_2_out_107), .out_108(driver_l_2_out_108), .out_109(driver_l_2_out_109),
    .out_110(driver_l_2_out_110), .out_111(driver_l_2_out_111), .out_112(driver_l_2_out_112),
    .out_113(driver_l_2_out_113), .out_114(driver_l_2_out_114), .out_115(driver_l_2_out_115),
    .out_116(driver_l_2_out_116), .out_117(driver_l_2_out_117), .out_118(driver_l_2_out_118),
    .out_119(driver_l_2_out_119), .out_120(driver_l_2_out_120), .out_121(driver_l_2_out_121),
    .out_122(driver_l_2_out_122), .out_123(driver_l_2_out_123), .out_124(driver_l_2_out_124),
    .out_125(driver_l_2_out_125), .out_126(driver_l_2_out_126), .out_127(driver_l_2_out_127),
    .out_128(driver_l_2_out_128), .out_129(driver_l_2_out_129), .out_130(driver_l_2_out_130),
    .out_131(driver_l_2_out_131), .out_132(driver_l_2_out_132), .gamestate(ATCcurEN), .curr_enemy(gameState));
  DotMatrix #(.inputtype("row"), .matrixcols(31), .matrixrows(32)) dotmatrix_9 (
    .row0(driver_l_2_out_5), .row1(driver_l_2_out_9), .row2(driver_l_2_out_13), .row3(driver_l_2_out_17),
    .row4(driver_l_2_out_21), .row5(driver_l_2_out_25), .row6(driver_l_2_out_29), .row7(driver_l_2_out_33),
    .row8(driver_l_2_out_37), .row9(driver_l_2_out_41), .row10(driver_l_2_out_45), .row11(driver_l_2_out_49),
    .row12(driver_l_2_out_53), .row13(driver_l_2_out_57), .row14(driver_l_2_out_61),
    .row15(driver_l_2_out_65), .row16(driver_l_2_out_69), .row17(driver_l_2_out_73),
    .row18(driver_l_2_out_77), .row19(driver_l_2_out_81), .row20(driver_l_2_out_85),
    .row21(driver_l_2_out_89), .row22(driver_l_2_out_93), .row23(driver_l_2_out_97),
    .row24(driver_l_2_out_101), .row25(driver_l_2_out_105), .row26(driver_l_2_out_109),
    .row27(driver_l_2_out_113), .row28(driver_l_2_out_117), .row29(driver_l_2_out_121),
    .row30(driver_l_2_out_125), .row31(driver_l_2_out_129));
  DotMatrix #(.inputtype("row"), .matrixcols(30), .matrixrows(32)) dotmatrix_10 (
    .row0(driver_l_2_out_6), .row1(driver_l_2_out_10), .row2(driver_l_2_out_14), .row3(driver_l_2_out_18),
    .row4(driver_l_2_out_22), .row5(driver_l_2_out_26), .row6(driver_l_2_out_30), .row7(driver_l_2_out_34),
    .row8(driver_l_2_out_38), .row9(driver_l_2_out_42), .row10(driver_l_2_out_46), .row11(driver_l_2_out_50),
    .row12(driver_l_2_out_54), .row13(driver_l_2_out_58), .row14(driver_l_2_out_62),
    .row15(driver_l_2_out_66), .row16(driver_l_2_out_70), .row17(driver_l_2_out_74),
    .row18(driver_l_2_out_78), .row19(driver_l_2_out_82), .row20(driver_l_2_out_86),
    .row21(driver_l_2_out_90), .row22(driver_l_2_out_94), .row23(driver_l_2_out_98),
    .row24(driver_l_2_out_102), .row25(driver_l_2_out_106), .row26(driver_l_2_out_110),
    .row27(driver_l_2_out_114), .row28(driver_l_2_out_118), .row29(driver_l_2_out_122),
    .row30(driver_l_2_out_126), .row31(driver_l_2_out_130));
  DotMatrix #(.inputtype("row"), .matrixcols(29), .matrixrows(32)) dotmatrix_11 (
    .row0(driver_l_2_out_7), .row1(driver_l_2_out_11), .row2(driver_l_2_out_15), .row3(driver_l_2_out_19),
    .row4(driver_l_2_out_23), .row5(driver_l_2_out_27), .row6(driver_l_2_out_31), .row7(driver_l_2_out_35),
    .row8(driver_l_2_out_39), .row9(driver_l_2_out_43), .row10(driver_l_2_out_47), .row11(driver_l_2_out_51),
    .row12(driver_l_2_out_55), .row13(driver_l_2_out_59), .row14(driver_l_2_out_63),
    .row15(driver_l_2_out_67), .row16(driver_l_2_out_71), .row17(driver_l_2_out_75),
    .row18(driver_l_2_out_79), .row19(driver_l_2_out_83), .row20(driver_l_2_out_87),
    .row21(driver_l_2_out_91), .row22(driver_l_2_out_95), .row23(driver_l_2_out_99),
    .row24(driver_l_2_out_103), .row25(driver_l_2_out_107), .row26(driver_l_2_out_111),
    .row27(driver_l_2_out_115), .row28(driver_l_2_out_119), .row29(driver_l_2_out_123),
    .row30(driver_l_2_out_127), .row31(driver_l_2_out_131));
  DotMatrix #(.inputtype("row"), .matrixcols(28), .matrixrows(32)) dotmatrix_12 (
    .row0(driver_l_2_out_8), .row1(driver_l_2_out_12), .row2(driver_l_2_out_16), .row3(driver_l_2_out_20),
    .row4(driver_l_2_out_24), .row5(driver_l_2_out_28), .row6(driver_l_2_out_32), .row7(driver_l_2_out_36),
    .row8(driver_l_2_out_40), .row9(driver_l_2_out_44), .row10(driver_l_2_out_48), .row11(driver_l_2_out_52),
    .row12(driver_l_2_out_56), .row13(driver_l_2_out_60), .row14(driver_l_2_out_64),
    .row15(driver_l_2_out_68), .row16(driver_l_2_out_72), .row17(driver_l_2_out_76),
    .row18(driver_l_2_out_80), .row19(driver_l_2_out_84), .row20(driver_l_2_out_88),
    .row21(driver_l_2_out_92), .row22(driver_l_2_out_96), .row23(driver_l_2_out_100),
    .row24(driver_l_2_out_104), .row25(driver_l_2_out_108), .row26(driver_l_2_out_112),
    .row27(driver_l_2_out_116), .row28(driver_l_2_out_120), .row29(driver_l_2_out_124),
    .row30(driver_l_2_out_128), .row31(driver_l_2_out_132));
  driver_r driver_r_2 (
    .out_5(driver_r_2_out_5), .out_6(driver_r_2_out_6), .out_7(driver_r_2_out_7), .out_8(driver_r_2_out_8),
    .out_9(driver_r_2_out_9), .out_10(driver_r_2_out_10), .out_11(driver_r_2_out_11),
    .out_12(driver_r_2_out_12), .out_13(driver_r_2_out_13), .out_14(driver_r_2_out_14),
    .out_15(driver_r_2_out_15), .out_16(driver_r_2_out_16), .out_17(driver_r_2_out_17),
    .out_18(driver_r_2_out_18), .out_19(driver_r_2_out_19), .out_20(driver_r_2_out_20),
    .out_21(driver_r_2_out_21), .out_22(driver_r_2_out_22), .out_23(driver_r_2_out_23),
    .out_24(driver_r_2_out_24), .out_25(driver_r_2_out_25), .out_26(driver_r_2_out_26),
    .out_27(driver_r_2_out_27), .out_28(driver_r_2_out_28), .out_29(driver_r_2_out_29),
    .out_30(driver_r_2_out_30), .out_31(driver_r_2_out_31), .out_32(driver_r_2_out_32),
    .out_33(driver_r_2_out_33), .out_34(driver_r_2_out_34), .out_35(driver_r_2_out_35),
    .out_36(driver_r_2_out_36), .out_37(driver_r_2_out_37), .out_38(driver_r_2_out_38),
    .out_39(driver_r_2_out_39), .out_40(driver_r_2_out_40), .out_41(driver_r_2_out_41),
    .out_42(driver_r_2_out_42), .out_43(driver_r_2_out_43), .out_44(driver_r_2_out_44),
    .out_45(driver_r_2_out_45), .out_46(driver_r_2_out_46), .out_47(driver_r_2_out_47),
    .out_48(driver_r_2_out_48), .out_49(driver_r_2_out_49), .out_50(driver_r_2_out_50),
    .out_51(driver_r_2_out_51), .out_52(driver_r_2_out_52), .out_53(driver_r_2_out_53),
    .out_54(driver_r_2_out_54), .out_55(driver_r_2_out_55), .out_56(driver_r_2_out_56),
    .out_57(driver_r_2_out_57), .out_58(driver_r_2_out_58), .out_59(driver_r_2_out_59),
    .out_60(driver_r_2_out_60), .out_61(driver_r_2_out_61), .out_62(driver_r_2_out_62),
    .out_63(driver_r_2_out_63), .out_64(driver_r_2_out_64), .out_65(driver_r_2_out_65),
    .out_66(driver_r_2_out_66), .out_67(driver_r_2_out_67), .out_68(driver_r_2_out_68),
    .out_69(driver_r_2_out_69), .out_70(driver_r_2_out_70), .out_71(driver_r_2_out_71),
    .out_72(driver_r_2_out_72), .out_73(driver_r_2_out_73), .out_74(driver_r_2_out_74),
    .out_75(driver_r_2_out_75), .out_76(driver_r_2_out_76), .out_77(driver_r_2_out_77),
    .out_78(driver_r_2_out_78), .out_79(driver_r_2_out_79), .out_80(driver_r_2_out_80),
    .out_81(driver_r_2_out_81), .out_82(driver_r_2_out_82), .out_83(driver_r_2_out_83),
    .out_84(driver_r_2_out_84), .out_85(driver_r_2_out_85), .out_86(driver_r_2_out_86),
    .out_87(driver_r_2_out_87), .out_88(driver_r_2_out_88), .out_89(driver_r_2_out_89),
    .out_90(driver_r_2_out_90), .out_91(driver_r_2_out_91), .out_92(driver_r_2_out_92),
    .out_93(driver_r_2_out_93), .out_94(driver_r_2_out_94), .out_95(driver_r_2_out_95),
    .out_96(driver_r_2_out_96), .out_97(driver_r_2_out_97), .out_98(driver_r_2_out_98),
    .out_99(driver_r_2_out_99), .out_100(driver_r_2_out_100), .out_101(driver_r_2_out_101),
    .out_102(driver_r_2_out_102), .out_103(driver_r_2_out_103), .out_104(driver_r_2_out_104),
    .out_105(driver_r_2_out_105), .out_106(driver_r_2_out_106), .out_107(driver_r_2_out_107),
    .out_108(driver_r_2_out_108), .out_109(driver_r_2_out_109), .out_110(driver_r_2_out_110),
    .out_111(driver_r_2_out_111), .out_112(driver_r_2_out_112), .out_113(driver_r_2_out_113),
    .out_114(driver_r_2_out_114), .out_115(driver_r_2_out_115), .out_116(driver_r_2_out_116),
    .out_117(driver_r_2_out_117), .out_118(driver_r_2_out_118), .out_119(driver_r_2_out_119),
    .out_120(driver_r_2_out_120), .out_121(driver_r_2_out_121), .out_122(driver_r_2_out_122),
    .out_123(driver_r_2_out_123), .out_124(driver_r_2_out_124), .out_125(driver_r_2_out_125),
    .out_126(driver_r_2_out_126), .out_127(driver_r_2_out_127), .out_128(driver_r_2_out_128),
    .out_129(driver_r_2_out_129), .out_130(driver_r_2_out_130), .out_131(driver_r_2_out_131),
    .out_132(driver_r_2_out_132), .ASSH(ASSH), .b(b), .curr_enem(gameState), .gameState(ATCcurEN));
  DotMatrix #(.inputtype("row"), .matrixcols(30), .matrixrows(32)) dotmatrix_13 (
    .row0(driver_r_2_out_7), .row1(driver_r_2_out_11), .row2(driver_r_2_out_15), .row3(driver_r_2_out_19),
    .row4(driver_r_2_out_23), .row5(driver_r_2_out_27), .row6(driver_r_2_out_31), .row7(driver_r_2_out_35),
    .row8(driver_r_2_out_39), .row9(driver_r_2_out_43), .row10(driver_r_2_out_47), .row11(driver_r_2_out_51),
    .row12(driver_r_2_out_55), .row13(driver_r_2_out_59), .row14(driver_r_2_out_63),
    .row15(driver_r_2_out_67), .row16(driver_r_2_out_71), .row17(driver_r_2_out_75),
    .row18(driver_r_2_out_79), .row19(driver_r_2_out_83), .row20(driver_r_2_out_87),
    .row21(driver_r_2_out_91), .row22(driver_r_2_out_95), .row23(driver_r_2_out_99),
    .row24(driver_r_2_out_103), .row25(driver_r_2_out_107), .row26(driver_r_2_out_111),
    .row27(driver_r_2_out_115), .row28(driver_r_2_out_119), .row29(driver_r_2_out_123),
    .row30(driver_r_2_out_127), .row31(driver_r_2_out_131));
  DotMatrix #(.inputtype("row"), .matrixcols(31), .matrixrows(32)) dotmatrix_14 (
    .row0(driver_r_2_out_6), .row1(driver_r_2_out_10), .row2(driver_r_2_out_14), .row3(driver_r_2_out_18),
    .row4(driver_r_2_out_22), .row5(driver_r_2_out_26), .row6(driver_r_2_out_30), .row7(driver_r_2_out_34),
    .row8(driver_r_2_out_38), .row9(driver_r_2_out_42), .row10(driver_r_2_out_46), .row11(driver_r_2_out_50),
    .row12(driver_r_2_out_54), .row13(driver_r_2_out_58), .row14(driver_r_2_out_62),
    .row15(driver_r_2_out_66), .row16(driver_r_2_out_70), .row17(driver_r_2_out_74),
    .row18(driver_r_2_out_78), .row19(driver_r_2_out_82), .row20(driver_r_2_out_86),
    .row21(driver_r_2_out_90), .row22(driver_r_2_out_94), .row23(driver_r_2_out_98),
    .row24(driver_r_2_out_102), .row25(driver_r_2_out_106), .row26(driver_r_2_out_110),
    .row27(driver_r_2_out_114), .row28(driver_r_2_out_118), .row29(driver_r_2_out_122),
    .row30(driver_r_2_out_126), .row31(driver_r_2_out_130));
  DotMatrix #(.inputtype("row"), .matrixcols(29), .matrixrows(32)) dotmatrix_15 (
    .row0(driver_r_2_out_8), .row1(driver_r_2_out_12), .row2(driver_r_2_out_16), .row3(driver_r_2_out_20),
    .row4(driver_r_2_out_24), .row5(driver_r_2_out_28), .row6(driver_r_2_out_32), .row7(driver_r_2_out_36),
    .row8(driver_r_2_out_40), .row9(driver_r_2_out_44), .row10(driver_r_2_out_48), .row11(driver_r_2_out_52),
    .row12(driver_r_2_out_56), .row13(driver_r_2_out_60), .row14(driver_r_2_out_64),
    .row15(driver_r_2_out_68), .row16(driver_r_2_out_72), .row17(driver_r_2_out_76),
    .row18(driver_r_2_out_80), .row19(driver_r_2_out_84), .row20(driver_r_2_out_88),
    .row21(driver_r_2_out_92), .row22(driver_r_2_out_96), .row23(driver_r_2_out_100),
    .row24(driver_r_2_out_104), .row25(driver_r_2_out_108), .row26(driver_r_2_out_112),
    .row27(driver_r_2_out_116), .row28(driver_r_2_out_120), .row29(driver_r_2_out_124),
    .row30(driver_r_2_out_128), .row31(driver_r_2_out_132));
  DotMatrix #(.inputtype("row"), .matrixcols(32), .matrixrows(32)) dotmatrix_16 (
    .row0(driver_r_2_out_5), .row1(driver_r_2_out_9), .row2(driver_r_2_out_13), .row3(driver_r_2_out_17),
    .row4(driver_r_2_out_21), .row5(driver_r_2_out_25), .row6(driver_r_2_out_29), .row7(driver_r_2_out_33),
    .row8(driver_r_2_out_37), .row9(driver_r_2_out_41), .row10(driver_r_2_out_45), .row11(driver_r_2_out_49),
    .row12(driver_r_2_out_53), .row13(driver_r_2_out_57), .row14(driver_r_2_out_61),
    .row15(driver_r_2_out_65), .row16(driver_r_2_out_69), .row17(driver_r_2_out_73),
    .row18(driver_r_2_out_77), .row19(driver_r_2_out_81), .row20(driver_r_2_out_85),
    .row21(driver_r_2_out_89), .row22(driver_r_2_out_93), .row23(driver_r_2_out_97),
    .row24(driver_r_2_out_101), .row25(driver_r_2_out_105), .row26(driver_r_2_out_109),
    .row27(driver_r_2_out_113), .row28(driver_r_2_out_117), .row29(driver_r_2_out_121),
    .row30(driver_r_2_out_125), .row31(driver_r_2_out_129));
endmodule

module control_elems (
  input  [8:0] b,
  input  [15:0] ASSH,
  output _1,
  output _2,
  output _3,
  output _4,
  output _6,
  output _7,
  output _9,
  output _10,
  output _11,
  output _5,
  output _8,
  output is_a_chest
);

  look_on_minimap look_on_minimap_1 ();
  wall_pass wall_pass_1 (.in_1(ASSH[7:0]), .out_2(_8));
  chest_or_not chest_or_not_1 (.Worm(ASSH[7:0]), .Chest(is_a_chest));
  wall_pass wall_pass_2 (.in_1(ASSH[15:8]), .out_2(_5));

  assign _1 = b[0];
  assign _2 = b[1];
  assign _3 = b[2];
  assign _4 = b[3];
  assign _6 = b[4];
  assign _7 = b[5];
  assign _9 = b[6];
  assign _10 = b[7];
  assign _11 = b[8];

  // Notes on the sheet:
  //   Взгляд на миникарту
  //   Дальний
endmodule

module wall_pass (
  input  [7:0] in_1,
  output out_2
);

  Comparator comparator_1 (.a(8'h23), .b(in_1), .eq(out_2));  // open: gt, lt
endmodule

module driver_r (
  input  [1:0] curr_enem,
  input  [1:0] gameState,
  input  [8:0] b,
  input  [15:0] ASSH,
  output [31:0] out_5,
  output [30:0] out_6,
  output [29:0] out_7,
  output [28:0] out_8,
  output [31:0] out_9,
  output [30:0] out_10,
  output [29:0] out_11,
  output [28:0] out_12,
  output [31:0] out_13,
  output [30:0] out_14,
  output [29:0] out_15,
  output [28:0] out_16,
  output [31:0] out_17,
  output [30:0] out_18,
  output [29:0] out_19,
  output [28:0] out_20,
  output [31:0] out_21,
  output [30:0] out_22,
  output [29:0] out_23,
  output [28:0] out_24,
  output [31:0] out_25,
  output [30:0] out_26,
  output [29:0] out_27,
  output [28:0] out_28,
  output [31:0] out_29,
  output [30:0] out_30,
  output [29:0] out_31,
  output [28:0] out_32,
  output [31:0] out_33,
  output [30:0] out_34,
  output [29:0] out_35,
  output [28:0] out_36,
  output [31:0] out_37,
  output [30:0] out_38,
  output [29:0] out_39,
  output [28:0] out_40,
  output [31:0] out_41,
  output [30:0] out_42,
  output [29:0] out_43,
  output [28:0] out_44,
  output [31:0] out_45,
  output [30:0] out_46,
  output [29:0] out_47,
  output [28:0] out_48,
  output [31:0] out_49,
  output [30:0] out_50,
  output [29:0] out_51,
  output [28:0] out_52,
  output [31:0] out_53,
  output [30:0] out_54,
  output [29:0] out_55,
  output [28:0] out_56,
  output [31:0] out_57,
  output [30:0] out_58,
  output [29:0] out_59,
  output [28:0] out_60,
  output [31:0] out_61,
  output [30:0] out_62,
  output [29:0] out_63,
  output [28:0] out_64,
  output [31:0] out_65,
  output [30:0] out_66,
  output [29:0] out_67,
  output [28:0] out_68,
  output [31:0] out_69,
  output [30:0] out_70,
  output [29:0] out_71,
  output [28:0] out_72,
  output [31:0] out_73,
  output [30:0] out_74,
  output [29:0] out_75,
  output [28:0] out_76,
  output [31:0] out_77,
  output [30:0] out_78,
  output [29:0] out_79,
  output [28:0] out_80,
  output [31:0] out_81,
  output [30:0] out_82,
  output [29:0] out_83,
  output [28:0] out_84,
  output [31:0] out_85,
  output [30:0] out_86,
  output [29:0] out_87,
  output [28:0] out_88,
  output [31:0] out_89,
  output [30:0] out_90,
  output [29:0] out_91,
  output [28:0] out_92,
  output [31:0] out_93,
  output [30:0] out_94,
  output [29:0] out_95,
  output [28:0] out_96,
  output [31:0] out_97,
  output [30:0] out_98,
  output [29:0] out_99,
  output [28:0] out_100,
  output [31:0] out_101,
  output [30:0] out_102,
  output [29:0] out_103,
  output [28:0] out_104,
  output [31:0] out_105,
  output [30:0] out_106,
  output [29:0] out_107,
  output [28:0] out_108,
  output [31:0] out_109,
  output [30:0] out_110,
  output [29:0] out_111,
  output [28:0] out_112,
  output [31:0] out_113,
  output [30:0] out_114,
  output [29:0] out_115,
  output [28:0] out_116,
  output [31:0] out_117,
  output [30:0] out_118,
  output [29:0] out_119,
  output [28:0] out_120,
  output [31:0] out_121,
  output [30:0] out_122,
  output [29:0] out_123,
  output [28:0] out_124,
  output [31:0] out_125,
  output [30:0] out_126,
  output [29:0] out_127,
  output [28:0] out_128,
  output [31:0] out_129,
  output [30:0] out_130,
  output [29:0] out_131,
  output [28:0] out_132
);

  wire _1, _2, _3, _4, _5, _6, _7, _8, _9, _10, _11, control_elems_1_is_a_chest, isBattle;
  wire [28:0] _29_bit_str_1, _29_bit_str_2, _29_bit_str_3, _29_bit_str_4, _29_bit_str_5, _29_bit_str_6,
       _29_bit_str_7, _29_bit_str_8, _29_bit_str_9, _29_bit_str_10, _29_bit_str_11, _29_bit_str_12,
       _29_bit_str_13, _29_bit_str_14, _29_bit_str_15, _29_bit_str_16, _29_bit_str_17, _29_bit_str_18,
       _29_bit_str_19, _29_bit_str_20, _29_bit_str_21, _29_bit_str_22, _29_bit_str_23, _29_bit_str_24,
       _29_bit_str_25, _29_bit_str_26, _29_bit_str_27, _29_bit_str_28, _29_bit_str_29, _29_bit_str_30,
       _29_bit_str_31, _29_bit_str_32;
  wire [29:0] _30_bit_str_1, _30_bit_str_2, _30_bit_str_3, _30_bit_str_4, _30_bit_str_5, _30_bit_str_6,
       _30_bit_str_7, _30_bit_str_8, _30_bit_str_9, _30_bit_str_10, _30_bit_str_11, _30_bit_str_12,
       _30_bit_str_13, _30_bit_str_14, _30_bit_str_15, _30_bit_str_16, _30_bit_str_17, _30_bit_str_18,
       _30_bit_str_19, _30_bit_str_20, _30_bit_str_21, _30_bit_str_22, _30_bit_str_23, _30_bit_str_24,
       _30_bit_str_25, _30_bit_str_26, _30_bit_str_27, _30_bit_str_28, _30_bit_str_29, _30_bit_str_30,
       _30_bit_str_31, _30_bit_str_32;
  wire [30:0] _31_bit_str_1, _31_bit_str_2, _31_bit_str_3, _31_bit_str_4, _31_bit_str_5, _31_bit_str_6,
       _31_bit_str_7, _31_bit_str_8, _31_bit_str_9, _31_bit_str_10, _31_bit_str_11, _31_bit_str_12,
       _31_bit_str_13, _31_bit_str_14, _31_bit_str_15, _31_bit_str_16, _31_bit_str_17, _31_bit_str_18,
       _31_bit_str_19, _31_bit_str_20, _31_bit_str_21, _31_bit_str_22, _31_bit_str_23, _31_bit_str_24,
       _31_bit_str_25, _31_bit_str_26, _31_bit_str_27, _31_bit_str_28, _31_bit_str_29, _31_bit_str_30,
       _31_bit_str_31, _31_bit_str_32;
  wire [31:0] _32_bit_str_1, _32_bit_str_2, _32_bit_str_3, _32_bit_str_4, _32_bit_str_5, _32_bit_str_6,
       _32_bit_str_7, _32_bit_str_8, _32_bit_str_9, _32_bit_str_10, _32_bit_str_11, _32_bit_str_12,
       _32_bit_str_13, _32_bit_str_14, _32_bit_str_15, _32_bit_str_16, _32_bit_str_17, _32_bit_str_18,
       _32_bit_str_19, _32_bit_str_20, _32_bit_str_21, _32_bit_str_22, _32_bit_str_23, _32_bit_str_24,
       _32_bit_str_25, _32_bit_str_26, _32_bit_str_27, _32_bit_str_28, _32_bit_str_29, _32_bit_str_30,
       _32_bit_str_31, _32_bit_str_32;

  look_on_minimap look_on_minimap_1 ();
  control_elems control_elems_1 (
    .b(b), .ASSH(ASSH), ._1(_1), ._2(_2), ._3(_3), ._4(_4), ._6(_6), ._7(_7), ._9(_9), ._10(_10), ._11(_11),
    ._5(_5), ._8(_8), .is_a_chest(control_elems_1_is_a_chest));
  Shifter #(.width(32)) shifter_1 (.in(_32_bit_str_1), .\dist (5'b00100), .out(out_5));
  Shifter #(.width(32)) shifter_2 (.in(_32_bit_str_2), .\dist (5'b00100), .out(out_9));
  Shifter #(.width(32)) shifter_3 (.in(_32_bit_str_3), .\dist (5'b00100), .out(out_13));
  Shifter #(.width(32)) shifter_4 (.in(_32_bit_str_4), .\dist (5'b00100), .out(out_17));
  Shifter #(.width(32)) shifter_5 (.in(_32_bit_str_5), .\dist (5'b00100), .out(out_21));
  Shifter #(.width(32)) shifter_6 (.in(_32_bit_str_6), .\dist (5'b00100), .out(out_25));
  Shifter #(.width(32)) shifter_7 (.in(_32_bit_str_7), .\dist (5'b00100), .out(out_29));
  Shifter #(.width(32)) shifter_8 (.in(_32_bit_str_8), .\dist (5'b00100), .out(out_33));
  Shifter #(.width(32)) shifter_9 (.in(_32_bit_str_9), .\dist (5'b00100), .out(out_37));
  Shifter #(.width(32)) shifter_10 (.in(_32_bit_str_10), .\dist (5'b00100), .out(out_41));
  Shifter #(.width(32)) shifter_11 (.in(_32_bit_str_11), .\dist (5'b00100), .out(out_45));
  Shifter #(.width(32)) shifter_12 (.in(_32_bit_str_12), .\dist (5'b00100), .out(out_49));
  Shifter #(.width(32)) shifter_13 (.in(_32_bit_str_13), .\dist (5'b00100), .out(out_53));
  Shifter #(.width(32)) shifter_14 (.in(_32_bit_str_14), .\dist (5'b00100), .out(out_57));
  Shifter #(.width(32)) shifter_15 (.in(_32_bit_str_15), .\dist (5'b00100), .out(out_61));
  Shifter #(.width(32)) shifter_16 (.in(_32_bit_str_16), .\dist (5'b00100), .out(out_65));
  Shifter #(.width(32)) shifter_17 (.in(_32_bit_str_17), .\dist (5'b00100), .out(out_69));
  Shifter #(.width(32)) shifter_18 (.in(_32_bit_str_18), .\dist (5'b00100), .out(out_73));
  Shifter #(.width(32)) shifter_19 (.in(_32_bit_str_19), .\dist (5'b00100), .out(out_77));
  Shifter #(.width(32)) shifter_20 (.in(_32_bit_str_20), .\dist (5'b00100), .out(out_81));
  Shifter #(.width(32)) shifter_21 (.in(_32_bit_str_21), .\dist (5'b00100), .out(out_85));
  Shifter #(.width(32)) shifter_22 (.in(_32_bit_str_22), .\dist (5'b00100), .out(out_89));
  Shifter #(.width(32)) shifter_23 (.in(_32_bit_str_23), .\dist (5'b00100), .out(out_93));
  Shifter #(.width(32)) shifter_24 (.in(_32_bit_str_24), .\dist (5'b00100), .out(out_97));
  Shifter #(.width(32)) shifter_25 (.in(_32_bit_str_25), .\dist (5'b00100), .out(out_101));
  Shifter #(.width(32)) shifter_26 (.in(_32_bit_str_26), .\dist (5'b00100), .out(out_105));
  Shifter #(.width(32)) shifter_27 (.in(_32_bit_str_27), .\dist (5'b00100), .out(out_109));
  Shifter #(.width(32)) shifter_28 (.in(_32_bit_str_28), .\dist (5'b00100), .out(out_113));
  Shifter #(.width(32)) shifter_29 (.in(_32_bit_str_29), .\dist (5'b00100), .out(out_117));
  Shifter #(.width(32)) shifter_30 (.in(_32_bit_str_30), .\dist (5'b00100), .out(out_121));
  Shifter #(.width(32)) shifter_31 (.in(_32_bit_str_31), .\dist (5'b00100), .out(out_125));
  Shifter #(.width(32)) shifter_32 (.in(_32_bit_str_32), .\dist (5'b00100), .out(out_129));
  Tile_r_1_color tile_r_1_color_1 (
    .out_5(_29_bit_str_1), .out_6(_29_bit_str_2), .out_7(_29_bit_str_3), .out_8(_29_bit_str_4),
    .out_9(_29_bit_str_5), .out_10(_29_bit_str_6), .out_11(_29_bit_str_7), .out_12(_29_bit_str_8),
    .out_13(_29_bit_str_9), .out_14(_29_bit_str_10), .out_15(_29_bit_str_11), .out_16(_29_bit_str_12),
    .out_17(_29_bit_str_13), .out_18(_29_bit_str_14), .out_19(_29_bit_str_15), .out_20(_29_bit_str_16),
    .out_21(_29_bit_str_17), .out_22(_29_bit_str_18), .out_23(_29_bit_str_19), .out_24(_29_bit_str_20),
    .out_25(_29_bit_str_21), .out_26(_29_bit_str_22), .out_27(_29_bit_str_23), .out_28(_29_bit_str_24),
    .out_29(_29_bit_str_25), .out_30(_29_bit_str_26), .out_31(_29_bit_str_27), .out_32(_29_bit_str_28),
    .out_33(_29_bit_str_29), .out_34(_29_bit_str_30), .out_35(_29_bit_str_31), .out_36(_29_bit_str_32),
    ._11(_11), ._10(_10), .isBattle(isBattle), .is_a_chest(control_elems_1_is_a_chest));
  Comparator #(.width(2), .mode("unsigned")) comparator_1 (.a(2'b10), .b(gameState), .eq(isBattle));  // open: gt, lt
  Shifter #(.width(31)) shifter_33 (.in(_31_bit_str_1), .\dist (5'b00100), .out(out_6));
  Shifter #(.width(31)) shifter_34 (.in(_31_bit_str_2), .\dist (5'b00100), .out(out_10));
  Shifter #(.width(31)) shifter_35 (.in(_31_bit_str_3), .\dist (5'b00100), .out(out_14));
  Shifter #(.width(31)) shifter_36 (.in(_31_bit_str_4), .\dist (5'b00100), .out(out_18));
  Shifter #(.width(31)) shifter_37 (.in(_31_bit_str_5), .\dist (5'b00100), .out(out_22));
  Shifter #(.width(31)) shifter_38 (.in(_31_bit_str_6), .\dist (5'b00100), .out(out_26));
  Shifter #(.width(31)) shifter_39 (.in(_31_bit_str_7), .\dist (5'b00100), .out(out_30));
  Shifter #(.width(31)) shifter_40 (.in(_31_bit_str_8), .\dist (5'b00100), .out(out_34));
  Shifter #(.width(31)) shifter_41 (.in(_31_bit_str_9), .\dist (5'b00100), .out(out_38));
  Shifter #(.width(31)) shifter_42 (.in(_31_bit_str_10), .\dist (5'b00100), .out(out_42));
  Shifter #(.width(31)) shifter_43 (.in(_31_bit_str_11), .\dist (5'b00100), .out(out_46));
  Shifter #(.width(31)) shifter_44 (.in(_31_bit_str_12), .\dist (5'b00100), .out(out_50));
  Shifter #(.width(31)) shifter_45 (.in(_31_bit_str_13), .\dist (5'b00100), .out(out_54));
  Shifter #(.width(31)) shifter_46 (.in(_31_bit_str_14), .\dist (5'b00100), .out(out_58));
  Shifter #(.width(31)) shifter_47 (.in(_31_bit_str_15), .\dist (5'b00100), .out(out_62));
  Shifter #(.width(31)) shifter_48 (.in(_31_bit_str_16), .\dist (5'b00100), .out(out_66));
  Shifter #(.width(31)) shifter_49 (.in(_31_bit_str_17), .\dist (5'b00100), .out(out_70));
  Shifter #(.width(31)) shifter_50 (.in(_31_bit_str_18), .\dist (5'b00100), .out(out_74));
  Shifter #(.width(31)) shifter_51 (.in(_31_bit_str_19), .\dist (5'b00100), .out(out_78));
  Shifter #(.width(31)) shifter_52 (.in(_31_bit_str_20), .\dist (5'b00100), .out(out_82));
  Shifter #(.width(31)) shifter_53 (.in(_31_bit_str_21), .\dist (5'b00100), .out(out_86));
  Shifter #(.width(31)) shifter_54 (.in(_31_bit_str_22), .\dist (5'b00100), .out(out_90));
  Shifter #(.width(31)) shifter_55 (.in(_31_bit_str_23), .\dist (5'b00100), .out(out_94));
  Shifter #(.width(31)) shifter_56 (.in(_31_bit_str_24), .\dist (5'b00100), .out(out_98));
  Shifter #(.width(31)) shifter_57 (.in(_31_bit_str_25), .\dist (5'b00100), .out(out_102));
  Shifter #(.width(31)) shifter_58 (.in(_31_bit_str_26), .\dist (5'b00100), .out(out_106));
  Shifter #(.width(31)) shifter_59 (.in(_31_bit_str_27), .\dist (5'b00100), .out(out_110));
  Shifter #(.width(31)) shifter_60 (.in(_31_bit_str_28), .\dist (5'b00100), .out(out_114));
  Shifter #(.width(31)) shifter_61 (.in(_31_bit_str_29), .\dist (5'b00100), .out(out_118));
  Shifter #(.width(31)) shifter_62 (.in(_31_bit_str_30), .\dist (5'b00100), .out(out_122));
  Shifter #(.width(31)) shifter_63 (.in(_31_bit_str_31), .\dist (5'b00100), .out(out_126));
  Shifter #(.width(31)) shifter_64 (.in(_31_bit_str_32), .\dist (5'b00100), .out(out_130));
  Tile_r_2_color tile_r_2_color_1 (
    ._11(_11), ._10(_10), ._9(_9), ._8(_8), ._7(_7), .isBattle(isBattle), .out_7(_30_bit_str_1),
    .out_8(_30_bit_str_2), .out_9(_30_bit_str_3), .out_10(_30_bit_str_4), .out_11(_30_bit_str_5),
    .out_12(_30_bit_str_6), .out_13(_30_bit_str_7), .out_14(_30_bit_str_8), .out_15(_30_bit_str_9),
    .out_16(_30_bit_str_10), .out_17(_30_bit_str_11), .out_18(_30_bit_str_12), .out_19(_30_bit_str_13),
    .out_20(_30_bit_str_14), .out_21(_30_bit_str_15), .out_22(_30_bit_str_16), .out_23(_30_bit_str_17),
    .out_24(_30_bit_str_18), .out_25(_30_bit_str_19), .out_26(_30_bit_str_20), .out_27(_30_bit_str_21),
    .out_28(_30_bit_str_22), .out_29(_30_bit_str_23), .out_30(_30_bit_str_24), .out_31(_30_bit_str_25),
    .out_32(_30_bit_str_26), .out_33(_30_bit_str_27), .out_34(_30_bit_str_28), .out_35(_30_bit_str_29),
    .out_36(_30_bit_str_30), .out_37(_30_bit_str_31), .out_38(_30_bit_str_32));
  Shifter #(.width(30)) shifter_65 (.in(_30_bit_str_1), .\dist (5'b00100), .out(out_7));
  Shifter #(.width(30)) shifter_66 (.in(_30_bit_str_2), .\dist (5'b00100), .out(out_11));
  Shifter #(.width(30)) shifter_67 (.in(_30_bit_str_3), .\dist (5'b00100), .out(out_15));
  Shifter #(.width(30)) shifter_68 (.in(_30_bit_str_4), .\dist (5'b00100), .out(out_19));
  Shifter #(.width(30)) shifter_69 (.in(_30_bit_str_5), .\dist (5'b00100), .out(out_23));
  Shifter #(.width(30)) shifter_70 (.in(_30_bit_str_6), .\dist (5'b00100), .out(out_27));
  Shifter #(.width(30)) shifter_71 (.in(_30_bit_str_7), .\dist (5'b00100), .out(out_31));
  Shifter #(.width(30)) shifter_72 (.in(_30_bit_str_8), .\dist (5'b00100), .out(out_35));
  Shifter #(.width(30)) shifter_73 (.in(_30_bit_str_9), .\dist (5'b00100), .out(out_39));
  Shifter #(.width(30)) shifter_74 (.in(_30_bit_str_10), .\dist (5'b00100), .out(out_43));
  Shifter #(.width(30)) shifter_75 (.in(_30_bit_str_11), .\dist (5'b00100), .out(out_47));
  Shifter #(.width(30)) shifter_76 (.in(_30_bit_str_12), .\dist (5'b00100), .out(out_51));
  Shifter #(.width(30)) shifter_77 (.in(_30_bit_str_13), .\dist (5'b00100), .out(out_55));
  Shifter #(.width(30)) shifter_78 (.in(_30_bit_str_14), .\dist (5'b00100), .out(out_59));
  Shifter #(.width(30)) shifter_79 (.in(_30_bit_str_15), .\dist (5'b00100), .out(out_63));
  Shifter #(.width(30)) shifter_80 (.in(_30_bit_str_16), .\dist (5'b00100), .out(out_67));
  Shifter #(.width(30)) shifter_81 (.in(_30_bit_str_17), .\dist (5'b00100), .out(out_71));
  Shifter #(.width(30)) shifter_82 (.in(_30_bit_str_18), .\dist (5'b00100), .out(out_75));
  Shifter #(.width(30)) shifter_83 (.in(_30_bit_str_19), .\dist (5'b00100), .out(out_79));
  Shifter #(.width(30)) shifter_84 (.in(_30_bit_str_20), .\dist (5'b00100), .out(out_83));
  Shifter #(.width(30)) shifter_85 (.in(_30_bit_str_21), .\dist (5'b00100), .out(out_87));
  Shifter #(.width(30)) shifter_86 (.in(_30_bit_str_22), .\dist (5'b00100), .out(out_91));
  Shifter #(.width(30)) shifter_87 (.in(_30_bit_str_23), .\dist (5'b00100), .out(out_95));
  Shifter #(.width(30)) shifter_88 (.in(_30_bit_str_24), .\dist (5'b00100), .out(out_99));
  Shifter #(.width(30)) shifter_89 (.in(_30_bit_str_25), .\dist (5'b00100), .out(out_103));
  Shifter #(.width(30)) shifter_90 (.in(_30_bit_str_26), .\dist (5'b00100), .out(out_107));
  Shifter #(.width(30)) shifter_91 (.in(_30_bit_str_27), .\dist (5'b00100), .out(out_111));
  Shifter #(.width(30)) shifter_92 (.in(_30_bit_str_28), .\dist (5'b00100), .out(out_115));
  Shifter #(.width(30)) shifter_93 (.in(_30_bit_str_29), .\dist (5'b00100), .out(out_119));
  Shifter #(.width(30)) shifter_94 (.in(_30_bit_str_30), .\dist (5'b00100), .out(out_123));
  Shifter #(.width(30)) shifter_95 (.in(_30_bit_str_31), .\dist (5'b00100), .out(out_127));
  Shifter #(.width(30)) shifter_96 (.in(_30_bit_str_32), .\dist (5'b00100), .out(out_131));
  Tile_r_3_color tile_r_3_color_1 (
    ._11(_11), ._10(_10), ._9(_9), ._8(_8), ._7(_7), ._6(_6), ._5(_5), ._4(_4), .isBattle(isBattle),
    .out_10(_31_bit_str_1), .out_11(_31_bit_str_2), .out_12(_31_bit_str_3), .out_13(_31_bit_str_4),
    .out_14(_31_bit_str_5), .out_15(_31_bit_str_6), .out_16(_31_bit_str_7), .out_17(_31_bit_str_8),
    .out_18(_31_bit_str_9), .out_19(_31_bit_str_10), .out_20(_31_bit_str_11), .out_21(_31_bit_str_12),
    .out_22(_31_bit_str_13), .out_23(_31_bit_str_14), .out_24(_31_bit_str_15), .out_25(_31_bit_str_16),
    .out_26(_31_bit_str_17), .out_27(_31_bit_str_18), .out_28(_31_bit_str_19), .out_29(_31_bit_str_20),
    .out_30(_31_bit_str_21), .out_31(_31_bit_str_22), .out_32(_31_bit_str_23), .out_33(_31_bit_str_24),
    .out_34(_31_bit_str_25), .out_35(_31_bit_str_26), .out_36(_31_bit_str_27), .out_37(_31_bit_str_28),
    .out_38(_31_bit_str_29), .out_39(_31_bit_str_30), .out_40(_31_bit_str_31), .out_41(_31_bit_str_32));
  Tile_r_4_color tile_r_4_color_1 (
    ._8(_8), ._6(_6), ._5(_5), ._4(_4), ._3(_3), ._2(_2), ._1(_1), .enemy(curr_enem), .gameState(gameState),
    .out_10(_32_bit_str_1), .out_11(_32_bit_str_2), .out_12(_32_bit_str_3), .out_13(_32_bit_str_4),
    .out_14(_32_bit_str_5), .out_15(_32_bit_str_6), .out_16(_32_bit_str_7), .out_17(_32_bit_str_8),
    .out_18(_32_bit_str_9), .out_19(_32_bit_str_10), .out_20(_32_bit_str_11), .out_21(_32_bit_str_12),
    .out_22(_32_bit_str_13), .out_23(_32_bit_str_14), .out_24(_32_bit_str_15), .out_25(_32_bit_str_16),
    .out_26(_32_bit_str_17), .out_27(_32_bit_str_18), .out_28(_32_bit_str_19), .out_29(_32_bit_str_20),
    .out_30(_32_bit_str_21), .out_31(_32_bit_str_22), .out_32(_32_bit_str_23), .out_33(_32_bit_str_24),
    .out_34(_32_bit_str_25), .out_35(_32_bit_str_26), .out_36(_32_bit_str_27), .out_37(_32_bit_str_28),
    .out_38(_32_bit_str_29), .out_39(_32_bit_str_30), .out_40(_32_bit_str_31), .out_41(_32_bit_str_32));
  Shifter #(.width(29)) shifter_97 (.in(_29_bit_str_1), .\dist (5'b00100), .out(out_8));
  Shifter #(.width(29)) shifter_98 (.in(_29_bit_str_2), .\dist (5'b00100), .out(out_12));
  Shifter #(.width(29)) shifter_99 (.in(_29_bit_str_3), .\dist (5'b00100), .out(out_16));
  Shifter #(.width(29)) shifter_100 (.in(_29_bit_str_4), .\dist (5'b00100), .out(out_20));
  Shifter #(.width(29)) shifter_101 (.in(_29_bit_str_5), .\dist (5'b00100), .out(out_24));
  Shifter #(.width(29)) shifter_102 (.in(_29_bit_str_6), .\dist (5'b00100), .out(out_28));
  Shifter #(.width(29)) shifter_103 (.in(_29_bit_str_7), .\dist (5'b00100), .out(out_32));
  Shifter #(.width(29)) shifter_104 (.in(_29_bit_str_8), .\dist (5'b00100), .out(out_36));
  Shifter #(.width(29)) shifter_105 (.in(_29_bit_str_9), .\dist (5'b00100), .out(out_40));
  Shifter #(.width(29)) shifter_106 (.in(_29_bit_str_10), .\dist (5'b00100), .out(out_44));
  Shifter #(.width(29)) shifter_107 (.in(_29_bit_str_11), .\dist (5'b00100), .out(out_48));
  Shifter #(.width(29)) shifter_108 (.in(_29_bit_str_12), .\dist (5'b00100), .out(out_52));
  Shifter #(.width(29)) shifter_109 (.in(_29_bit_str_13), .\dist (5'b00100), .out(out_56));
  Shifter #(.width(29)) shifter_110 (.in(_29_bit_str_14), .\dist (5'b00100), .out(out_60));
  Shifter #(.width(29)) shifter_111 (.in(_29_bit_str_15), .\dist (5'b00100), .out(out_64));
  Shifter #(.width(29)) shifter_112 (.in(_29_bit_str_16), .\dist (5'b00100), .out(out_68));
  Shifter #(.width(29)) shifter_113 (.in(_29_bit_str_17), .\dist (5'b00100), .out(out_72));
  Shifter #(.width(29)) shifter_114 (.in(_29_bit_str_18), .\dist (5'b00100), .out(out_76));
  Shifter #(.width(29)) shifter_115 (.in(_29_bit_str_19), .\dist (5'b00100), .out(out_80));
  Shifter #(.width(29)) shifter_116 (.in(_29_bit_str_20), .\dist (5'b00100), .out(out_84));
  Shifter #(.width(29)) shifter_117 (.in(_29_bit_str_21), .\dist (5'b00100), .out(out_88));
  Shifter #(.width(29)) shifter_118 (.in(_29_bit_str_22), .\dist (5'b00100), .out(out_92));
  Shifter #(.width(29)) shifter_119 (.in(_29_bit_str_23), .\dist (5'b00100), .out(out_96));
  Shifter #(.width(29)) shifter_120 (.in(_29_bit_str_24), .\dist (5'b00100), .out(out_100));
  Shifter #(.width(29)) shifter_121 (.in(_29_bit_str_25), .\dist (5'b00100), .out(out_104));
  Shifter #(.width(29)) shifter_122 (.in(_29_bit_str_26), .\dist (5'b00100), .out(out_108));
  Shifter #(.width(29)) shifter_123 (.in(_29_bit_str_27), .\dist (5'b00100), .out(out_112));
  Shifter #(.width(29)) shifter_124 (.in(_29_bit_str_28), .\dist (5'b00100), .out(out_116));
  Shifter #(.width(29)) shifter_125 (.in(_29_bit_str_29), .\dist (5'b00100), .out(out_120));
  Shifter #(.width(29)) shifter_126 (.in(_29_bit_str_30), .\dist (5'b00100), .out(out_124));
  Shifter #(.width(29)) shifter_127 (.in(_29_bit_str_31), .\dist (5'b00100), .out(out_128));
  Shifter #(.width(29)) shifter_128 (.in(_29_bit_str_32), .\dist (5'b00100), .out(out_132));

  // Other names for the same wires on the sheet: enemy[1:0] = curr_enem

  // Notes on the sheet:
  //   ФОН / 4 Цвет
  //   Void / 3 Цвет
  //   Void / 2 Цвет
  //   Void / 1 Цвет
endmodule

module Tile_r_1_color (
  input  _11,
  input  _10,
  input  isBattle,
  input  is_a_chest,
  output [28:0] out_5,
  output [28:0] out_6,
  output [28:0] out_7,
  output [28:0] out_8,
  output [28:0] out_9,
  output [28:0] out_10,
  output [28:0] out_11,
  output [28:0] out_12,
  output [28:0] out_13,
  output [28:0] out_14,
  output [28:0] out_15,
  output [28:0] out_16,
  output [28:0] out_17,
  output [28:0] out_18,
  output [28:0] out_19,
  output [28:0] out_20,
  output [28:0] out_21,
  output [28:0] out_22,
  output [28:0] out_23,
  output [28:0] out_24,
  output [28:0] out_25,
  output [28:0] out_26,
  output [28:0] out_27,
  output [28:0] out_28,
  output [28:0] out_29,
  output [28:0] out_30,
  output [28:0] out_31,
  output [28:0] out_32,
  output [28:0] out_33,
  output [28:0] out_34,
  output [28:0] out_35,
  output [28:0] out_36
);

  wire _14, _15, chest, not_1_out;
  wire [28:0] _1_el_str_1, _1_el_str_2, _1_el_str_3, _1_el_str_4, _1_el_str_5, _1_el_str_6, _1_el_str_7,
       _1_el_str_8, _1_el_str_9, _1_el_str_10, _1_el_str_11, _1_el_str_12, _1_el_str_13, _1_el_str_14,
       _1_el_str_15, _1_el_str_16, _1_el_str_17, _1_el_str_18, _1_el_str_19, _1_el_str_20, _1_el_str_21,
       _1_el_str_22, _1_el_str_23, _1_el_str_24, _1_el_str_25, _1_el_str_26, _1_el_str_27, _1_el_str_28,
       _1_el_str_29, _1_el_str_30, _1_el_str_31, _1_el_str_32, bit_extender_1_out, bit_extender_2_out,
       bit_extender_3_out, bit_extender_4_out, bit_extender_5_out, bit_extender_6_out, chest_str_1,
       chest_str_2, chest_str_3, chest_str_4, chest_str_5, chest_str_6, chest_str_7, chest_str_8,
       chest_str_9, chest_str_10, chest_str_11, chest_str_12, chest_str_13, chest_str_14, chest_str_15,
       chest_str_16, chest_str_17, chest_str_18, chest_str_19, chest_str_20, chest_str_21, chest_str_22,
       chest_str_23, chest_str_24, chest_str_25, chest_str_26, chest_str_27, chest_str_28, chest_str_29,
       chest_str_30, chest_str_31, chest_str_32;

  assign _15 = not_1_out ? _11 : 1'bz;  // Controlled_Buffer controlled_buffer_1
  assign _14 = not_1_out ? _10 : 1'bz;  // Controlled_Buffer controlled_buffer_2
  not not_1 (not_1_out, isBattle);
  assign chest = not_1_out ? is_a_chest : 1'bz;  // Controlled_Buffer controlled_buffer_3
  assign chest = isBattle ? 1'b0 : 1'bz;  // Controlled_Buffer controlled_buffer_4
  assign _15 = isBattle ? 1'b0 : 1'bz;  // Controlled_Buffer controlled_buffer_5
  assign _14 = isBattle ? 1'b0 : 1'bz;  // Controlled_Buffer controlled_buffer_6
  assign _1_el_str_1 = _15 ? {29{1'b0}} : 29'bz;  // Controlled_Buffer controlled_buffer_7
  assign _1_el_str_2 = _15 ? {29{1'b0}} : 29'bz;  // Controlled_Buffer controlled_buffer_8
  assign _1_el_str_3 = _15 ? 29'h3 : 29'bz;  // Controlled_Buffer controlled_buffer_9
  assign _1_el_str_4 = _15 ? 29'hf : 29'bz;  // Controlled_Buffer controlled_buffer_10
  assign _1_el_str_5 = _15 ? 29'h3f : 29'bz;  // Controlled_Buffer controlled_buffer_11
  assign _1_el_str_6 = _15 ? 29'hff : 29'bz;  // Controlled_Buffer controlled_buffer_12
  assign _1_el_str_7 = _15 ? 29'hff : 29'bz;  // Controlled_Buffer controlled_buffer_13
  assign _1_el_str_8 = _15 ? 29'hff : 29'bz;  // Controlled_Buffer controlled_buffer_14
  assign _1_el_str_9 = _15 ? 29'hff : 29'bz;  // Controlled_Buffer controlled_buffer_15
  assign _1_el_str_10 = _15 ? 29'hff : 29'bz;  // Controlled_Buffer controlled_buffer_16
  assign _1_el_str_11 = _15 ? 29'hff : 29'bz;  // Controlled_Buffer controlled_buffer_17
  assign _1_el_str_12 = _15 ? 29'hff : 29'bz;  // Controlled_Buffer controlled_buffer_18
  assign _1_el_str_13 = _15 ? 29'hff : 29'bz;  // Controlled_Buffer controlled_buffer_19
  assign _1_el_str_14 = _15 ? 29'hff : 29'bz;  // Controlled_Buffer controlled_buffer_20
  assign _1_el_str_15 = _15 ? 29'hff : 29'bz;  // Controlled_Buffer controlled_buffer_21
  assign _1_el_str_16 = _15 ? 29'hff : 29'bz;  // Controlled_Buffer controlled_buffer_22
  assign _1_el_str_17 = _15 ? 29'hff : 29'bz;  // Controlled_Buffer controlled_buffer_23
  assign _1_el_str_18 = _15 ? 29'hff : 29'bz;  // Controlled_Buffer controlled_buffer_24
  assign _1_el_str_19 = _15 ? 29'hff : 29'bz;  // Controlled_Buffer controlled_buffer_25
  assign _1_el_str_20 = _15 ? 29'hff : 29'bz;  // Controlled_Buffer controlled_buffer_26
  assign _1_el_str_21 = _15 ? 29'hff : 29'bz;  // Controlled_Buffer controlled_buffer_27
  assign _1_el_str_22 = _15 ? 29'hff : 29'bz;  // Controlled_Buffer controlled_buffer_28
  assign _1_el_str_23 = _15 ? 29'hff : 29'bz;  // Controlled_Buffer controlled_buffer_29
  assign _1_el_str_24 = _15 ? 29'hff : 29'bz;  // Controlled_Buffer controlled_buffer_30
  assign _1_el_str_25 = _15 ? 29'h7f : 29'bz;  // Controlled_Buffer controlled_buffer_31
  assign _1_el_str_26 = _15 ? 29'h3f : 29'bz;  // Controlled_Buffer controlled_buffer_32
  assign _1_el_str_27 = _15 ? 29'hf : 29'bz;  // Controlled_Buffer controlled_buffer_33
  assign _1_el_str_28 = _15 ? 29'h3 : 29'bz;  // Controlled_Buffer controlled_buffer_34
  assign _1_el_str_29 = _15 ? 29'h1 : 29'bz;  // Controlled_Buffer controlled_buffer_35
  assign _1_el_str_30 = _15 ? {29{1'b0}} : 29'bz;  // Controlled_Buffer controlled_buffer_36
  assign _1_el_str_31 = _15 ? {29{1'b0}} : 29'bz;  // Controlled_Buffer controlled_buffer_37
  assign _1_el_str_32 = _15 ? {29{1'b0}} : 29'bz;  // Controlled_Buffer controlled_buffer_38
  assign chest_str_19 = chest ? bit_extender_1_out : 29'bz;  // Controlled_Buffer controlled_buffer_39
  assign bit_extender_1_out = {{1{1'b0}}, 28'hff80000};  // Bit_Extender bit_extender_1
  assign bit_extender_2_out = {{1{1'b0}}, 28'h180000};  // Bit_Extender bit_extender_2
  assign chest_str_20 = chest ? bit_extender_2_out : 29'bz;  // Controlled_Buffer controlled_buffer_40
  assign chest_str_21 = chest ? bit_extender_3_out : 29'bz;  // Controlled_Buffer controlled_buffer_41
  assign bit_extender_3_out = {{1{1'b0}}, 28'hfe80000};  // Bit_Extender bit_extender_3
  assign bit_extender_4_out = {{1{1'b0}}, 28'h80000};  // Bit_Extender bit_extender_4
  assign chest_str_22 = chest ? bit_extender_4_out : 29'bz;  // Controlled_Buffer controlled_buffer_42
  assign chest_str_23 = chest ? bit_extender_5_out : 29'bz;  // Controlled_Buffer controlled_buffer_43
  assign bit_extender_5_out = {{1{1'b0}}, 28'h80000};  // Bit_Extender bit_extender_5
  assign bit_extender_6_out = {{1{1'b0}}, 28'hff80000};  // Bit_Extender bit_extender_6
  assign chest_str_24 = chest ? bit_extender_6_out : 29'bz;  // Controlled_Buffer controlled_buffer_44
  or_for_str_29_bit or_for_str_29_bit_1 (
    .in_1(_1_el_str_1), .in_2(chest_str_1), .out_one_str(out_5));  // open: in_3, in_4, in_5, in_6, in_7, in_8
  or_for_str_29_bit or_for_str_29_bit_2 (
    .in_1(_1_el_str_2), .in_2(chest_str_2), .out_one_str(out_6));  // open: in_3, in_4, in_5, in_6, in_7, in_8
  or_for_str_29_bit or_for_str_29_bit_3 (
    .in_1(_1_el_str_3), .in_2(chest_str_3), .out_one_str(out_7));  // open: in_3, in_4, in_5, in_6, in_7, in_8
  or_for_str_29_bit or_for_str_29_bit_4 (
    .in_1(_1_el_str_4), .in_2(chest_str_4), .out_one_str(out_8));  // open: in_3, in_4, in_5, in_6, in_7, in_8
  or_for_str_29_bit or_for_str_29_bit_5 (
    .in_1(_1_el_str_5), .in_2(chest_str_5), .out_one_str(out_9));  // open: in_3, in_4, in_5, in_6, in_7, in_8
  or_for_str_29_bit or_for_str_29_bit_6 (
    .in_1(_1_el_str_6), .in_2(chest_str_6), .out_one_str(out_10));  // open: in_3, in_4, in_5, in_6, in_7, in_8
  or_for_str_29_bit or_for_str_29_bit_7 (
    .in_1(_1_el_str_7), .in_2(chest_str_7), .out_one_str(out_11));  // open: in_3, in_4, in_5, in_6, in_7, in_8
  or_for_str_29_bit or_for_str_29_bit_8 (
    .in_1(_1_el_str_8), .in_2(chest_str_8), .out_one_str(out_12));  // open: in_3, in_4, in_5, in_6, in_7, in_8
  or_for_str_29_bit or_for_str_29_bit_9 (
    .in_1(_1_el_str_9), .in_2(chest_str_9), .out_one_str(out_13));  // open: in_3, in_4, in_5, in_6, in_7, in_8
  or_for_str_29_bit or_for_str_29_bit_10 (
    .in_1(_1_el_str_10), .in_2(chest_str_10), .out_one_str(out_14));  // open: in_3, in_4, in_5, in_6, in_7, in_8
  or_for_str_29_bit or_for_str_29_bit_11 (
    .in_1(_1_el_str_11), .in_2(chest_str_11), .out_one_str(out_15));  // open: in_3, in_4, in_5, in_6, in_7, in_8
  or_for_str_29_bit or_for_str_29_bit_12 (
    .in_1(_1_el_str_12), .in_2(chest_str_12), .out_one_str(out_16));  // open: in_3, in_4, in_5, in_6, in_7, in_8
  or_for_str_29_bit or_for_str_29_bit_13 (
    .in_1(_1_el_str_13), .in_2(chest_str_13), .out_one_str(out_17));  // open: in_3, in_4, in_5, in_6, in_7, in_8
  or_for_str_29_bit or_for_str_29_bit_14 (
    .in_1(_1_el_str_14), .in_2(chest_str_14), .out_one_str(out_18));  // open: in_3, in_4, in_5, in_6, in_7, in_8
  or_for_str_29_bit or_for_str_29_bit_15 (
    .in_1(_1_el_str_15), .in_2(chest_str_15), .out_one_str(out_19));  // open: in_3, in_4, in_5, in_6, in_7, in_8
  or_for_str_29_bit or_for_str_29_bit_16 (
    .in_1(_1_el_str_16), .in_2(chest_str_16), .out_one_str(out_20));  // open: in_3, in_4, in_5, in_6, in_7, in_8
  or_for_str_29_bit or_for_str_29_bit_17 (
    .in_1(_1_el_str_17), .in_2(chest_str_17), .out_one_str(out_21));  // open: in_3, in_4, in_5, in_6, in_7, in_8
  or_for_str_29_bit or_for_str_29_bit_18 (
    .in_1(_1_el_str_18), .in_2(chest_str_18), .out_one_str(out_22));  // open: in_3, in_4, in_5, in_6, in_7, in_8
  or_for_str_29_bit or_for_str_29_bit_19 (
    .in_1(_1_el_str_19), .in_2(chest_str_19), .out_one_str(out_23));  // open: in_3, in_4, in_5, in_6, in_7, in_8
  or_for_str_29_bit or_for_str_29_bit_20 (
    .in_1(_1_el_str_20), .in_2(chest_str_20), .out_one_str(out_24));  // open: in_3, in_4, in_5, in_6, in_7, in_8
  or_for_str_29_bit or_for_str_29_bit_21 (
    .in_1(_1_el_str_21), .in_2(chest_str_21), .out_one_str(out_25));  // open: in_3, in_4, in_5, in_6, in_7, in_8
  or_for_str_29_bit or_for_str_29_bit_22 (
    .in_1(_1_el_str_22), .in_2(chest_str_22), .out_one_str(out_26));  // open: in_3, in_4, in_5, in_6, in_7, in_8
  or_for_str_29_bit or_for_str_29_bit_23 (
    .in_1(_1_el_str_23), .in_2(chest_str_23), .out_one_str(out_27));  // open: in_3, in_4, in_5, in_6, in_7, in_8
  or_for_str_29_bit or_for_str_29_bit_24 (
    .in_1(_1_el_str_24), .in_2(chest_str_24), .out_one_str(out_28));  // open: in_3, in_4, in_5, in_6, in_7, in_8
  or_for_str_29_bit or_for_str_29_bit_25 (
    .in_1(_1_el_str_25), .in_2(chest_str_25), .out_one_str(out_29));  // open: in_3, in_4, in_5, in_6, in_7, in_8
  or_for_str_29_bit or_for_str_29_bit_26 (
    .in_1(_1_el_str_26), .in_2(chest_str_26), .out_one_str(out_30));  // open: in_3, in_4, in_5, in_6, in_7, in_8
  or_for_str_29_bit or_for_str_29_bit_27 (
    .in_1(_1_el_str_27), .in_2(chest_str_27), .out_one_str(out_31));  // open: in_3, in_4, in_5, in_6, in_7, in_8
  or_for_str_29_bit or_for_str_29_bit_28 (
    .in_1(_1_el_str_28), .in_2(chest_str_28), .out_one_str(out_32));  // open: in_3, in_4, in_5, in_6, in_7, in_8
  or_for_str_29_bit or_for_str_29_bit_29 (
    .in_1(_1_el_str_29), .in_2(chest_str_29), .out_one_str(out_33));  // open: in_3, in_4, in_5, in_6, in_7, in_8
  or_for_str_29_bit or_for_str_29_bit_30 (
    .in_1(_1_el_str_30), .in_2(chest_str_30), .out_one_str(out_34));  // open: in_3, in_4, in_5, in_6, in_7, in_8
  or_for_str_29_bit or_for_str_29_bit_31 (
    .in_1(_1_el_str_31), .in_2(chest_str_31), .out_one_str(out_35));  // open: in_3, in_4, in_5, in_6, in_7, in_8
  or_for_str_29_bit or_for_str_29_bit_32 (
    .in_1(_1_el_str_32), .in_2(chest_str_32), .out_one_str(out_36));  // open: in_3, in_4, in_5, in_6, in_7, in_8

  // Other names for the same wires on the sheet: str_1[28:0] = out_5; str_2[28:0] = out_6; str_3[28:0] = out_7;
  //   str_4[28:0] = out_8; str_5[28:0] = out_9; str_6[28:0] = out_10; str_7[28:0] = out_11; str_8[28:0] = out_12;
  //   str_9[28:0] = out_13; str_10[28:0] = out_14; str_11[28:0] = out_15; str_12[28:0] = out_16;
  //   str_13[28:0] = out_17; str_14[28:0] = out_18; str_15[28:0] = out_19; str_16[28:0] = out_20;
  //   str_17[28:0] = out_21; str_18[28:0] = out_22; str_19[28:0] = out_23; str_20[28:0] = out_24;
  //   str_21[28:0] = out_25; str_22[28:0] = out_26; str_23[28:0] = out_27; str_24[28:0] = out_28;
  //   str_25[28:0] = out_29; str_26[28:0] = out_30; str_27[28:0] = out_31; str_28[28:0] = out_32;
  //   str_29[28:0] = out_33; str_30[28:0] = out_34; str_31[28:0] = out_35; str_32[28:0] = out_36

  // Notes on the sheet:
  //   1 цвет
endmodule

module Tile_r_2_color (
  input  _11,
  input  _10,
  input  _9,
  input  _8,
  input  _7,
  input  isBattle,
  output [29:0] out_7,
  output [29:0] out_8,
  output [29:0] out_9,
  output [29:0] out_10,
  output [29:0] out_11,
  output [29:0] out_12,
  output [29:0] out_13,
  output [29:0] out_14,
  output [29:0] out_15,
  output [29:0] out_16,
  output [29:0] out_17,
  output [29:0] out_18,
  output [29:0] out_19,
  output [29:0] out_20,
  output [29:0] out_21,
  output [29:0] out_22,
  output [29:0] out_23,
  output [29:0] out_24,
  output [29:0] out_25,
  output [29:0] out_26,
  output [29:0] out_27,
  output [29:0] out_28,
  output [29:0] out_29,
  output [29:0] out_30,
  output [29:0] out_31,
  output [29:0] out_32,
  output [29:0] out_33,
  output [29:0] out_34,
  output [29:0] out_35,
  output [29:0] out_36,
  output [29:0] out_37,
  output [29:0] out_38
);

  wire _9_t, _10_t, _11_t, _12, _13, and_1_out, and_2_out, and_3_out, and_4_out, not_1_out;
  wire [29:0] _1_el_str_1, _1_el_str_2, _1_el_str_3, _1_el_str_4, _1_el_str_5, _1_el_str_6, _1_el_str_7,
       _1_el_str_8, _1_el_str_9, _1_el_str_10, _1_el_str_11, _1_el_str_12, _1_el_str_13, _1_el_str_14,
       _1_el_str_15, _1_el_str_16, _1_el_str_17, _1_el_str_18, _1_el_str_19, _1_el_str_20, _1_el_str_21,
       _1_el_str_22, _1_el_str_23, _1_el_str_24, _1_el_str_25, _1_el_str_26, _1_el_str_27, _1_el_str_28,
       _1_el_str_29, _1_el_str_30, _1_el_str_31, _1_el_str_32, _12_el_str_1, _12_el_str_2, _12_el_str_3,
       _12_el_str_4, _12_el_str_5, _12_el_str_6, _12_el_str_7, _12_el_str_8, _12_el_str_9, _12_el_str_10,
       _12_el_str_11, _12_el_str_12, _12_el_str_13, _12_el_str_14, _12_el_str_15, _12_el_str_16,
       _12_el_str_17, _12_el_str_18, _12_el_str_19, _12_el_str_20, _12_el_str_21, _12_el_str_22,
       _12_el_str_23, _12_el_str_24, _12_el_str_25, _12_el_str_26, _12_el_str_27, _12_el_str_28,
       _12_el_str_29, _12_el_str_30, _12_el_str_31, _12_el_str_32, _13_el_str_1, _13_el_str_2, _13_el_str_3,
       _13_el_str_4, _13_el_str_5, _13_el_str_6, _13_el_str_7, _13_el_str_8, _13_el_str_9, _13_el_str_10,
       _13_el_str_11, _13_el_str_12, _13_el_str_13, _13_el_str_14, _13_el_str_15, _13_el_str_16,
       _13_el_str_17, _13_el_str_18, _13_el_str_19, _13_el_str_20, _13_el_str_21, _13_el_str_22,
       _13_el_str_23, _13_el_str_24, _13_el_str_25, _13_el_str_26, _13_el_str_27, _13_el_str_28,
       _13_el_str_29, _13_el_str_30, _13_el_str_31, _13_el_str_32;

  assign _1_el_str_1 = _10_t ? {30{1'b0}} : 30'bz;  // Controlled_Buffer controlled_buffer_1
  assign _1_el_str_2 = _10_t ? {30{1'b0}} : 30'bz;  // Controlled_Buffer controlled_buffer_2
  assign _1_el_str_3 = _10_t ? {30{1'b0}} : 30'bz;  // Controlled_Buffer controlled_buffer_3
  assign _1_el_str_4 = _10_t ? {30{1'b0}} : 30'bz;  // Controlled_Buffer controlled_buffer_4
  assign _1_el_str_5 = _10_t ? {30{1'b0}} : 30'bz;  // Controlled_Buffer controlled_buffer_5
  assign _1_el_str_6 = _10_t ? 30'h300 : 30'bz;  // Controlled_Buffer controlled_buffer_6
  assign _1_el_str_7 = _10_t ? 30'hf00 : 30'bz;  // Controlled_Buffer controlled_buffer_7
  assign _1_el_str_8 = _10_t ? 30'h3f00 : 30'bz;  // Controlled_Buffer controlled_buffer_8
  assign _1_el_str_9 = _10_t ? 30'hff00 : 30'bz;  // Controlled_Buffer controlled_buffer_9
  assign _1_el_str_10 = _10_t ? 30'hff00 : 30'bz;  // Controlled_Buffer controlled_buffer_10
  assign _1_el_str_11 = _10_t ? 30'hff00 : 30'bz;  // Controlled_Buffer controlled_buffer_11
  assign _1_el_str_12 = _10_t ? 30'hff00 : 30'bz;  // Controlled_Buffer controlled_buffer_12
  assign _1_el_str_13 = _10_t ? 30'hff00 : 30'bz;  // Controlled_Buffer controlled_buffer_13
  assign _1_el_str_14 = _10_t ? 30'hff00 : 30'bz;  // Controlled_Buffer controlled_buffer_14
  assign _1_el_str_15 = _10_t ? 30'hff00 : 30'bz;  // Controlled_Buffer controlled_buffer_15
  assign _1_el_str_16 = _10_t ? 30'hff00 : 30'bz;  // Controlled_Buffer controlled_buffer_16
  assign _1_el_str_17 = _10_t ? 30'hff00 : 30'bz;  // Controlled_Buffer controlled_buffer_17
  assign _1_el_str_18 = _10_t ? 30'hff00 : 30'bz;  // Controlled_Buffer controlled_buffer_18
  assign _1_el_str_19 = _10_t ? 30'hff00 : 30'bz;  // Controlled_Buffer controlled_buffer_19
  assign _1_el_str_20 = _10_t ? 30'h7f00 : 30'bz;  // Controlled_Buffer controlled_buffer_20
  assign _1_el_str_21 = _10_t ? 30'h3f00 : 30'bz;  // Controlled_Buffer controlled_buffer_21
  assign _1_el_str_22 = _10_t ? 30'hf00 : 30'bz;  // Controlled_Buffer controlled_buffer_22
  assign _1_el_str_23 = _10_t ? 30'h300 : 30'bz;  // Controlled_Buffer controlled_buffer_23
  assign _1_el_str_24 = _10_t ? 30'h100 : 30'bz;  // Controlled_Buffer controlled_buffer_24
  assign _1_el_str_25 = _10_t ? {30{1'b0}} : 30'bz;  // Controlled_Buffer controlled_buffer_25
  assign _1_el_str_26 = _10_t ? {30{1'b0}} : 30'bz;  // Controlled_Buffer controlled_buffer_26
  assign _1_el_str_27 = _10_t ? {30{1'b0}} : 30'bz;  // Controlled_Buffer controlled_buffer_27
  assign _1_el_str_28 = _10_t ? {30{1'b0}} : 30'bz;  // Controlled_Buffer controlled_buffer_28
  assign _1_el_str_29 = _10_t ? {30{1'b0}} : 30'bz;  // Controlled_Buffer controlled_buffer_29
  assign _1_el_str_30 = _10_t ? {30{1'b0}} : 30'bz;  // Controlled_Buffer controlled_buffer_30
  assign _1_el_str_31 = _10_t ? {30{1'b0}} : 30'bz;  // Controlled_Buffer controlled_buffer_31
  assign _1_el_str_32 = _10_t ? {30{1'b0}} : 30'bz;  // Controlled_Buffer controlled_buffer_32
  assign _13_el_str_1 = _13 ? {30{1'b0}} : 30'bz;  // Controlled_Buffer controlled_buffer_33
  assign _13_el_str_2 = _13 ? {30{1'b0}} : 30'bz;  // Controlled_Buffer controlled_buffer_34
  assign _13_el_str_3 = _13 ? {30{1'b0}} : 30'bz;  // Controlled_Buffer controlled_buffer_35
  assign _13_el_str_4 = _13 ? {30{1'b0}} : 30'bz;  // Controlled_Buffer controlled_buffer_36
  assign _13_el_str_5 = _13 ? {30{1'b0}} : 30'bz;  // Controlled_Buffer controlled_buffer_37
  assign _13_el_str_6 = _13 ? 30'hff : 30'bz;  // Controlled_Buffer controlled_buffer_38
  assign _13_el_str_7 = _13 ? 30'hff : 30'bz;  // Controlled_Buffer controlled_buffer_39
  assign _13_el_str_8 = _13 ? 30'hff : 30'bz;  // Controlled_Buffer controlled_buffer_40
  assign _13_el_str_9 = _13 ? 30'hff : 30'bz;  // Controlled_Buffer controlled_buffer_41
  assign _13_el_str_10 = _13 ? 30'hff : 30'bz;  // Controlled_Buffer controlled_buffer_42
  assign _13_el_str_11 = _13 ? 30'hff : 30'bz;  // Controlled_Buffer controlled_buffer_43
  assign _13_el_str_12 = _13 ? 30'hff : 30'bz;  // Controlled_Buffer controlled_buffer_44
  assign _13_el_str_13 = _13 ? 30'hff : 30'bz;  // Controlled_Buffer controlled_buffer_45
  assign _13_el_str_14 = _13 ? 30'hff : 30'bz;  // Controlled_Buffer controlled_buffer_46
  assign _13_el_str_15 = _13 ? 30'hff : 30'bz;  // Controlled_Buffer controlled_buffer_47
  assign _13_el_str_16 = _13 ? 30'hff : 30'bz;  // Controlled_Buffer controlled_buffer_48
  assign _13_el_str_17 = _13 ? 30'hff : 30'bz;  // Controlled_Buffer controlled_buffer_49
  assign _13_el_str_18 = _13 ? 30'hff : 30'bz;  // Controlled_Buffer controlled_buffer_50
  assign _13_el_str_19 = _13 ? 30'hff : 30'bz;  // Controlled_Buffer controlled_buffer_51
  assign _13_el_str_20 = _13 ? 30'hff : 30'bz;  // Controlled_Buffer controlled_buffer_52
  assign _13_el_str_21 = _13 ? 30'hff : 30'bz;  // Controlled_Buffer controlled_buffer_53
  assign _13_el_str_22 = _13 ? 30'hff : 30'bz;  // Controlled_Buffer controlled_buffer_54
  assign _13_el_str_23 = _13 ? 30'hff : 30'bz;  // Controlled_Buffer controlled_buffer_55
  assign _13_el_str_24 = _13 ? 30'hff : 30'bz;  // Controlled_Buffer controlled_buffer_56
  assign _13_el_str_25 = _13 ? {30{1'b0}} : 30'bz;  // Controlled_Buffer controlled_buffer_57
  assign _13_el_str_26 = _13 ? {30{1'b0}} : 30'bz;  // Controlled_Buffer controlled_buffer_58
  assign _13_el_str_27 = _13 ? {30{1'b0}} : 30'bz;  // Controlled_Buffer controlled_buffer_59
  assign _13_el_str_28 = _13 ? {30{1'b0}} : 30'bz;  // Controlled_Buffer controlled_buffer_60
  assign _13_el_str_29 = _13 ? {30{1'b0}} : 30'bz;  // Controlled_Buffer controlled_buffer_61
  assign _13_el_str_30 = _13 ? {30{1'b0}} : 30'bz;  // Controlled_Buffer controlled_buffer_62
  assign _13_el_str_31 = _13 ? {30{1'b0}} : 30'bz;  // Controlled_Buffer controlled_buffer_63
  assign _13_el_str_32 = _13 ? {30{1'b0}} : 30'bz;  // Controlled_Buffer controlled_buffer_64
  assign _12_el_str_1 = _12 ? {30{1'b0}} : 30'bz;  // Controlled_Buffer controlled_buffer_65
  assign _12_el_str_2 = _12 ? {30{1'b0}} : 30'bz;  // Controlled_Buffer controlled_buffer_66
  assign _12_el_str_3 = _12 ? {30{1'b0}} : 30'bz;  // Controlled_Buffer controlled_buffer_67
  assign _12_el_str_4 = _12 ? {30{1'b0}} : 30'bz;  // Controlled_Buffer controlled_buffer_68
  assign _12_el_str_5 = _12 ? {30{1'b0}} : 30'bz;  // Controlled_Buffer controlled_buffer_69
  assign _12_el_str_6 = _12 ? 30'h1fffff00 : 30'bz;  // Controlled_Buffer controlled_buffer_70
  assign _12_el_str_7 = _12 ? 30'h1fffff00 : 30'bz;  // Controlled_Buffer controlled_buffer_71
  assign _12_el_str_8 = _12 ? 30'h1fffff00 : 30'bz;  // Controlled_Buffer controlled_buffer_72
  assign _12_el_str_9 = _12 ? 30'h1fffff00 : 30'bz;  // Controlled_Buffer controlled_buffer_73
  assign _12_el_str_10 = _12 ? 30'h1fffff00 : 30'bz;  // Controlled_Buffer controlled_buffer_74
  assign _12_el_str_11 = _12 ? 30'h1fffff00 : 30'bz;  // Controlled_Buffer controlled_buffer_75
  assign _12_el_str_12 = _12 ? 30'h1fffff00 : 30'bz;  // Controlled_Buffer controlled_buffer_76
  assign _12_el_str_13 = _12 ? 30'h1fffff00 : 30'bz;  // Controlled_Buffer controlled_buffer_77
  assign _12_el_str_14 = _12 ? 30'h1fffff00 : 30'bz;  // Controlled_Buffer controlled_buffer_78
  assign _12_el_str_15 = _12 ? 30'h1fffff00 : 30'bz;  // Controlled_Buffer controlled_buffer_79
  assign _12_el_str_16 = _12 ? 30'h1fffff00 : 30'bz;  // Controlled_Buffer controlled_buffer_80
  assign _12_el_str_17 = _12 ? 30'h1fffff00 : 30'bz;  // Controlled_Buffer controlled_buffer_81
  assign _12_el_str_18 = _12 ? 30'h1fffff00 : 30'bz;  // Controlled_Buffer controlled_buffer_82
  assign _12_el_str_19 = _12 ? 30'h1fffff00 : 30'bz;  // Controlled_Buffer controlled_buffer_83
  assign _12_el_str_20 = _12 ? 30'h1fffff00 : 30'bz;  // Controlled_Buffer controlled_buffer_84
  assign _12_el_str_21 = _12 ? 30'h1fffff00 : 30'bz;  // Controlled_Buffer controlled_buffer_85
  assign _12_el_str_22 = _12 ? 30'h1fffff00 : 30'bz;  // Controlled_Buffer controlled_buffer_86
  assign _12_el_str_23 = _12 ? 30'h1fffff00 : 30'bz;  // Controlled_Buffer controlled_buffer_87
  assign _12_el_str_24 = _12 ? 30'h1fffff00 : 30'bz;  // Controlled_Buffer controlled_buffer_88
  assign _12_el_str_25 = _12 ? {30{1'b0}} : 30'bz;  // Controlled_Buffer controlled_buffer_89
  assign _12_el_str_26 = _12 ? {30{1'b0}} : 30'bz;  // Controlled_Buffer controlled_buffer_90
  assign _12_el_str_27 = _12 ? {30{1'b0}} : 30'bz;  // Controlled_Buffer controlled_buffer_91
  assign _12_el_str_28 = _12 ? {30{1'b0}} : 30'bz;  // Controlled_Buffer controlled_buffer_92
  assign _12_el_str_29 = _12 ? {30{1'b0}} : 30'bz;  // Controlled_Buffer controlled_buffer_93
  assign _12_el_str_30 = _12 ? {30{1'b0}} : 30'bz;  // Controlled_Buffer controlled_buffer_94
  assign _12_el_str_31 = _12 ? {30{1'b0}} : 30'bz;  // Controlled_Buffer controlled_buffer_95
  assign _12_el_str_32 = _12 ? {30{1'b0}} : 30'bz;  // Controlled_Buffer controlled_buffer_96
  assign _13 = not_1_out ? and_1_out : 1'bz;  // Controlled_Buffer controlled_buffer_97
  and and_1 (and_1_out, _9, ~_11);  // AND_Gate
  assign _12 = not_1_out ? _8 : 1'bz;  // Controlled_Buffer controlled_buffer_98
  and and_2 (and_2_out, _7, ~_10);  // AND_Gate
  assign _11_t = not_1_out ? and_2_out : 1'bz;  // Controlled_Buffer controlled_buffer_99
  and and_3 (and_3_out, _9, ~_8);  // AND_Gate
  assign _10_t = not_1_out ? and_3_out : 1'bz;  // Controlled_Buffer controlled_buffer_100
  and and_4 (and_4_out, _7, ~_8);  // AND_Gate
  assign _9_t = not_1_out ? and_4_out : 1'bz;  // Controlled_Buffer controlled_buffer_101
  not not_1 (not_1_out, isBattle);
  assign _13 = isBattle ? 1'b0 : 1'bz;  // Controlled_Buffer controlled_buffer_102
  assign _12 = isBattle ? 1'b0 : 1'bz;  // Controlled_Buffer controlled_buffer_103
  assign _11_t = isBattle ? 1'b0 : 1'bz;  // Controlled_Buffer controlled_buffer_104
  assign _10_t = isBattle ? 1'b0 : 1'bz;  // Controlled_Buffer controlled_buffer_105
  assign _9_t = isBattle ? 1'b0 : 1'bz;  // Controlled_Buffer controlled_buffer_106
  look_on_minimap look_on_minimap_1 ();
  or_for_str_30_bit or_for_str_30_bit_1 (
    .in_1(_1_el_str_1), .in_2(_13_el_str_1), .in_3(_12_el_str_1), .out_one_str(out_7));  // open: in_4, in_5, in_6, in_7, in_8
  or_for_str_30_bit or_for_str_30_bit_2 (
    .in_1(_1_el_str_2), .in_2(_13_el_str_2), .in_3(_12_el_str_2), .out_one_str(out_8));  // open: in_4, in_5, in_6, in_7, in_8
  or_for_str_30_bit or_for_str_30_bit_3 (
    .in_1(_1_el_str_3), .in_2(_13_el_str_3), .in_3(_12_el_str_3), .out_one_str(out_9));  // open: in_4, in_5, in_6, in_7, in_8
  or_for_str_30_bit or_for_str_30_bit_4 (
    .in_1(_1_el_str_4), .in_2(_13_el_str_4), .in_3(_12_el_str_4), .out_one_str(out_10));  // open: in_4, in_5, in_6, in_7, in_8
  or_for_str_30_bit or_for_str_30_bit_5 (
    .in_1(_1_el_str_5), .in_2(_13_el_str_5), .in_3(_12_el_str_5), .out_one_str(out_11));  // open: in_4, in_5, in_6, in_7, in_8
  or_for_str_30_bit or_for_str_30_bit_6 (
    .in_1(_1_el_str_6), .in_2(_13_el_str_6), .in_3(_12_el_str_6), .out_one_str(out_12));  // open: in_4, in_5, in_6, in_7, in_8
  or_for_str_30_bit or_for_str_30_bit_7 (
    .in_1(_1_el_str_7), .in_2(_13_el_str_7), .in_3(_12_el_str_7), .out_one_str(out_13));  // open: in_4, in_5, in_6, in_7, in_8
  or_for_str_30_bit or_for_str_30_bit_8 (
    .in_1(_1_el_str_8), .in_2(_13_el_str_8), .in_3(_12_el_str_8), .out_one_str(out_14));  // open: in_4, in_5, in_6, in_7, in_8
  or_for_str_30_bit or_for_str_30_bit_9 (
    .in_1(_1_el_str_9), .in_2(_13_el_str_9), .in_3(_12_el_str_9), .out_one_str(out_15));  // open: in_4, in_5, in_6, in_7, in_8
  or_for_str_30_bit or_for_str_30_bit_10 (
    .in_1(_1_el_str_10), .in_2(_13_el_str_10), .in_3(_12_el_str_10), .out_one_str(out_16));  // open: in_4, in_5, in_6, in_7, in_8
  or_for_str_30_bit or_for_str_30_bit_11 (
    .in_1(_1_el_str_11), .in_2(_13_el_str_11), .in_3(_12_el_str_11), .out_one_str(out_17));  // open: in_4, in_5, in_6, in_7, in_8
  or_for_str_30_bit or_for_str_30_bit_12 (
    .in_1(_1_el_str_12), .in_2(_13_el_str_12), .in_3(_12_el_str_12), .out_one_str(out_18));  // open: in_4, in_5, in_6, in_7, in_8
  or_for_str_30_bit or_for_str_30_bit_13 (
    .in_1(_1_el_str_13), .in_2(_13_el_str_13), .in_3(_12_el_str_13), .out_one_str(out_19));  // open: in_4, in_5, in_6, in_7, in_8
  or_for_str_30_bit or_for_str_30_bit_14 (
    .in_1(_1_el_str_14), .in_2(_13_el_str_14), .in_3(_12_el_str_14), .out_one_str(out_20));  // open: in_4, in_5, in_6, in_7, in_8
  or_for_str_30_bit or_for_str_30_bit_15 (
    .in_1(_1_el_str_15), .in_2(_13_el_str_15), .in_3(_12_el_str_15), .out_one_str(out_21));  // open: in_4, in_5, in_6, in_7, in_8
  or_for_str_30_bit or_for_str_30_bit_16 (
    .in_1(_1_el_str_16), .in_2(_13_el_str_16), .in_3(_12_el_str_16), .out_one_str(out_22));  // open: in_4, in_5, in_6, in_7, in_8
  or_for_str_30_bit or_for_str_30_bit_17 (
    .in_1(_1_el_str_17), .in_2(_13_el_str_17), .in_3(_12_el_str_17), .out_one_str(out_23));  // open: in_4, in_5, in_6, in_7, in_8
  or_for_str_30_bit or_for_str_30_bit_18 (
    .in_1(_1_el_str_18), .in_2(_13_el_str_18), .in_3(_12_el_str_18), .out_one_str(out_24));  // open: in_4, in_5, in_6, in_7, in_8
  or_for_str_30_bit or_for_str_30_bit_19 (
    .in_1(_1_el_str_19), .in_2(_13_el_str_19), .in_3(_12_el_str_19), .out_one_str(out_25));  // open: in_4, in_5, in_6, in_7, in_8
  or_for_str_30_bit or_for_str_30_bit_20 (
    .in_1(_1_el_str_20), .in_2(_13_el_str_20), .in_3(_12_el_str_20), .out_one_str(out_26));  // open: in_4, in_5, in_6, in_7, in_8
  or_for_str_30_bit or_for_str_30_bit_21 (
    .in_1(_1_el_str_21), .in_2(_13_el_str_21), .in_3(_12_el_str_21), .out_one_str(out_27));  // open: in_4, in_5, in_6, in_7, in_8
  or_for_str_30_bit or_for_str_30_bit_22 (
    .in_1(_1_el_str_22), .in_2(_13_el_str_22), .in_3(_12_el_str_22), .out_one_str(out_28));  // open: in_4, in_5, in_6, in_7, in_8
  or_for_str_30_bit or_for_str_30_bit_23 (
    .in_1(_1_el_str_23), .in_2(_13_el_str_23), .in_3(_12_el_str_23), .out_one_str(out_29));  // open: in_4, in_5, in_6, in_7, in_8
  or_for_str_30_bit or_for_str_30_bit_24 (
    .in_1(_1_el_str_24), .in_2(_13_el_str_24), .in_3(_12_el_str_24), .out_one_str(out_30));  // open: in_4, in_5, in_6, in_7, in_8
  or_for_str_30_bit or_for_str_30_bit_25 (
    .in_1(_1_el_str_25), .in_2(_13_el_str_25), .in_3(_12_el_str_25), .out_one_str(out_31));  // open: in_4, in_5, in_6, in_7, in_8
  or_for_str_30_bit or_for_str_30_bit_26 (
    .in_1(_1_el_str_26), .in_2(_13_el_str_26), .in_3(_12_el_str_26), .out_one_str(out_32));  // open: in_4, in_5, in_6, in_7, in_8
  or_for_str_30_bit or_for_str_30_bit_27 (
    .in_1(_1_el_str_27), .in_2(_13_el_str_27), .in_3(_12_el_str_27), .out_one_str(out_33));  // open: in_4, in_5, in_6, in_7, in_8
  or_for_str_30_bit or_for_str_30_bit_28 (
    .in_1(_1_el_str_28), .in_2(_13_el_str_28), .in_3(_12_el_str_28), .out_one_str(out_34));  // open: in_4, in_5, in_6, in_7, in_8
  or_for_str_30_bit or_for_str_30_bit_29 (
    .in_1(_1_el_str_29), .in_2(_13_el_str_29), .in_3(_12_el_str_29), .out_one_str(out_35));  // open: in_4, in_5, in_6, in_7, in_8
  or_for_str_30_bit or_for_str_30_bit_30 (
    .in_1(_1_el_str_30), .in_2(_13_el_str_30), .in_3(_12_el_str_30), .out_one_str(out_36));  // open: in_4, in_5, in_6, in_7, in_8
  or_for_str_30_bit or_for_str_30_bit_31 (
    .in_1(_1_el_str_31), .in_2(_13_el_str_31), .in_3(_12_el_str_31), .out_one_str(out_37));  // open: in_4, in_5, in_6, in_7, in_8
  or_for_str_30_bit or_for_str_30_bit_32 (
    .in_1(_1_el_str_32), .in_2(_13_el_str_32), .in_3(_12_el_str_32), .out_one_str(out_38));  // open: in_4, in_5, in_6, in_7, in_8

  // Other names for the same wires on the sheet: str_1[29:0] = out_7; str_2[29:0] = out_8; str_3[29:0] = out_9;
  //   str_4[29:0] = out_10; str_5[29:0] = out_11; str_6[29:0] = out_12; str_7[29:0] = out_13; str_8[29:0] = out_14;
  //   str_9[29:0] = out_15; str_10[29:0] = out_16; str_11[29:0] = out_17; str_12[29:0] = out_18;
  //   str_13[29:0] = out_19; str_14[29:0] = out_20; str_15[29:0] = out_21; str_16[29:0] = out_22;
  //   str_17[29:0] = out_23; str_18[29:0] = out_24; str_19[29:0] = out_25; str_20[29:0] = out_26;
  //   str_21[29:0] = out_27; str_22[29:0] = out_28; str_23[29:0] = out_29; str_24[29:0] = out_30;
  //   str_25[29:0] = out_31; str_26[29:0] = out_32; str_27[29:0] = out_33; str_28[29:0] = out_34;
  //   str_29[29:0] = out_35; str_30[29:0] = out_36; str_31[29:0] = out_37; str_32[29:0] = out_38

  // Notes on the sheet:
  //   2 цвет
endmodule
module Tile_r_3_color (
  input  _11,
  input  _10,
  input  _9,
  input  _8,
  input  _7,
  input  _6,
  input  _5,
  input  _4,
  input  isBattle,
  output [30:0] out_10,
  output [30:0] out_11,
  output [30:0] out_12,
  output [30:0] out_13,
  output [30:0] out_14,
  output [30:0] out_15,
  output [30:0] out_16,
  output [30:0] out_17,
  output [30:0] out_18,
  output [30:0] out_19,
  output [30:0] out_20,
  output [30:0] out_21,
  output [30:0] out_22,
  output [30:0] out_23,
  output [30:0] out_24,
  output [30:0] out_25,
  output [30:0] out_26,
  output [30:0] out_27,
  output [30:0] out_28,
  output [30:0] out_29,
  output [30:0] out_30,
  output [30:0] out_31,
  output [30:0] out_32,
  output [30:0] out_33,
  output [30:0] out_34,
  output [30:0] out_35,
  output [30:0] out_36,
  output [30:0] out_37,
  output [30:0] out_38,
  output [30:0] out_39,
  output [30:0] out_40,
  output [30:0] out_41
);

  wire _4_t, _5_t, _6_t, _7_t, _8_t, and_2_out, and_3_out, and_5_out, and_6_out, and_7_out, not_1_out;
  wire [30:0] _1_el_str_1, _1_el_str_2, _1_el_str_3, _1_el_str_4, _1_el_str_5, _1_el_str_6, _1_el_str_7,
       _1_el_str_8, _1_el_str_9, _1_el_str_10, _1_el_str_11, _1_el_str_12, _1_el_str_13, _1_el_str_14,
       _1_el_str_15, _1_el_str_16, _1_el_str_17, _1_el_str_18, _1_el_str_19, _1_el_str_20, _1_el_str_21,
       _1_el_str_22, _1_el_str_23, _1_el_str_24, _1_el_str_25, _1_el_str_26, _1_el_str_27, _1_el_str_28,
       _1_el_str_29, _1_el_str_30, _1_el_str_31, _1_el_str_32, _5_el_str_1, _5_el_str_2, _5_el_str_3,
       _5_el_str_4, _5_el_str_5, _5_el_str_6, _5_el_str_7, _5_el_str_8, _5_el_str_9, _5_el_str_10,
       _5_el_str_11, _5_el_str_12, _5_el_str_13, _5_el_str_14, _5_el_str_15, _5_el_str_16, _5_el_str_17,
       _5_el_str_18, _5_el_str_19, _5_el_str_20, _5_el_str_21, _5_el_str_22, _5_el_str_23, _5_el_str_24,
       _5_el_str_25, _5_el_str_26, _5_el_str_27, _5_el_str_28, _5_el_str_29, _5_el_str_30, _5_el_str_31,
       _5_el_str_32, _7_el_str_1, _7_el_str_2, _7_el_str_3, _7_el_str_4, _7_el_str_5, _7_el_str_6,
       _7_el_str_7, _7_el_str_8, _7_el_str_9, _7_el_str_10, _7_el_str_11, _7_el_str_12, _7_el_str_13,
       _7_el_str_14, _7_el_str_15, _7_el_str_16, _7_el_str_17, _7_el_str_18, _7_el_str_19, _7_el_str_20,
       _7_el_str_21, _7_el_str_22, _7_el_str_23, _7_el_str_24, _7_el_str_25, _7_el_str_26, _7_el_str_27,
       _7_el_str_28, _7_el_str_29, _7_el_str_30, _7_el_str_31, _7_el_str_32;

  assign _1_el_str_1 = _8_t ? {31{1'b0}} : 31'bz;  // Controlled_Buffer controlled_buffer_1
  assign _1_el_str_2 = _8_t ? {31{1'b0}} : 31'bz;  // Controlled_Buffer controlled_buffer_2
  assign _1_el_str_3 = _8_t ? {31{1'b0}} : 31'bz;  // Controlled_Buffer controlled_buffer_3
  assign _1_el_str_4 = _8_t ? {31{1'b0}} : 31'bz;  // Controlled_Buffer controlled_buffer_4
  assign _1_el_str_5 = _8_t ? {31{1'b0}} : 31'bz;  // Controlled_Buffer controlled_buffer_5
  assign _1_el_str_6 = _8_t ? {31{1'b0}} : 31'bz;  // Controlled_Buffer controlled_buffer_6
  assign _1_el_str_7 = _8_t ? {31{1'b0}} : 31'bz;  // Controlled_Buffer controlled_buffer_7
  assign _1_el_str_8 = _8_t ? {31{1'b0}} : 31'bz;  // Controlled_Buffer controlled_buffer_8
  assign _1_el_str_9 = _8_t ? 31'hff00 : 31'bz;  // Controlled_Buffer controlled_buffer_9
  assign _1_el_str_10 = _8_t ? 31'hff00 : 31'bz;  // Controlled_Buffer controlled_buffer_10
  assign _1_el_str_11 = _8_t ? 31'hff00 : 31'bz;  // Controlled_Buffer controlled_buffer_11
  assign _1_el_str_12 = _8_t ? 31'hff00 : 31'bz;  // Controlled_Buffer controlled_buffer_12
  assign _1_el_str_13 = _8_t ? 31'hff00 : 31'bz;  // Controlled_Buffer controlled_buffer_13
  assign _1_el_str_14 = _8_t ? 31'hff00 : 31'bz;  // Controlled_Buffer controlled_buffer_14
  assign _1_el_str_15 = _8_t ? 31'hff00 : 31'bz;  // Controlled_Buffer controlled_buffer_15
  assign _1_el_str_16 = _8_t ? 31'hff00 : 31'bz;  // Controlled_Buffer controlled_buffer_16
  assign _1_el_str_17 = _8_t ? 31'hff00 : 31'bz;  // Controlled_Buffer controlled_buffer_17
  assign _1_el_str_18 = _8_t ? 31'hff00 : 31'bz;  // Controlled_Buffer controlled_buffer_18
  assign _1_el_str_19 = _8_t ? 31'hff00 : 31'bz;  // Controlled_Buffer controlled_buffer_19
  assign _1_el_str_20 = _8_t ? {31{1'b0}} : 31'bz;  // Controlled_Buffer controlled_buffer_20
  assign _1_el_str_21 = _8_t ? {31{1'b0}} : 31'bz;  // Controlled_Buffer controlled_buffer_21
  assign _1_el_str_22 = _8_t ? {31{1'b0}} : 31'bz;  // Controlled_Buffer controlled_buffer_22
  assign _1_el_str_23 = _8_t ? {31{1'b0}} : 31'bz;  // Controlled_Buffer controlled_buffer_23
  assign _1_el_str_24 = _8_t ? {31{1'b0}} : 31'bz;  // Controlled_Buffer controlled_buffer_24
  assign _1_el_str_25 = _8_t ? {31{1'b0}} : 31'bz;  // Controlled_Buffer controlled_buffer_25
  assign _1_el_str_26 = _8_t ? {31{1'b0}} : 31'bz;  // Controlled_Buffer controlled_buffer_26
  assign _1_el_str_27 = _8_t ? {31{1'b0}} : 31'bz;  // Controlled_Buffer controlled_buffer_27
  assign _1_el_str_28 = _8_t ? {31{1'b0}} : 31'bz;  // Controlled_Buffer controlled_buffer_28
  assign _1_el_str_29 = _8_t ? {31{1'b0}} : 31'bz;  // Controlled_Buffer controlled_buffer_29
  assign _1_el_str_30 = _8_t ? {31{1'b0}} : 31'bz;  // Controlled_Buffer controlled_buffer_30
  assign _1_el_str_31 = _8_t ? {31{1'b0}} : 31'bz;  // Controlled_Buffer controlled_buffer_31
  assign _1_el_str_32 = _8_t ? {31{1'b0}} : 31'bz;  // Controlled_Buffer controlled_buffer_32
  assign _7_el_str_1 = _7_t ? {31{1'b0}} : 31'bz;  // Controlled_Buffer controlled_buffer_33
  assign _7_el_str_2 = _7_t ? {31{1'b0}} : 31'bz;  // Controlled_Buffer controlled_buffer_34
  assign _7_el_str_3 = _7_t ? {31{1'b0}} : 31'bz;  // Controlled_Buffer controlled_buffer_35
  assign _7_el_str_4 = _7_t ? {31{1'b0}} : 31'bz;  // Controlled_Buffer controlled_buffer_36
  assign _7_el_str_5 = _7_t ? {31{1'b0}} : 31'bz;  // Controlled_Buffer controlled_buffer_37
  assign _7_el_str_6 = _7_t ? {31{1'b0}} : 31'bz;  // Controlled_Buffer controlled_buffer_38
  assign _7_el_str_7 = _7_t ? {31{1'b0}} : 31'bz;  // Controlled_Buffer controlled_buffer_39
  assign _7_el_str_8 = _7_t ? {31{1'b0}} : 31'bz;  // Controlled_Buffer controlled_buffer_40
  assign _7_el_str_9 = _7_t ? 31'h1fff0000 : 31'bz;  // Controlled_Buffer controlled_buffer_41
  assign _7_el_str_10 = _7_t ? 31'h1fff0000 : 31'bz;  // Controlled_Buffer controlled_buffer_42
  assign _7_el_str_11 = _7_t ? 31'h1fff0000 : 31'bz;  // Controlled_Buffer controlled_buffer_43
  assign _7_el_str_12 = _7_t ? 31'h1fff0000 : 31'bz;  // Controlled_Buffer controlled_buffer_44
  assign _7_el_str_13 = _7_t ? 31'h1fff0000 : 31'bz;  // Controlled_Buffer controlled_buffer_45
  assign _7_el_str_14 = _7_t ? 31'h1fff0000 : 31'bz;  // Controlled_Buffer controlled_buffer_46
  assign _7_el_str_15 = _7_t ? 31'h1fff0000 : 31'bz;  // Controlled_Buffer controlled_buffer_47
  assign _7_el_str_16 = _7_t ? 31'h1fff0000 : 31'bz;  // Controlled_Buffer controlled_buffer_48
  assign _7_el_str_17 = _7_t ? 31'h1fff0000 : 31'bz;  // Controlled_Buffer controlled_buffer_49
  assign _7_el_str_18 = _7_t ? 31'h1fff0000 : 31'bz;  // Controlled_Buffer controlled_buffer_50
  assign _7_el_str_19 = _7_t ? 31'h1fff0000 : 31'bz;  // Controlled_Buffer controlled_buffer_51
  assign _7_el_str_20 = _7_t ? {31{1'b0}} : 31'bz;  // Controlled_Buffer controlled_buffer_52
  assign _7_el_str_21 = _7_t ? {31{1'b0}} : 31'bz;  // Controlled_Buffer controlled_buffer_53
  assign _7_el_str_22 = _7_t ? {31{1'b0}} : 31'bz;  // Controlled_Buffer controlled_buffer_54
  assign _7_el_str_23 = _7_t ? {31{1'b0}} : 31'bz;  // Controlled_Buffer controlled_buffer_55
  assign _7_el_str_24 = _7_t ? {31{1'b0}} : 31'bz;  // Controlled_Buffer controlled_buffer_56
  assign _7_el_str_25 = _7_t ? {31{1'b0}} : 31'bz;  // Controlled_Buffer controlled_buffer_57
  assign _7_el_str_26 = _7_t ? {31{1'b0}} : 31'bz;  // Controlled_Buffer controlled_buffer_58
  assign _7_el_str_27 = _7_t ? {31{1'b0}} : 31'bz;  // Controlled_Buffer controlled_buffer_59
  assign _7_el_str_28 = _7_t ? {31{1'b0}} : 31'bz;  // Controlled_Buffer controlled_buffer_60
  assign _7_el_str_29 = _7_t ? {31{1'b0}} : 31'bz;  // Controlled_Buffer controlled_buffer_61
  assign _7_el_str_30 = _7_t ? {31{1'b0}} : 31'bz;  // Controlled_Buffer controlled_buffer_62
  assign _7_el_str_31 = _7_t ? {31{1'b0}} : 31'bz;  // Controlled_Buffer controlled_buffer_63
  assign _7_el_str_32 = _7_t ? {31{1'b0}} : 31'bz;  // Controlled_Buffer controlled_buffer_64
  // AND_Gate and_1 has open pins: in0=_6, in1=_11, in2=_9, out=open
  and and_2 (and_2_out, ~_9, ~_8, _6);  // AND_Gate
  and and_3 (and_3_out, _4, ~_7, ~_10);  // AND_Gate
  and and_4 (and_3_out, ~_7, ~_8, _4);  // AND_Gate
  assign _5_el_str_1 = _5_t ? {31{1'b0}} : 31'bz;  // Controlled_Buffer controlled_buffer_65
  assign _5_el_str_2 = _5_t ? {31{1'b0}} : 31'bz;  // Controlled_Buffer controlled_buffer_66
  assign _5_el_str_3 = _5_t ? {31{1'b0}} : 31'bz;  // Controlled_Buffer controlled_buffer_67
  assign _5_el_str_4 = _5_t ? {31{1'b0}} : 31'bz;  // Controlled_Buffer controlled_buffer_68
  assign _5_el_str_5 = _5_t ? {31{1'b0}} : 31'bz;  // Controlled_Buffer controlled_buffer_69
  assign _5_el_str_6 = _5_t ? {31{1'b0}} : 31'bz;  // Controlled_Buffer controlled_buffer_70
  assign _5_el_str_7 = _5_t ? {31{1'b0}} : 31'bz;  // Controlled_Buffer controlled_buffer_71
  assign _5_el_str_8 = _5_t ? {31{1'b0}} : 31'bz;  // Controlled_Buffer controlled_buffer_72
  assign _5_el_str_9 = _5_t ? 31'h30000 : 31'bz;  // Controlled_Buffer controlled_buffer_73
  assign _5_el_str_10 = _5_t ? 31'h1f0000 : 31'bz;  // Controlled_Buffer controlled_buffer_74
  assign _5_el_str_11 = _5_t ? 31'h7f0000 : 31'bz;  // Controlled_Buffer controlled_buffer_75
  assign _5_el_str_12 = _5_t ? 31'h7f0000 : 31'bz;  // Controlled_Buffer controlled_buffer_76
  assign _5_el_str_13 = _5_t ? 31'h7f0000 : 31'bz;  // Controlled_Buffer controlled_buffer_77
  assign _5_el_str_14 = _5_t ? 31'h7f0000 : 31'bz;  // Controlled_Buffer controlled_buffer_78
  assign _5_el_str_15 = _5_t ? 31'h7f0000 : 31'bz;  // Controlled_Buffer controlled_buffer_79
  assign _5_el_str_16 = _5_t ? 31'h7f0000 : 31'bz;  // Controlled_Buffer controlled_buffer_80
  assign _5_el_str_17 = _5_t ? 31'h7f0000 : 31'bz;  // Controlled_Buffer controlled_buffer_81
  assign _5_el_str_18 = _5_t ? 31'h1f0000 : 31'bz;  // Controlled_Buffer controlled_buffer_82
  assign _5_el_str_19 = _5_t ? 31'h30000 : 31'bz;  // Controlled_Buffer controlled_buffer_83
  assign _5_el_str_20 = _5_t ? {31{1'b0}} : 31'bz;  // Controlled_Buffer controlled_buffer_84
  assign _5_el_str_21 = _5_t ? {31{1'b0}} : 31'bz;  // Controlled_Buffer controlled_buffer_85
  assign _5_el_str_22 = _5_t ? {31{1'b0}} : 31'bz;  // Controlled_Buffer controlled_buffer_86
  assign _5_el_str_23 = _5_t ? {31{1'b0}} : 31'bz;  // Controlled_Buffer controlled_buffer_87
  assign _5_el_str_24 = _5_t ? {31{1'b0}} : 31'bz;  // Controlled_Buffer controlled_buffer_88
  assign _5_el_str_25 = _5_t ? {31{1'b0}} : 31'bz;  // Controlled_Buffer controlled_buffer_89
  assign _5_el_str_26 = _5_t ? {31{1'b0}} : 31'bz;  // Controlled_Buffer controlled_buffer_90
  assign _5_el_str_27 = _5_t ? {31{1'b0}} : 31'bz;  // Controlled_Buffer controlled_buffer_91
  assign _5_el_str_28 = _5_t ? {31{1'b0}} : 31'bz;  // Controlled_Buffer controlled_buffer_92
  assign _5_el_str_29 = _5_t ? {31{1'b0}} : 31'bz;  // Controlled_Buffer controlled_buffer_93
  assign _5_el_str_30 = _5_t ? {31{1'b0}} : 31'bz;  // Controlled_Buffer controlled_buffer_94
  assign _5_el_str_31 = _5_t ? {31{1'b0}} : 31'bz;  // Controlled_Buffer controlled_buffer_95
  assign _5_el_str_32 = _5_t ? {31{1'b0}} : 31'bz;  // Controlled_Buffer controlled_buffer_96
  assign _8_t = not_1_out ? and_2_out : 1'bz;  // Controlled_Buffer controlled_buffer_97
  assign _7_t = not_1_out ? and_5_out : 1'bz;  // Controlled_Buffer controlled_buffer_98
  and and_5 (and_5_out, ~_8, _5);  // AND_Gate
  assign _6_t = not_1_out ? and_3_out : 1'bz;  // Controlled_Buffer controlled_buffer_99
  assign _5_t = not_1_out ? and_6_out : 1'bz;  // Controlled_Buffer controlled_buffer_100
  and and_6 (and_6_out, _6, ~_8, ~_5);  // AND_Gate
  assign _4_t = not_1_out ? and_7_out : 1'bz;  // Controlled_Buffer controlled_buffer_101
  and and_7 (and_7_out, _4, ~_8, ~_5);  // AND_Gate
  not not_1 (not_1_out, isBattle);
  look_on_minimap look_on_minimap_1 ();
  assign _8_t = isBattle ? 1'b0 : 1'bz;  // Controlled_Buffer controlled_buffer_102
  assign _7_t = isBattle ? 1'b0 : 1'bz;  // Controlled_Buffer controlled_buffer_103
  assign _6_t = isBattle ? 1'b0 : 1'bz;  // Controlled_Buffer controlled_buffer_104
  assign _5_t = isBattle ? 1'b0 : 1'bz;  // Controlled_Buffer controlled_buffer_105
  assign _4_t = isBattle ? 1'b0 : 1'bz;  // Controlled_Buffer controlled_buffer_106
  or_for_str_31_bit or_for_str_31_bit_1 (
    .in_1(_1_el_str_1), .in_2(_7_el_str_1), .in_3(_5_el_str_1), .out_one_str(out_10));  // open: in_4, in_5, in_6, in_7, in_8
  or_for_str_31_bit or_for_str_31_bit_2 (
    .in_1(_1_el_str_2), .in_2(_7_el_str_2), .in_3(_5_el_str_2), .out_one_str(out_11));  // open: in_4, in_5, in_6, in_7, in_8
  or_for_str_31_bit or_for_str_31_bit_3 (
    .in_1(_1_el_str_3), .in_2(_7_el_str_3), .in_3(_5_el_str_3), .out_one_str(out_12));  // open: in_4, in_5, in_6, in_7, in_8
  or_for_str_31_bit or_for_str_31_bit_4 (
    .in_1(_1_el_str_4), .in_2(_7_el_str_4), .in_3(_5_el_str_4), .out_one_str(out_13));  // open: in_4, in_5, in_6, in_7, in_8
  or_for_str_31_bit or_for_str_31_bit_5 (
    .in_1(_1_el_str_5), .in_2(_7_el_str_5), .in_3(_5_el_str_5), .out_one_str(out_14));  // open: in_4, in_5, in_6, in_7, in_8
  or_for_str_31_bit or_for_str_31_bit_6 (
    .in_1(_1_el_str_6), .in_2(_7_el_str_6), .in_3(_5_el_str_6), .out_one_str(out_15));  // open: in_4, in_5, in_6, in_7, in_8
  or_for_str_31_bit or_for_str_31_bit_7 (
    .in_1(_1_el_str_7), .in_2(_7_el_str_7), .in_3(_5_el_str_7), .out_one_str(out_16));  // open: in_4, in_5, in_6, in_7, in_8
  or_for_str_31_bit or_for_str_31_bit_8 (
    .in_1(_1_el_str_8), .in_2(_7_el_str_8), .in_3(_5_el_str_8), .out_one_str(out_17));  // open: in_4, in_5, in_6, in_7, in_8
  or_for_str_31_bit or_for_str_31_bit_9 (
    .in_1(_1_el_str_9), .in_2(_7_el_str_9), .in_3(_5_el_str_9), .out_one_str(out_18));  // open: in_4, in_5, in_6, in_7, in_8
  or_for_str_31_bit or_for_str_31_bit_10 (
    .in_1(_1_el_str_10), .in_2(_7_el_str_10), .in_3(_5_el_str_10), .out_one_str(out_19));  // open: in_4, in_5, in_6, in_7, in_8
  or_for_str_31_bit or_for_str_31_bit_11 (
    .in_1(_1_el_str_11), .in_2(_7_el_str_11), .in_3(_5_el_str_11), .out_one_str(out_20));  // open: in_4, in_5, in_6, in_7, in_8
  or_for_str_31_bit or_for_str_31_bit_12 (
    .in_1(_1_el_str_12), .in_2(_7_el_str_12), .in_3(_5_el_str_12), .out_one_str(out_21));  // open: in_4, in_5, in_6, in_7, in_8
  or_for_str_31_bit or_for_str_31_bit_13 (
    .in_1(_1_el_str_13), .in_2(_7_el_str_13), .in_3(_5_el_str_13), .out_one_str(out_22));  // open: in_4, in_5, in_6, in_7, in_8
  or_for_str_31_bit or_for_str_31_bit_14 (
    .in_1(_1_el_str_14), .in_2(_7_el_str_14), .in_3(_5_el_str_14), .out_one_str(out_23));  // open: in_4, in_5, in_6, in_7, in_8
  or_for_str_31_bit or_for_str_31_bit_15 (
    .in_1(_1_el_str_15), .in_2(_7_el_str_15), .in_3(_5_el_str_15), .out_one_str(out_24));  // open: in_4, in_5, in_6, in_7, in_8
  or_for_str_31_bit or_for_str_31_bit_16 (
    .in_1(_1_el_str_16), .in_2(_7_el_str_16), .in_3(_5_el_str_16), .out_one_str(out_25));  // open: in_4, in_5, in_6, in_7, in_8
  or_for_str_31_bit or_for_str_31_bit_17 (
    .in_1(_1_el_str_17), .in_2(_7_el_str_17), .in_3(_5_el_str_17), .out_one_str(out_26));  // open: in_4, in_5, in_6, in_7, in_8
  or_for_str_31_bit or_for_str_31_bit_18 (
    .in_1(_1_el_str_18), .in_2(_7_el_str_18), .in_3(_5_el_str_18), .out_one_str(out_27));  // open: in_4, in_5, in_6, in_7, in_8
  or_for_str_31_bit or_for_str_31_bit_19 (
    .in_1(_1_el_str_19), .in_2(_7_el_str_19), .in_3(_5_el_str_19), .out_one_str(out_28));  // open: in_4, in_5, in_6, in_7, in_8
  or_for_str_31_bit or_for_str_31_bit_20 (
    .in_1(_1_el_str_20), .in_2(_7_el_str_20), .in_3(_5_el_str_20), .out_one_str(out_29));  // open: in_4, in_5, in_6, in_7, in_8
  or_for_str_31_bit or_for_str_31_bit_21 (
    .in_1(_1_el_str_21), .in_2(_7_el_str_21), .in_3(_5_el_str_21), .out_one_str(out_30));  // open: in_4, in_5, in_6, in_7, in_8
  or_for_str_31_bit or_for_str_31_bit_22 (
    .in_1(_1_el_str_22), .in_2(_7_el_str_22), .in_3(_5_el_str_22), .out_one_str(out_31));  // open: in_4, in_5, in_6, in_7, in_8
  or_for_str_31_bit or_for_str_31_bit_23 (
    .in_1(_1_el_str_23), .in_2(_7_el_str_23), .in_3(_5_el_str_23), .out_one_str(out_32));  // open: in_4, in_5, in_6, in_7, in_8
  or_for_str_31_bit or_for_str_31_bit_24 (
    .in_1(_1_el_str_24), .in_2(_7_el_str_24), .in_3(_5_el_str_24), .out_one_str(out_33));  // open: in_4, in_5, in_6, in_7, in_8
  or_for_str_31_bit or_for_str_31_bit_25 (
    .in_1(_1_el_str_25), .in_2(_7_el_str_25), .in_3(_5_el_str_25), .out_one_str(out_34));  // open: in_4, in_5, in_6, in_7, in_8
  or_for_str_31_bit or_for_str_31_bit_26 (
    .in_1(_1_el_str_26), .in_2(_7_el_str_26), .in_3(_5_el_str_26), .out_one_str(out_35));  // open: in_4, in_5, in_6, in_7, in_8
  or_for_str_31_bit or_for_str_31_bit_27 (
    .in_1(_1_el_str_27), .in_2(_7_el_str_27), .in_3(_5_el_str_27), .out_one_str(out_36));  // open: in_4, in_5, in_6, in_7, in_8
  or_for_str_31_bit or_for_str_31_bit_28 (
    .in_1(_1_el_str_28), .in_2(_7_el_str_28), .in_3(_5_el_str_28), .out_one_str(out_37));  // open: in_4, in_5, in_6, in_7, in_8
  or_for_str_31_bit or_for_str_31_bit_29 (
    .in_1(_1_el_str_29), .in_2(_7_el_str_29), .in_3(_5_el_str_29), .out_one_str(out_38));  // open: in_4, in_5, in_6, in_7, in_8
  or_for_str_31_bit or_for_str_31_bit_30 (
    .in_1(_1_el_str_30), .in_2(_7_el_str_30), .in_3(_5_el_str_30), .out_one_str(out_39));  // open: in_4, in_5, in_6, in_7, in_8
  or_for_str_31_bit or_for_str_31_bit_31 (
    .in_1(_1_el_str_31), .in_2(_7_el_str_31), .in_3(_5_el_str_31), .out_one_str(out_40));  // open: in_4, in_5, in_6, in_7, in_8
  or_for_str_31_bit or_for_str_31_bit_32 (
    .in_1(_1_el_str_32), .in_2(_7_el_str_32), .in_3(_5_el_str_32), .out_one_str(out_41));  // open: in_4, in_5, in_6, in_7, in_8
  look_on_minimap look_on_minimap_2 ();

  // Other names for the same wires on the sheet: str_1[30:0] = out_10; str_2[30:0] = out_11; str_3[30:0] = out_12;
  //   str_4[30:0] = out_13; str_5[30:0] = out_14; str_6[30:0] = out_15; str_7[30:0] = out_16; str_8[30:0] = out_17;
  //   str_9[30:0] = out_18; str_10[30:0] = out_19; str_11[30:0] = out_20; str_12[30:0] = out_21;
  //   str_13[30:0] = out_22; str_14[30:0] = out_23; str_15[30:0] = out_24; str_16[30:0] = out_25;
  //   str_17[30:0] = out_26; str_18[30:0] = out_27; str_19[30:0] = out_28; str_20[30:0] = out_29;
  //   str_21[30:0] = out_30; str_22[30:0] = out_31; str_23[30:0] = out_32; str_24[30:0] = out_33;
  //   str_25[30:0] = out_34; str_26[30:0] = out_35; str_27[30:0] = out_36; str_28[30:0] = out_37;
  //   str_29[30:0] = out_38; str_30[30:0] = out_39; str_31[30:0] = out_40; str_32[30:0] = out_41

  // Notes on the sheet:
  //   8 -> 1
endmodule

module Tile_r_4_color (
  input  _8,
  input  _6,
  input  _5,
  input  _4,
  input  _3,
  input  _2,
  input  _1,
  input  [1:0] enemy,
  input  [1:0] gameState,
  output [31:0] out_10,
  output [31:0] out_11,
  output [31:0] out_12,
  output [31:0] out_13,
  output [31:0] out_14,
  output [31:0] out_15,
  output [31:0] out_16,
  output [31:0] out_17,
  output [31:0] out_18,
  output [31:0] out_19,
  output [31:0] out_20,
  output [31:0] out_21,
  output [31:0] out_22,
  output [31:0] out_23,
  output [31:0] out_24,
  output [31:0] out_25,
  output [31:0] out_26,
  output [31:0] out_27,
  output [31:0] out_28,
  output [31:0] out_29,
  output [31:0] out_30,
  output [31:0] out_31,
  output [31:0] out_32,
  output [31:0] out_33,
  output [31:0] out_34,
  output [31:0] out_35,
  output [31:0] out_36,
  output [31:0] out_37,
  output [31:0] out_38,
  output [31:0] out_39,
  output [31:0] out_40,
  output [31:0] out_41
);

  wire _1_t, _2_t, _3_t, and_1_out, and_2_out, and_3_out, and_4_out, and_5_out, and_6_out, ferret, isBattle,
       isbattle_whichenemy_1_ferret, isbattle_whichenemy_1_mouse, isbattle_whichenemy_1_rat,
       isbattle_whichenemy_1_snake, not_1_out, or_1_out, rat_mouse, snake;
  wire [31:0] _1_el_str_1, _1_el_str_2, _1_el_str_3, _1_el_str_4, _1_el_str_5, _1_el_str_6, _1_el_str_7,
       _1_el_str_8, _1_el_str_9, _1_el_str_10, _1_el_str_11, _1_el_str_12, _1_el_str_13, _1_el_str_14,
       _1_el_str_15, _1_el_str_16, _1_el_str_17, _1_el_str_18, _1_el_str_19, _1_el_str_20, _1_el_str_21,
       _1_el_str_22, _1_el_str_23, _1_el_str_24, _1_el_str_25, _1_el_str_26, _1_el_str_27, _1_el_str_28,
       _1_el_str_29, _1_el_str_30, _1_el_str_31, _1_el_str_32, _7_el_str_1, _7_el_str_2, _7_el_str_3,
       _7_el_str_4, _7_el_str_5, _7_el_str_6, _7_el_str_7, _7_el_str_8, _7_el_str_9, _7_el_str_10,
       _7_el_str_11, _7_el_str_12, _7_el_str_13, _7_el_str_14, _7_el_str_15, _7_el_str_16, _7_el_str_17,
       _7_el_str_18, _7_el_str_19, _7_el_str_20, _7_el_str_21, _7_el_str_22, _7_el_str_23, _7_el_str_24,
       _7_el_str_25, _7_el_str_26, _7_el_str_27, _7_el_str_28, _7_el_str_29, _7_el_str_30, _7_el_str_31,
       _7_el_str_32, controlled_buffer_138_out, controlled_buffer_139_out, controlled_buffer_140_out,
       controlled_buffer_141_out, controlled_buffer_142_out, controlled_buffer_143_out,
       controlled_buffer_144_out, controlled_buffer_145_out, controlled_buffer_146_out,
       controlled_buffer_147_out, controlled_buffer_148_out, controlled_buffer_149_out,
       controlled_buffer_150_out, controlled_buffer_151_out, controlled_buffer_152_out,
       controlled_buffer_153_out, controlled_buffer_154_out, controlled_buffer_155_out,
       controlled_buffer_156_out, controlled_buffer_157_out, controlled_buffer_158_out,
       controlled_buffer_159_out, controlled_buffer_160_out, controlled_buffer_161_out,
       controlled_buffer_162_out, controlled_buffer_163_out, controlled_buffer_164_out,
       controlled_buffer_165_out, controlled_buffer_166_out, controlled_buffer_167_out,
       controlled_buffer_168_out, controlled_buffer_169_out, ferret_str_1, ferret_str_2, ferret_str_3,
       ferret_str_4, ferret_str_5, ferret_str_6, ferret_str_7, ferret_str_8, ferret_str_9, ferret_str_10,
       ferret_str_11, ferret_str_12, ferret_str_13, ferret_str_14, ferret_str_15, ferret_str_16,
       ferret_str_17, ferret_str_18, ferret_str_19, ferret_str_20, ferret_str_21, ferret_str_22,
       ferret_str_23, ferret_str_24, ferret_str_25, ferret_str_26, ferret_str_27, ferret_str_28,
       ferret_str_29, ferret_str_30, ferret_str_31, ferret_str_32, mouse_rat_str_1, mouse_rat_str_2,
       mouse_rat_str_3, mouse_rat_str_4, mouse_rat_str_5, mouse_rat_str_6, mouse_rat_str_7, mouse_rat_str_8,
       mouse_rat_str_9, mouse_rat_str_10, mouse_rat_str_11, mouse_rat_str_12, mouse_rat_str_13,
       mouse_rat_str_14, mouse_rat_str_15, mouse_rat_str_16, mouse_rat_str_17, mouse_rat_str_18,
       mouse_rat_str_19, mouse_rat_str_20, mouse_rat_str_21, mouse_rat_str_22, mouse_rat_str_23,
       mouse_rat_str_24, mouse_rat_str_25, mouse_rat_str_26, mouse_rat_str_27, mouse_rat_str_28,
       mouse_rat_str_29, mouse_rat_str_30, mouse_rat_str_31, mouse_rat_str_32, snake_str_1, snake_str_2,
       snake_str_3, snake_str_4, snake_str_5, snake_str_6, snake_str_7, snake_str_8, snake_str_9,
       snake_str_10, snake_str_11, snake_str_12, snake_str_13, snake_str_14, snake_str_15, snake_str_16,
       snake_str_17, snake_str_18, snake_str_19, snake_str_20, snake_str_21, snake_str_22, snake_str_23,
       snake_str_24, snake_str_25, snake_str_26, snake_str_27, snake_str_28, snake_str_29, snake_str_30,
       snake_str_31, snake_str_32;

  and and_1 (and_1_out, ~_8, ~_5, _3, ~_6);  // AND_Gate
  and and_2 (and_2_out, ~_8, ~_5, _2);  // AND_Gate
  and and_3 (and_3_out, ~_8, ~_5, _1, ~_4);  // AND_Gate
  isBattle_whichenemy isbattle_whichenemy_1 (
    .curr_enemy(enemy), .GameState(gameState), .rat(isbattle_whichenemy_1_rat),
    .mouse(isbattle_whichenemy_1_mouse), .ferret(isbattle_whichenemy_1_ferret),
    .snake(isbattle_whichenemy_1_snake), .isBattle(isBattle));
  assign _1_el_str_1 = _2_t ? {32{1'b0}} : 32'bz;  // Controlled_Buffer controlled_buffer_1
  assign _1_el_str_2 = _2_t ? {32{1'b0}} : 32'bz;  // Controlled_Buffer controlled_buffer_2
  assign _1_el_str_3 = _2_t ? {32{1'b0}} : 32'bz;  // Controlled_Buffer controlled_buffer_3
  assign _1_el_str_4 = _2_t ? {32{1'b0}} : 32'bz;  // Controlled_Buffer controlled_buffer_4
  assign _1_el_str_5 = _2_t ? {32{1'b0}} : 32'bz;  // Controlled_Buffer controlled_buffer_5
  assign _1_el_str_6 = _2_t ? {32{1'b0}} : 32'bz;  // Controlled_Buffer controlled_buffer_6
  assign _1_el_str_7 = _2_t ? {32{1'b0}} : 32'bz;  // Controlled_Buffer controlled_buffer_7
  assign _1_el_str_8 = _2_t ? {32{1'b0}} : 32'bz;  // Controlled_Buffer controlled_buffer_8
  assign _1_el_str_9 = _2_t ? {32{1'b0}} : 32'bz;  // Controlled_Buffer controlled_buffer_9
  assign _1_el_str_10 = _2_t ? {32{1'b0}} : 32'bz;  // Controlled_Buffer controlled_buffer_10
  assign _1_el_str_11 = _2_t ? 32'h1f800000 : 32'bz;  // Controlled_Buffer controlled_buffer_11
  assign _1_el_str_12 = _2_t ? 32'h1f800000 : 32'bz;  // Controlled_Buffer controlled_buffer_12
  assign _1_el_str_13 = _2_t ? 32'h1f800000 : 32'bz;  // Controlled_Buffer controlled_buffer_13
  assign _1_el_str_14 = _2_t ? 32'h1f800000 : 32'bz;  // Controlled_Buffer controlled_buffer_14
  assign _1_el_str_15 = _2_t ? 32'h1f800000 : 32'bz;  // Controlled_Buffer controlled_buffer_15
  assign _1_el_str_16 = _2_t ? 32'h1f800000 : 32'bz;  // Controlled_Buffer controlled_buffer_16
  assign _1_el_str_17 = _2_t ? 32'h1f800000 : 32'bz;  // Controlled_Buffer controlled_buffer_17
  assign _1_el_str_18 = _2_t ? {32{1'b0}} : 32'bz;  // Controlled_Buffer controlled_buffer_18
  assign _1_el_str_19 = _2_t ? {32{1'b0}} : 32'bz;  // Controlled_Buffer controlled_buffer_19
  assign _1_el_str_20 = _2_t ? {32{1'b0}} : 32'bz;  // Controlled_Buffer controlled_buffer_20
  assign _1_el_str_21 = _2_t ? {32{1'b0}} : 32'bz;  // Controlled_Buffer controlled_buffer_21
  assign _1_el_str_22 = _2_t ? {32{1'b0}} : 32'bz;  // Controlled_Buffer controlled_buffer_22
  assign _1_el_str_23 = _2_t ? {32{1'b0}} : 32'bz;  // Controlled_Buffer controlled_buffer_23
  assign _1_el_str_24 = _2_t ? {32{1'b0}} : 32'bz;  // Controlled_Buffer controlled_buffer_24
  assign _1_el_str_25 = _2_t ? {32{1'b0}} : 32'bz;  // Controlled_Buffer controlled_buffer_25
  assign _1_el_str_26 = _2_t ? {32{1'b0}} : 32'bz;  // Controlled_Buffer controlled_buffer_26
  assign _1_el_str_27 = _2_t ? {32{1'b0}} : 32'bz;  // Controlled_Buffer controlled_buffer_27
  assign _1_el_str_28 = _2_t ? {32{1'b0}} : 32'bz;  // Controlled_Buffer controlled_buffer_28
  assign _1_el_str_29 = _2_t ? {32{1'b0}} : 32'bz;  // Controlled_Buffer controlled_buffer_29
  assign _1_el_str_30 = _2_t ? {32{1'b0}} : 32'bz;  // Controlled_Buffer controlled_buffer_30
  assign _1_el_str_31 = _2_t ? {32{1'b0}} : 32'bz;  // Controlled_Buffer controlled_buffer_31
  assign _1_el_str_32 = _2_t ? {32{1'b0}} : 32'bz;  // Controlled_Buffer controlled_buffer_32
  assign _7_el_str_1 = _3_t ? {32{1'b0}} : 32'bz;  // Controlled_Buffer controlled_buffer_33
  assign _7_el_str_2 = _3_t ? {32{1'b0}} : 32'bz;  // Controlled_Buffer controlled_buffer_34
  assign _7_el_str_3 = _3_t ? {32{1'b0}} : 32'bz;  // Controlled_Buffer controlled_buffer_35
  assign _7_el_str_4 = _3_t ? {32{1'b0}} : 32'bz;  // Controlled_Buffer controlled_buffer_36
  assign _7_el_str_5 = _3_t ? {32{1'b0}} : 32'bz;  // Controlled_Buffer controlled_buffer_37
  assign _7_el_str_6 = _3_t ? {32{1'b0}} : 32'bz;  // Controlled_Buffer controlled_buffer_38
  assign _7_el_str_7 = _3_t ? {32{1'b0}} : 32'bz;  // Controlled_Buffer controlled_buffer_39
  assign _7_el_str_8 = _3_t ? {32{1'b0}} : 32'bz;  // Controlled_Buffer controlled_buffer_40
  assign _7_el_str_9 = _3_t ? {32{1'b0}} : 32'bz;  // Controlled_Buffer controlled_buffer_41
  assign _7_el_str_10 = _3_t ? {32{1'b0}} : 32'bz;  // Controlled_Buffer controlled_buffer_42
  assign _7_el_str_11 = _3_t ? 32'h7f0000 : 32'bz;  // Controlled_Buffer controlled_buffer_43
  assign _7_el_str_12 = _3_t ? 32'h7f0000 : 32'bz;  // Controlled_Buffer controlled_buffer_44
  assign _7_el_str_13 = _3_t ? 32'h7f0000 : 32'bz;  // Controlled_Buffer controlled_buffer_45
  assign _7_el_str_14 = _3_t ? 32'h7f0000 : 32'bz;  // Controlled_Buffer controlled_buffer_46
  assign _7_el_str_15 = _3_t ? 32'h7f0000 : 32'bz;  // Controlled_Buffer controlled_buffer_47
  assign _7_el_str_16 = _3_t ? 32'h7f0000 : 32'bz;  // Controlled_Buffer controlled_buffer_48
  assign _7_el_str_17 = _3_t ? 32'h7f0000 : 32'bz;  // Controlled_Buffer controlled_buffer_49
  assign _7_el_str_18 = _3_t ? {32{1'b0}} : 32'bz;  // Controlled_Buffer controlled_buffer_50
  assign _7_el_str_19 = _3_t ? {32{1'b0}} : 32'bz;  // Controlled_Buffer controlled_buffer_51
  assign _7_el_str_20 = _3_t ? {32{1'b0}} : 32'bz;  // Controlled_Buffer controlled_buffer_52
  assign _7_el_str_21 = _3_t ? {32{1'b0}} : 32'bz;  // Controlled_Buffer controlled_buffer_53
  assign _7_el_str_22 = _3_t ? {32{1'b0}} : 32'bz;  // Controlled_Buffer controlled_buffer_54
  assign _7_el_str_23 = _3_t ? {32{1'b0}} : 32'bz;  // Controlled_Buffer controlled_buffer_55
  assign _7_el_str_24 = _3_t ? {32{1'b0}} : 32'bz;  // Controlled_Buffer controlled_buffer_56
  assign _7_el_str_25 = _3_t ? {32{1'b0}} : 32'bz;  // Controlled_Buffer controlled_buffer_57
  assign _7_el_str_26 = _3_t ? {32{1'b0}} : 32'bz;  // Controlled_Buffer controlled_buffer_58
  assign _7_el_str_27 = _3_t ? {32{1'b0}} : 32'bz;  // Controlled_Buffer controlled_buffer_59
  assign _7_el_str_28 = _3_t ? {32{1'b0}} : 32'bz;  // Controlled_Buffer controlled_buffer_60
  assign _7_el_str_29 = _3_t ? {32{1'b0}} : 32'bz;  // Controlled_Buffer controlled_buffer_61
  assign _7_el_str_30 = _3_t ? {32{1'b0}} : 32'bz;  // Controlled_Buffer controlled_buffer_62
  assign _7_el_str_31 = _3_t ? {32{1'b0}} : 32'bz;  // Controlled_Buffer controlled_buffer_63
  assign _7_el_str_32 = _3_t ? {32{1'b0}} : 32'bz;  // Controlled_Buffer controlled_buffer_64
  assign _3_t = not_1_out ? and_1_out : 1'bz;  // Controlled_Buffer controlled_buffer_65
  assign _3_t = isBattle ? 1'b0 : 1'bz;  // Controlled_Buffer controlled_buffer_66
  assign _2_t = not_1_out ? and_2_out : 1'bz;  // Controlled_Buffer controlled_buffer_67
  assign _2_t = isBattle ? 1'b0 : 1'bz;  // Controlled_Buffer controlled_buffer_68
  assign _1_t = not_1_out ? and_3_out : 1'bz;  // Controlled_Buffer controlled_buffer_69
  assign _1_t = isBattle ? 1'b0 : 1'bz;  // Controlled_Buffer controlled_buffer_70
  not not_1 (not_1_out, isBattle);
  or or_1 (or_1_out, isbattle_whichenemy_1_rat, isbattle_whichenemy_1_mouse);
  and and_4 (and_4_out, or_1_out, isBattle);
  and and_5 (and_5_out, isbattle_whichenemy_1_ferret, isBattle);
  and and_6 (and_6_out, isbattle_whichenemy_1_snake, isBattle);
  Pull_Resistor pull_resistor_1 (.node(rat_mouse));
  assign rat_mouse = and_4_out ? 1'b1 : 1'bz;  // Controlled_Buffer controlled_buffer_71
  assign ferret = and_5_out ? 1'b1 : 1'bz;  // Controlled_Buffer controlled_buffer_72
  Pull_Resistor pull_resistor_2 (.node(ferret));
  assign snake = and_6_out ? 1'b1 : 1'bz;  // Controlled_Buffer controlled_buffer_73
  assign ferret_str_1 = ferret ? 32'h9000 : 32'bz;  // Controlled_Buffer controlled_buffer_74
  assign ferret_str_2 = ferret ? 32'h1ffe00 : 32'bz;  // Controlled_Buffer controlled_buffer_75
  assign ferret_str_3 = ferret ? 32'h7fff80 : 32'bz;  // Controlled_Buffer controlled_buffer_76
  assign ferret_str_4 = ferret ? 32'hce07e0 : 32'bz;  // Controlled_Buffer controlled_buffer_77
  assign ferret_str_5 = ferret ? 32'h9c335c : 32'bz;  // Controlled_Buffer controlled_buffer_78
  assign ferret_str_6 = ferret ? 32'h84b882 : 32'bz;  // Controlled_Buffer controlled_buffer_79
  assign ferret_str_7 = ferret ? 32'h18e6c17 : 32'bz;  // Controlled_Buffer controlled_buffer_80
  assign ferret_str_8 = ferret ? 32'h144fe0f : 32'bz;  // Controlled_Buffer controlled_buffer_81
  assign ferret_str_9 = ferret ? 32'h36cfc05 : 32'bz;  // Controlled_Buffer controlled_buffer_82
  assign ferret_str_10 = ferret ? 32'h238780d : 32'bz;  // Controlled_Buffer controlled_buffer_83
  assign ferret_str_11 = ferret ? 32'h2003816 : 32'bz;  // Controlled_Buffer controlled_buffer_84
  assign ferret_str_12 = ferret ? 32'h2041c72 : 32'bz;  // Controlled_Buffer controlled_buffer_85
  assign ferret_str_13 = ferret ? 32'h20c00c4 : 32'bz;  // Controlled_Buffer controlled_buffer_86
  assign ferret_str_14 = ferret ? 32'h67e0018 : 32'bz;  // Controlled_Buffer controlled_buffer_87
  assign ferret_str_15 = ferret ? 32'h47f0070 : 32'bz;  // Controlled_Buffer controlled_buffer_88
  assign ferret_str_16 = ferret ? 32'h47ffbe0 : 32'bz;  // Controlled_Buffer controlled_buffer_89
  assign ferret_str_17 = ferret ? 32'h47fffc0 : 32'bz;  // Controlled_Buffer controlled_buffer_90
  assign ferret_str_18 = ferret ? 32'h4bfff80 : 32'bz;  // Controlled_Buffer controlled_buffer_91
  assign ferret_str_19 = ferret ? 32'h41fff80 : 32'bz;  // Controlled_Buffer controlled_buffer_92
  assign ferret_str_20 = ferret ? 32'hf87fff00 : 32'bz;  // Controlled_Buffer controlled_buffer_93
  assign ferret_str_21 = ferret ? 32'hf8ffff00 : 32'bz;  // Controlled_Buffer controlled_buffer_94
  assign ferret_str_22 = ferret ? 32'hfafffe00 : 32'bz;  // Controlled_Buffer controlled_buffer_95
  assign ferret_str_23 = ferret ? 32'hfdfffe00 : 32'bz;  // Controlled_Buffer controlled_buffer_96
  assign ferret_str_24 = ferret ? 32'hfb7ffe00 : 32'bz;  // Controlled_Buffer controlled_buffer_97
  assign ferret_str_25 = ferret ? 32'hf87ffe00 : 32'bz;  // Controlled_Buffer controlled_buffer_98
  assign ferret_str_26 = ferret ? 32'hfffc00 : 32'bz;  // Controlled_Buffer controlled_buffer_99
  assign ferret_str_27 = ferret ? 32'h1fffc00 : 32'bz;  // Controlled_Buffer controlled_buffer_100
  assign ferret_str_28 = ferret ? 32'h3fffc00 : 32'bz;  // Controlled_Buffer controlled_buffer_101
  assign ferret_str_29 = ferret ? 32'h7fff800 : 32'bz;  // Controlled_Buffer controlled_buffer_102
  assign ferret_str_30 = ferret ? 32'h7fff800 : 32'bz;  // Controlled_Buffer controlled_buffer_103
  assign ferret_str_31 = ferret ? {32{1'b0}} : 32'bz;  // Controlled_Buffer controlled_buffer_104
  assign ferret_str_32 = ferret ? {32{1'b0}} : 32'bz;  // Controlled_Buffer controlled_buffer_105
  Pull_Resistor pull_resistor_3 (.node(snake));
  assign mouse_rat_str_1 = rat_mouse ? 32'h380 : 32'bz;  // Controlled_Buffer controlled_buffer_106
  assign mouse_rat_str_2 = rat_mouse ? 32'h27f : 32'bz;  // Controlled_Buffer controlled_buffer_107
  assign mouse_rat_str_3 = rat_mouse ? 32'h16e : 32'bz;  // Controlled_Buffer controlled_buffer_108
  assign mouse_rat_str_4 = rat_mouse ? 32'h7fc : 32'bz;  // Controlled_Buffer controlled_buffer_109
  assign mouse_rat_str_5 = rat_mouse ? 32'h1ff0 : 32'bz;  // Controlled_Buffer controlled_buffer_110
  assign mouse_rat_str_6 = rat_mouse ? 32'h7fc0 : 32'bz;  // Controlled_Buffer controlled_buffer_111
  assign mouse_rat_str_7 = rat_mouse ? 32'hff80 : 32'bz;  // Controlled_Buffer controlled_buffer_112
  assign mouse_rat_str_8 = rat_mouse ? 32'h1ffc0 : 32'bz;  // Controlled_Buffer controlled_buffer_113
  assign mouse_rat_str_9 = rat_mouse ? 32'h1ffe0 : 32'bz;  // Controlled_Buffer controlled_buffer_114
  assign mouse_rat_str_10 = rat_mouse ? 32'h3fe20 : 32'bz;  // Controlled_Buffer controlled_buffer_115
  assign mouse_rat_str_11 = rat_mouse ? 32'h7fc00 : 32'bz;  // Controlled_Buffer controlled_buffer_116
  assign mouse_rat_str_12 = rat_mouse ? 32'h7fc00 : 32'bz;  // Controlled_Buffer controlled_buffer_117
  assign mouse_rat_str_13 = rat_mouse ? 32'h7fc00 : 32'bz;  // Controlled_Buffer controlled_buffer_118
  assign mouse_rat_str_14 = rat_mouse ? 32'hffe00 : 32'bz;  // Controlled_Buffer controlled_buffer_119
  assign mouse_rat_str_15 = rat_mouse ? 32'hfff00 : 32'bz;  // Controlled_Buffer controlled_buffer_120
  assign mouse_rat_str_16 = rat_mouse ? 32'hfff00 : 32'bz;  // Controlled_Buffer controlled_buffer_121
  assign mouse_rat_str_17 = rat_mouse ? 32'hfff00 : 32'bz;  // Controlled_Buffer controlled_buffer_122
  assign mouse_rat_str_18 = rat_mouse ? 32'hfff00 : 32'bz;  // Controlled_Buffer controlled_buffer_123
  assign mouse_rat_str_19 = rat_mouse ? 32'hfff00 : 32'bz;  // Controlled_Buffer controlled_buffer_124
  assign mouse_rat_str_20 = rat_mouse ? 32'hfff00 : 32'bz;  // Controlled_Buffer controlled_buffer_125
  assign mouse_rat_str_21 = rat_mouse ? 32'hfff00 : 32'bz;  // Controlled_Buffer controlled_buffer_126
  assign mouse_rat_str_22 = rat_mouse ? 32'h7fe00 : 32'bz;  // Controlled_Buffer controlled_buffer_127
  assign mouse_rat_str_23 = rat_mouse ? 32'h7ff800 : 32'bz;  // Controlled_Buffer controlled_buffer_128
  assign mouse_rat_str_24 = rat_mouse ? 32'hcfff00 : 32'bz;  // Controlled_Buffer controlled_buffer_129
  assign mouse_rat_str_25 = rat_mouse ? 32'h87ff80 : 32'bz;  // Controlled_Buffer controlled_buffer_130
  assign mouse_rat_str_26 = rat_mouse ? 32'h800000 : 32'bz;  // Controlled_Buffer controlled_buffer_131
  assign mouse_rat_str_27 = rat_mouse ? 32'hff0000 : 32'bz;  // Controlled_Buffer controlled_buffer_132
  assign mouse_rat_str_28 = rat_mouse ? 32'hfff0 : 32'bz;  // Controlled_Buffer controlled_buffer_133
  assign mouse_rat_str_29 = rat_mouse ? {32{1'b0}} : 32'bz;  // Controlled_Buffer controlled_buffer_134
  assign mouse_rat_str_30 = rat_mouse ? {32{1'b0}} : 32'bz;  // Controlled_Buffer controlled_buffer_135
  assign mouse_rat_str_31 = rat_mouse ? {32{1'b0}} : 32'bz;  // Controlled_Buffer controlled_buffer_136
  assign mouse_rat_str_32 = rat_mouse ? {32{1'b0}} : 32'bz;  // Controlled_Buffer controlled_buffer_137
  assign controlled_buffer_138_out = snake ? 32'hc180 : 32'bz;  // Controlled_Buffer controlled_buffer_138
  assign controlled_buffer_139_out = snake ? 32'h1c300 : 32'bz;  // Controlled_Buffer controlled_buffer_139
  assign controlled_buffer_140_out = snake ? 32'h1ce00 : 32'bz;  // Controlled_Buffer controlled_buffer_140
  assign controlled_buffer_141_out = snake ? 32'h39e00 : 32'bz;  // Controlled_Buffer controlled_buffer_141
  assign controlled_buffer_142_out = snake ? 32'h67c00 : 32'bz;  // Controlled_Buffer controlled_buffer_142
  assign controlled_buffer_143_out = snake ? 32'h5f800 : 32'bz;  // Controlled_Buffer controlled_buffer_143
  assign controlled_buffer_144_out = snake ? 32'hbf000 : 32'bz;  // Controlled_Buffer controlled_buffer_144
  assign controlled_buffer_145_out = snake ? 32'h7e000 : 32'bz;  // Controlled_Buffer controlled_buffer_145
  assign controlled_buffer_146_out = snake ? 32'hfc000 : 32'bz;  // Controlled_Buffer controlled_buffer_146
  assign controlled_buffer_147_out = snake ? 32'h1fc000 : 32'bz;  // Controlled_Buffer controlled_buffer_147
  assign controlled_buffer_148_out = snake ? 32'h7f8000 : 32'bz;  // Controlled_Buffer controlled_buffer_148
  assign controlled_buffer_149_out = snake ? 32'hfff800 : 32'bz;  // Controlled_Buffer controlled_buffer_149
  assign controlled_buffer_150_out = snake ? 32'hfffe00 : 32'bz;  // Controlled_Buffer controlled_buffer_150
  assign controlled_buffer_151_out = snake ? 32'h1efff00 : 32'bz;  // Controlled_Buffer controlled_buffer_151
  assign controlled_buffer_152_out = snake ? 32'h1cfcf80 : 32'bz;  // Controlled_Buffer controlled_buffer_152
  assign controlled_buffer_153_out = snake ? 32'h1dff7c0 : 32'bz;  // Controlled_Buffer controlled_buffer_153
  assign controlled_buffer_154_out = snake ? 32'h3fdfbc0 : 32'bz;  // Controlled_Buffer controlled_buffer_154
  assign controlled_buffer_155_out = snake ? 32'h7f8fde0 : 32'bz;  // Controlled_Buffer controlled_buffer_155
  assign controlled_buffer_156_out = snake ? 32'hffe8dde0 : 32'bz;  // Controlled_Buffer controlled_buffer_156
  assign controlled_buffer_157_out = snake ? 32'hffa1dee0 : 32'bz;  // Controlled_Buffer controlled_buffer_157
  assign controlled_buffer_158_out = snake ? 32'hfd818ce0 : 32'bz;  // Controlled_Buffer controlled_buffer_158
  assign controlled_buffer_159_out = snake ? 32'hfd8392e0 : 32'bz;  // Controlled_Buffer controlled_buffer_159
  assign controlled_buffer_160_out = snake ? 32'h48b1ee0 : 32'bz;  // Controlled_Buffer controlled_buffer_160
  assign controlled_buffer_161_out = snake ? 32'h2e1ee0 : 32'bz;  // Controlled_Buffer controlled_buffer_161
  assign controlled_buffer_162_out = snake ? 32'h3c1de0 : 32'bz;  // Controlled_Buffer controlled_buffer_162
  assign controlled_buffer_163_out = snake ? 32'h1821e0 : 32'bz;  // Controlled_Buffer controlled_buffer_163
  assign controlled_buffer_164_out = snake ? 32'h7bc0 : 32'bz;  // Controlled_Buffer controlled_buffer_164
  assign controlled_buffer_165_out = snake ? 32'hf7c0 : 32'bz;  // Controlled_Buffer controlled_buffer_165
  assign controlled_buffer_166_out = snake ? 32'h1f780 : 32'bz;  // Controlled_Buffer controlled_buffer_166
  assign controlled_buffer_167_out = snake ? 32'h3ef80 : 32'bz;  // Controlled_Buffer controlled_buffer_167
  assign controlled_buffer_168_out = snake ? {32{1'b0}} : 32'bz;  // Controlled_Buffer controlled_buffer_168
  assign controlled_buffer_169_out = snake ? {32{1'b0}} : 32'bz;  // Controlled_Buffer controlled_buffer_169
  Shifter #(.width(32), .shift("lr")) shifter_1 (.in(controlled_buffer_138_out), .\dist (5'b00100), .out(snake_str_1));
  Shifter #(.width(32), .shift("lr")) shifter_2 (.in(controlled_buffer_139_out), .\dist (5'b00100), .out(snake_str_2));
  Shifter #(.width(32), .shift("lr")) shifter_3 (.in(controlled_buffer_140_out), .\dist (5'b00100), .out(snake_str_3));
  Shifter #(.width(32), .shift("lr")) shifter_4 (.in(controlled_buffer_141_out), .\dist (5'b00100), .out(snake_str_4));
  Shifter #(.width(32), .shift("lr")) shifter_5 (.in(controlled_buffer_142_out), .\dist (5'b00100), .out(snake_str_5));
  Shifter #(.width(32), .shift("lr")) shifter_6 (.in(controlled_buffer_143_out), .\dist (5'b00100), .out(snake_str_6));
  Shifter #(.width(32), .shift("lr")) shifter_7 (.in(controlled_buffer_144_out), .\dist (5'b00100), .out(snake_str_7));
  Shifter #(.width(32), .shift("lr")) shifter_8 (.in(controlled_buffer_145_out), .\dist (5'b00100), .out(snake_str_8));
  Shifter #(.width(32), .shift("lr")) shifter_9 (.in(controlled_buffer_146_out), .\dist (5'b00100), .out(snake_str_9));
  Shifter #(.width(32), .shift("lr")) shifter_10 (
    .in(controlled_buffer_147_out), .\dist (5'b00100), .out(snake_str_10));
  Shifter #(.width(32), .shift("lr")) shifter_11 (
    .in(controlled_buffer_148_out), .\dist (5'b00100), .out(snake_str_11));
  Shifter #(.width(32), .shift("lr")) shifter_12 (
    .in(controlled_buffer_149_out), .\dist (5'b00100), .out(snake_str_12));
  Shifter #(.width(32), .shift("lr")) shifter_13 (
    .in(controlled_buffer_150_out), .\dist (5'b00100), .out(snake_str_13));
  Shifter #(.width(32), .shift("lr")) shifter_14 (
    .in(controlled_buffer_151_out), .\dist (5'b00100), .out(snake_str_14));
  Shifter #(.width(32), .shift("lr")) shifter_15 (
    .in(controlled_buffer_152_out), .\dist (5'b00100), .out(snake_str_15));
  Shifter #(.width(32), .shift("lr")) shifter_16 (
    .in(controlled_buffer_153_out), .\dist (5'b00100), .out(snake_str_16));
  Shifter #(.width(32), .shift("lr")) shifter_17 (
    .in(controlled_buffer_154_out), .\dist (5'b00100), .out(snake_str_17));
  Shifter #(.width(32), .shift("lr")) shifter_18 (
    .in(controlled_buffer_155_out), .\dist (5'b00100), .out(snake_str_18));
  Shifter #(.width(32), .shift("lr")) shifter_19 (
    .in(controlled_buffer_156_out), .\dist (5'b00100), .out(snake_str_19));
  Shifter #(.width(32), .shift("lr")) shifter_20 (
    .in(controlled_buffer_157_out), .\dist (5'b00100), .out(snake_str_20));
  Shifter #(.width(32), .shift("lr")) shifter_21 (
    .in(controlled_buffer_158_out), .\dist (5'b00100), .out(snake_str_21));
  Shifter #(.width(32), .shift("lr")) shifter_22 (
    .in(controlled_buffer_159_out), .\dist (5'b00100), .out(snake_str_22));
  Shifter #(.width(32), .shift("lr")) shifter_23 (
    .in(controlled_buffer_160_out), .\dist (5'b00100), .out(snake_str_23));
  Shifter #(.width(32), .shift("lr")) shifter_24 (
    .in(controlled_buffer_161_out), .\dist (5'b00100), .out(snake_str_24));
  Shifter #(.width(32), .shift("lr")) shifter_25 (
    .in(controlled_buffer_162_out), .\dist (5'b00100), .out(snake_str_25));
  Shifter #(.width(32), .shift("lr")) shifter_26 (
    .in(controlled_buffer_163_out), .\dist (5'b00100), .out(snake_str_26));
  Shifter #(.width(32), .shift("lr")) shifter_27 (
    .in(controlled_buffer_164_out), .\dist (5'b00100), .out(snake_str_27));
  Shifter #(.width(32), .shift("lr")) shifter_28 (
    .in(controlled_buffer_165_out), .\dist (5'b00100), .out(snake_str_28));
  Shifter #(.width(32), .shift("lr")) shifter_29 (
    .in(controlled_buffer_166_out), .\dist (5'b00100), .out(snake_str_29));
  Shifter #(.width(32), .shift("lr")) shifter_30 (
    .in(controlled_buffer_167_out), .\dist (5'b00100), .out(snake_str_30));
  Shifter #(.width(32), .shift("lr")) shifter_31 (
    .in(controlled_buffer_168_out), .\dist (5'b00100), .out(snake_str_31));
  Shifter #(.width(32), .shift("lr")) shifter_32 (
    .in(controlled_buffer_169_out), .\dist (5'b00100), .out(snake_str_32));
  or_for_str_32_bit or_for_str_32_bit_1 (
    .in_1(_1_el_str_1), .in_2(_7_el_str_1), .in_3(mouse_rat_str_1), .in_4(ferret_str_1), .in_5(snake_str_1),
    .out_one_str(out_10));  // open: in_6, in_7, in_8
  or_for_str_32_bit or_for_str_32_bit_2 (
    .in_1(_1_el_str_2), .in_2(_7_el_str_2), .in_3(mouse_rat_str_2), .in_4(ferret_str_2), .in_5(snake_str_2),
    .out_one_str(out_11));  // open: in_6, in_7, in_8
  or_for_str_32_bit or_for_str_32_bit_3 (
    .in_1(_1_el_str_3), .in_2(_7_el_str_3), .in_3(mouse_rat_str_3), .in_4(ferret_str_3), .in_5(snake_str_3),
    .out_one_str(out_12));  // open: in_6, in_7, in_8
  or_for_str_32_bit or_for_str_32_bit_4 (
    .in_1(_1_el_str_4), .in_2(_7_el_str_4), .in_3(mouse_rat_str_4), .in_4(ferret_str_4), .in_5(snake_str_4),
    .out_one_str(out_13));  // open: in_6, in_7, in_8
  or_for_str_32_bit or_for_str_32_bit_5 (
    .in_1(_1_el_str_5), .in_2(_7_el_str_5), .in_3(mouse_rat_str_5), .in_4(ferret_str_5), .in_5(snake_str_5),
    .out_one_str(out_14));  // open: in_6, in_7, in_8
  or_for_str_32_bit or_for_str_32_bit_6 (
    .in_1(_1_el_str_6), .in_2(_7_el_str_6), .in_3(mouse_rat_str_6), .in_4(ferret_str_6), .in_5(snake_str_6),
    .out_one_str(out_15));  // open: in_6, in_7, in_8
  or_for_str_32_bit or_for_str_32_bit_7 (
    .in_1(_1_el_str_7), .in_2(_7_el_str_7), .in_3(mouse_rat_str_7), .in_4(ferret_str_7), .in_5(snake_str_7),
    .out_one_str(out_16));  // open: in_6, in_7, in_8
  or_for_str_32_bit or_for_str_32_bit_8 (
    .in_1(_1_el_str_8), .in_2(_7_el_str_8), .in_3(mouse_rat_str_8), .in_4(ferret_str_8), .in_5(snake_str_8),
    .out_one_str(out_17));  // open: in_6, in_7, in_8
  or_for_str_32_bit or_for_str_32_bit_9 (
    .in_1(_1_el_str_9), .in_2(_7_el_str_9), .in_3(mouse_rat_str_9), .in_4(ferret_str_9), .in_5(snake_str_9),
    .out_one_str(out_18));  // open: in_6, in_7, in_8
  or_for_str_32_bit or_for_str_32_bit_10 (
    .in_1(_1_el_str_10), .in_2(_7_el_str_10), .in_3(mouse_rat_str_10), .in_4(ferret_str_10),
    .in_5(snake_str_10), .out_one_str(out_19));  // open: in_6, in_7, in_8
  or_for_str_32_bit or_for_str_32_bit_11 (
    .in_1(_1_el_str_11), .in_2(_7_el_str_11), .in_3(mouse_rat_str_11), .in_4(ferret_str_11),
    .in_5(snake_str_11), .out_one_str(out_20));  // open: in_6, in_7, in_8
  or_for_str_32_bit or_for_str_32_bit_12 (
    .in_1(_1_el_str_12), .in_2(_7_el_str_12), .in_3(mouse_rat_str_12), .in_4(ferret_str_12),
    .in_5(snake_str_12), .out_one_str(out_21));  // open: in_6, in_7, in_8
  or_for_str_32_bit or_for_str_32_bit_13 (
    .in_1(_1_el_str_13), .in_2(_7_el_str_13), .in_3(mouse_rat_str_13), .in_4(ferret_str_13),
    .in_5(snake_str_13), .out_one_str(out_22));  // open: in_6, in_7, in_8
  or_for_str_32_bit or_for_str_32_bit_14 (
    .in_1(_1_el_str_14), .in_2(_7_el_str_14), .in_3(mouse_rat_str_14), .in_4(ferret_str_14),
    .in_5(snake_str_14), .out_one_str(out_23));  // open: in_6, in_7, in_8
  or_for_str_32_bit or_for_str_32_bit_15 (
    .in_1(_1_el_str_15), .in_2(_7_el_str_15), .in_3(mouse_rat_str_15), .in_4(ferret_str_15),
    .in_5(snake_str_15), .out_one_str(out_24));  // open: in_6, in_7, in_8
  or_for_str_32_bit or_for_str_32_bit_16 (
    .in_1(_1_el_str_16), .in_2(_7_el_str_16), .in_3(mouse_rat_str_16), .in_4(ferret_str_16),
    .in_5(snake_str_16), .out_one_str(out_25));  // open: in_6, in_7, in_8
  or_for_str_32_bit or_for_str_32_bit_17 (
    .in_1(_1_el_str_17), .in_2(_7_el_str_17), .in_3(mouse_rat_str_17), .in_4(ferret_str_17),
    .in_5(snake_str_17), .out_one_str(out_26));  // open: in_6, in_7, in_8
  or_for_str_32_bit or_for_str_32_bit_18 (
    .in_1(_1_el_str_18), .in_2(_7_el_str_18), .in_3(mouse_rat_str_18), .in_4(ferret_str_18),
    .in_5(snake_str_18), .out_one_str(out_27));  // open: in_6, in_7, in_8
  or_for_str_32_bit or_for_str_32_bit_19 (
    .in_1(_1_el_str_19), .in_2(_7_el_str_19), .in_3(mouse_rat_str_19), .in_4(ferret_str_19),
    .in_5(snake_str_19), .out_one_str(out_28));  // open: in_6, in_7, in_8
  or_for_str_32_bit or_for_str_32_bit_20 (
    .in_1(_1_el_str_20), .in_2(_7_el_str_20), .in_3(mouse_rat_str_20), .in_4(ferret_str_20),
    .in_5(snake_str_20), .out_one_str(out_29));  // open: in_6, in_7, in_8
  or_for_str_32_bit or_for_str_32_bit_21 (
    .in_1(_1_el_str_21), .in_2(_7_el_str_21), .in_3(mouse_rat_str_21), .in_4(ferret_str_21),
    .in_5(snake_str_21), .out_one_str(out_30));  // open: in_6, in_7, in_8
  or_for_str_32_bit or_for_str_32_bit_22 (
    .in_1(_1_el_str_22), .in_2(_7_el_str_22), .in_3(mouse_rat_str_22), .in_4(ferret_str_22),
    .in_5(snake_str_22), .out_one_str(out_31));  // open: in_6, in_7, in_8
  or_for_str_32_bit or_for_str_32_bit_23 (
    .in_1(_1_el_str_23), .in_2(_7_el_str_23), .in_3(mouse_rat_str_23), .in_4(ferret_str_23),
    .in_5(snake_str_23), .out_one_str(out_32));  // open: in_6, in_7, in_8
  or_for_str_32_bit or_for_str_32_bit_24 (
    .in_1(_1_el_str_24), .in_2(_7_el_str_24), .in_3(mouse_rat_str_24), .in_4(ferret_str_24),
    .in_5(snake_str_24), .out_one_str(out_33));  // open: in_6, in_7, in_8
  or_for_str_32_bit or_for_str_32_bit_25 (
    .in_1(_1_el_str_25), .in_2(_7_el_str_25), .in_3(mouse_rat_str_25), .in_4(ferret_str_25),
    .in_5(snake_str_25), .out_one_str(out_34));  // open: in_6, in_7, in_8
  or_for_str_32_bit or_for_str_32_bit_26 (
    .in_1(_1_el_str_26), .in_2(_7_el_str_26), .in_3(mouse_rat_str_26), .in_4(ferret_str_26),
    .in_5(snake_str_26), .out_one_str(out_35));  // open: in_6, in_7, in_8
  or_for_str_32_bit or_for_str_32_bit_27 (
    .in_1(_1_el_str_27), .in_2(_7_el_str_27), .in_3(mouse_rat_str_27), .in_4(ferret_str_27),
    .in_5(snake_str_27), .out_one_str(out_36));  // open: in_6, in_7, in_8
  or_for_str_32_bit or_for_str_32_bit_28 (
    .in_1(_1_el_str_28), .in_2(_7_el_str_28), .in_3(mouse_rat_str_28), .in_4(ferret_str_28),
    .in_5(snake_str_28), .out_one_str(out_37));  // open: in_6, in_7, in_8
  or_for_str_32_bit or_for_str_32_bit_29 (
    .in_1(_1_el_str_29), .in_2(_7_el_str_29), .in_3(mouse_rat_str_29), .in_4(ferret_str_29),
    .in_5(snake_str_29), .out_one_str(out_38));  // open: in_6, in_7, in_8
  or_for_str_32_bit or_for_str_32_bit_30 (
    .in_1(_1_el_str_30), .in_2(_7_el_str_30), .in_3(mouse_rat_str_30), .in_4(ferret_str_30),
    .in_5(snake_str_30), .out_one_str(out_39));  // open: in_6, in_7, in_8
  or_for_str_32_bit or_for_str_32_bit_31 (
    .in_1(_1_el_str_31), .in_2(_7_el_str_31), .in_3(mouse_rat_str_31), .in_4(ferret_str_31),
    .in_5(snake_str_31), .out_one_str(out_40));  // open: in_6, in_7, in_8
  or_for_str_32_bit or_for_str_32_bit_32 (
    .in_1(_1_el_str_32), .in_2(_7_el_str_32), .in_3(mouse_rat_str_32), .in_4(ferret_str_32),
    .in_5(snake_str_32), .out_one_str(out_41));  // open: in_6, in_7, in_8

  // Other names for the same wires on the sheet: str_1[31:0] = out_10; str_2[31:0] = out_11; str_3[31:0] = out_12;
  //   str_4[31:0] = out_13; str_5[31:0] = out_14; str_6[31:0] = out_15; str_7[31:0] = out_16; str_8[31:0] = out_17;
  //   str_9[31:0] = out_18; str_10[31:0] = out_19; str_11[31:0] = out_20; str_12[31:0] = out_21;
  //   str_13[31:0] = out_22; str_14[31:0] = out_23; str_15[31:0] = out_24; str_16[31:0] = out_25;
  //   str_17[31:0] = out_26; str_18[31:0] = out_27; str_19[31:0] = out_28; str_20[31:0] = out_29;
  //   str_21[31:0] = out_30; str_22[31:0] = out_31; str_23[31:0] = out_32; str_24[31:0] = out_33;
  //   str_25[31:0] = out_34; str_26[31:0] = out_35; str_27[31:0] = out_36; str_28[31:0] = out_37;
  //   str_29[31:0] = out_38; str_30[31:0] = out_39; str_31[31:0] = out_40; str_32[31:0] = out_41

  // Notes on the sheet:
  //   2 -> 1
  //   3 -> 7
endmodule

module or_for_str_30_bit (
  input  [29:0] in_1,
  input  [29:0] in_2,
  input  [29:0] in_3,
  input  [29:0] in_4,
  input  [29:0] in_5,
  input  [29:0] in_6,
  input  [29:0] in_7,
  input  [29:0] in_8,
  output [29:0] out_one_str
);

  Pull_Resistor pull_resistor_1 (.node(in_1));
  Pull_Resistor pull_resistor_2 (.node(in_2));
  Pull_Resistor pull_resistor_3 (.node(in_3));
  Pull_Resistor pull_resistor_4 (.node(in_4));
  Pull_Resistor pull_resistor_5 (.node(in_5));
  Pull_Resistor pull_resistor_6 (.node(in_6));
  Pull_Resistor pull_resistor_7 (.node(in_7));
  Pull_Resistor pull_resistor_8 (.node(in_8));
  assign out_one_str = in_1 | in_2 | in_3 | in_4 | in_5 | in_6 | in_7 | in_8;  // OR_Gate or_1, 30 bits wide
endmodule

module or_for_str_28_bit (
  input  [27:0] in_1,
  input  [27:0] in_2,
  input  [27:0] in_3,
  input  [27:0] in_4,
  input  [27:0] in_5,
  input  [27:0] in_6,
  input  [27:0] in_7,
  input  [27:0] in_8,
  output [27:0] out_one_str
);

  Pull_Resistor pull_resistor_1 (.node(in_1));
  Pull_Resistor pull_resistor_2 (.node(in_2));
  Pull_Resistor pull_resistor_3 (.node(in_3));
  Pull_Resistor pull_resistor_4 (.node(in_4));
  Pull_Resistor pull_resistor_5 (.node(in_5));
  Pull_Resistor pull_resistor_6 (.node(in_6));
  Pull_Resistor pull_resistor_7 (.node(in_7));
  Pull_Resistor pull_resistor_8 (.node(in_8));
  assign out_one_str = in_1 | in_2 | in_3 | in_4 | in_5 | in_6 | in_7 | in_8;  // OR_Gate or_1, 28 bits wide
endmodule

module or_for_str_29_bit (
  input  [28:0] in_1,
  input  [28:0] in_2,
  input  [28:0] in_3,
  input  [28:0] in_4,
  input  [28:0] in_5,
  input  [28:0] in_6,
  input  [28:0] in_7,
  input  [28:0] in_8,
  output [28:0] out_one_str
);

  Pull_Resistor pull_resistor_1 (.node(in_1));
  Pull_Resistor pull_resistor_2 (.node(in_2));
  Pull_Resistor pull_resistor_3 (.node(in_3));
  Pull_Resistor pull_resistor_4 (.node(in_4));
  Pull_Resistor pull_resistor_5 (.node(in_5));
  Pull_Resistor pull_resistor_6 (.node(in_6));
  Pull_Resistor pull_resistor_7 (.node(in_7));
  Pull_Resistor pull_resistor_8 (.node(in_8));
  assign out_one_str = in_1 | in_2 | in_3 | in_4 | in_5 | in_6 | in_7 | in_8;  // OR_Gate or_1, 29 bits wide
endmodule

module or_for_str_31_bit (
  input  [30:0] in_1,
  input  [30:0] in_2,
  input  [30:0] in_3,
  input  [30:0] in_4,
  input  [30:0] in_5,
  input  [30:0] in_6,
  input  [30:0] in_7,
  input  [30:0] in_8,
  output [30:0] out_one_str
);

  Pull_Resistor pull_resistor_1 (.node(in_1));
  Pull_Resistor pull_resistor_2 (.node(in_2));
  Pull_Resistor pull_resistor_3 (.node(in_3));
  Pull_Resistor pull_resistor_4 (.node(in_4));
  Pull_Resistor pull_resistor_5 (.node(in_5));
  Pull_Resistor pull_resistor_6 (.node(in_6));
  Pull_Resistor pull_resistor_7 (.node(in_7));
  Pull_Resistor pull_resistor_8 (.node(in_8));
  assign out_one_str = in_1 | in_2 | in_3 | in_4 | in_5 | in_6 | in_7 | in_8;  // OR_Gate or_1, 31 bits wide
endmodule

module or_for_str_32_bit (
  input  [31:0] in_1,
  input  [31:0] in_2,
  input  [31:0] in_3,
  input  [31:0] in_4,
  input  [31:0] in_5,
  input  [31:0] in_6,
  input  [31:0] in_7,
  input  [31:0] in_8,
  output [31:0] out_one_str
);

  Pull_Resistor pull_resistor_1 (.node(in_1));
  Pull_Resistor pull_resistor_2 (.node(in_2));
  Pull_Resistor pull_resistor_3 (.node(in_3));
  Pull_Resistor pull_resistor_4 (.node(in_4));
  Pull_Resistor pull_resistor_5 (.node(in_5));
  Pull_Resistor pull_resistor_6 (.node(in_6));
  Pull_Resistor pull_resistor_7 (.node(in_7));
  Pull_Resistor pull_resistor_8 (.node(in_8));
  assign out_one_str = in_1 | in_2 | in_3 | in_4 | in_5 | in_6 | in_7 | in_8;  // OR_Gate or_1, 32 bits wide
endmodule

module driver_l (
  input  [1:0] gamestate,
  input  [1:0] curr_enemy,
  input  [8:0] b,
  input  [15:0] ASSH,
  output [30:0] out_5,
  output [29:0] out_6,
  output [28:0] out_7,
  output [27:0] out_8,
  output [30:0] out_9,
  output [29:0] out_10,
  output [28:0] out_11,
  output [27:0] out_12,
  output [30:0] out_13,
  output [29:0] out_14,
  output [28:0] out_15,
  output [27:0] out_16,
  output [30:0] out_17,
  output [29:0] out_18,
  output [28:0] out_19,
  output [27:0] out_20,
  output [30:0] out_21,
  output [29:0] out_22,
  output [28:0] out_23,
  output [27:0] out_24,
  output [30:0] out_25,
  output [29:0] out_26,
  output [28:0] out_27,
  output [27:0] out_28,
  output [30:0] out_29,
  output [29:0] out_30,
  output [28:0] out_31,
  output [27:0] out_32,
  output [30:0] out_33,
  output [29:0] out_34,
  output [28:0] out_35,
  output [27:0] out_36,
  output [30:0] out_37,
  output [29:0] out_38,
  output [28:0] out_39,
  output [27:0] out_40,
  output [30:0] out_41,
  output [29:0] out_42,
  output [28:0] out_43,
  output [27:0] out_44,
  output [30:0] out_45,
  output [29:0] out_46,
  output [28:0] out_47,
  output [27:0] out_48,
  output [30:0] out_49,
  output [29:0] out_50,
  output [28:0] out_51,
  output [27:0] out_52,
  output [30:0] out_53,
  output [29:0] out_54,
  output [28:0] out_55,
  output [27:0] out_56,
  output [30:0] out_57,
  output [29:0] out_58,
  output [28:0] out_59,
  output [27:0] out_60,
  output [30:0] out_61,
  output [29:0] out_62,
  output [28:0] out_63,
  output [27:0] out_64,
  output [30:0] out_65,
  output [29:0] out_66,
  output [28:0] out_67,
  output [27:0] out_68,
  output [30:0] out_69,
  output [29:0] out_70,
  output [28:0] out_71,
  output [27:0] out_72,
  output [30:0] out_73,
  output [29:0] out_74,
  output [28:0] out_75,
  output [27:0] out_76,
  output [30:0] out_77,
  output [29:0] out_78,
  output [28:0] out_79,
  output [27:0] out_80,
  output [30:0] out_81,
  output [29:0] out_82,
  output [28:0] out_83,
  output [27:0] out_84,
  output [30:0] out_85,
  output [29:0] out_86,
  output [28:0] out_87,
  output [27:0] out_88,
  output [30:0] out_89,
  output [29:0] out_90,
  output [28:0] out_91,
  output [27:0] out_92,
  output [30:0] out_93,
  output [29:0] out_94,
  output [28:0] out_95,
  output [27:0] out_96,
  output [30:0] out_97,
  output [29:0] out_98,
  output [28:0] out_99,
  output [27:0] out_100,
  output [30:0] out_101,
  output [29:0] out_102,
  output [28:0] out_103,
  output [27:0] out_104,
  output [30:0] out_105,
  output [29:0] out_106,
  output [28:0] out_107,
  output [27:0] out_108,
  output [30:0] out_109,
  output [29:0] out_110,
  output [28:0] out_111,
  output [27:0] out_112,
  output [30:0] out_113,
  output [29:0] out_114,
  output [28:0] out_115,
  output [27:0] out_116,
  output [30:0] out_117,
  output [29:0] out_118,
  output [28:0] out_119,
  output [27:0] out_120,
  output [30:0] out_121,
  output [29:0] out_122,
  output [28:0] out_123,
  output [27:0] out_124,
  output [30:0] out_125,
  output [29:0] out_126,
  output [28:0] out_127,
  output [27:0] out_128,
  output [30:0] out_129,
  output [29:0] out_130,
  output [28:0] out_131,
  output [27:0] out_132
);

  wire _1, _2, _3, _4, _5, _6, _7, _8, _9, _10, _11, control_elems_1_is_a_chest, isBattle;

  look_on_minimap look_on_minimap_1 ();
  control_elems control_elems_1 (
    .b(b), .ASSH(ASSH), ._1(_1), ._2(_2), ._3(_3), ._4(_4), ._6(_6), ._7(_7), ._9(_9), ._10(_10), ._11(_11),
    ._5(_5), ._8(_8), .is_a_chest(control_elems_1_is_a_chest));
  Tile_l_1_color tile_l_1_color_1 (
    ._11(_11), ._10(_10), .isBattle(isBattle), .is_a_chest(control_elems_1_is_a_chest), .out_5(out_8),
    .out_6(out_12), .out_7(out_16), .out_8(out_20), .out_9(out_24), .out_10(out_28), .out_11(out_32),
    .out_12(out_36), .out_13(out_40), .out_14(out_44), .out_15(out_48), .out_16(out_52), .out_17(out_56),
    .out_18(out_60), .out_19(out_64), .out_20(out_68), .out_21(out_72), .out_22(out_76), .out_23(out_80),
    .out_24(out_84), .out_25(out_88), .out_26(out_92), .out_27(out_96), .out_28(out_100), .out_29(out_104),
    .out_30(out_108), .out_31(out_112), .out_32(out_116), .out_33(out_120), .out_34(out_124),
    .out_35(out_128), .out_36(out_132));
  Comparator #(.width(2), .mode("unsigned")) comparator_1 (.a(2'b10), .b(gamestate), .eq(isBattle));  // open: gt, lt
  Tile_l_2_color tile_l_2_color_1 (
    ._11(_11), ._10(_10), ._9(_9), ._8(_8), ._7(_7), .isBattle(isBattle), .out_7(out_7), .out_8(out_11),
    .out_9(out_15), .out_10(out_19), .out_11(out_23), .out_12(out_27), .out_13(out_31), .out_14(out_35),
    .out_15(out_39), .out_16(out_43), .out_17(out_47), .out_18(out_51), .out_19(out_55), .out_20(out_59),
    .out_21(out_63), .out_22(out_67), .out_23(out_71), .out_24(out_75), .out_25(out_79), .out_26(out_83),
    .out_27(out_87), .out_28(out_91), .out_29(out_95), .out_30(out_99), .out_31(out_103), .out_32(out_107),
    .out_33(out_111), .out_34(out_115), .out_35(out_119), .out_36(out_123), .out_37(out_127), .out_38(out_131));
  Tile_l_3_color tile_l_3_color_1 (
    ._11(_11), ._10(_10), ._9(_9), ._8(_8), ._7(_7), ._6(_6), ._5(_5), ._4(_4), .isBattle(isBattle),
    .out_10(out_6), .out_11(out_10), .out_12(out_14), .out_13(out_18), .out_14(out_22), .out_15(out_26),
    .out_16(out_30), .out_17(out_34), .out_18(out_38), .out_19(out_42), .out_20(out_46), .out_21(out_50),
    .out_22(out_54), .out_23(out_58), .out_24(out_62), .out_25(out_66), .out_26(out_70), .out_27(out_74),
    .out_28(out_78), .out_29(out_82), .out_30(out_86), .out_31(out_90), .out_32(out_94), .out_33(out_98),
    .out_34(out_102), .out_35(out_106), .out_36(out_110), .out_37(out_114), .out_38(out_118),
    .out_39(out_122), .out_40(out_126), .out_41(out_130));
  Tile_l_4_color tile_l_4_color_1 (
    ._8(_8), ._6(_6), ._5(_5), ._4(_4), ._3(_3), ._2(_2), ._1(_1), .enemy(curr_enemy), .gameState(gamestate),
    .out_10(out_5), .out_11(out_9), .out_12(out_13), .out_13(out_17), .out_14(out_21), .out_15(out_25),
    .out_16(out_29), .out_17(out_33), .out_18(out_37), .out_19(out_41), .out_20(out_45), .out_21(out_49),
    .out_22(out_53), .out_23(out_57), .out_24(out_61), .out_25(out_65), .out_26(out_69), .out_27(out_73),
    .out_28(out_77), .out_29(out_81), .out_30(out_85), .out_31(out_89), .out_32(out_93), .out_33(out_97),
    .out_34(out_101), .out_35(out_105), .out_36(out_109), .out_37(out_113), .out_38(out_117),
    .out_39(out_121), .out_40(out_125), .out_41(out_129));

  // Other names for the same wires on the sheet: _29_bit_str_1[27:0] = out_8; _29_bit_str_2[27:0] = out_12;
  //   _29_bit_str_3[27:0] = out_16; _29_bit_str_4[27:0] = out_20; _29_bit_str_5[27:0] = out_24;
  //   _29_bit_str_6[27:0] = out_28; _29_bit_str_7[27:0] = out_32; _29_bit_str_8[27:0] = out_36;
  //   _29_bit_str_9[27:0] = out_40; _29_bit_str_10[27:0] = out_44; _29_bit_str_11[27:0] = out_48;
  //   _29_bit_str_12[27:0] = out_52; _29_bit_str_13[27:0] = out_56; _29_bit_str_14[27:0] = out_60;
  //   _29_bit_str_15[27:0] = out_64; _29_bit_str_16[27:0] = out_68; _29_bit_str_17[27:0] = out_72;
  //   _29_bit_str_18[27:0] = out_76; _29_bit_str_19[27:0] = out_80; _29_bit_str_20[27:0] = out_84;
  //   _29_bit_str_21[27:0] = out_88; _29_bit_str_22[27:0] = out_92; _29_bit_str_23[27:0] = out_96;
  //   _29_bit_str_24[27:0] = out_100; _29_bit_str_25[27:0] = out_104; _29_bit_str_26[27:0] = out_108;
  //   _29_bit_str_27[27:0] = out_112; _29_bit_str_28[27:0] = out_116; _29_bit_str_29[27:0] = out_120;
  //   _29_bit_str_30[27:0] = out_124; _29_bit_str_31[27:0] = out_128; _29_bit_str_32[27:0] = out_132;
  //   _30_bit_str_1[28:0] = out_7; _30_bit_str_2[28:0] = out_11; _30_bit_str_3[28:0] = out_15;
  //   _30_bit_str_4[28:0] = out_19; _30_bit_str_5[28:0] = out_23; _30_bit_str_6[28:0] = out_27;
  //   _30_bit_str_7[28:0] = out_31; _30_bit_str_8[28:0] = out_35; _30_bit_str_9[28:0] = out_39;
  //   _30_bit_str_10[28:0] = out_43; _30_bit_str_11[28:0] = out_47; _30_bit_str_12[28:0] = out_51;
  //   _30_bit_str_13[28:0] = out_55; _30_bit_str_14[28:0] = out_59; _30_bit_str_15[28:0] = out_63;
  //   _30_bit_str_16[28:0] = out_67; _30_bit_str_17[28:0] = out_71; _30_bit_str_18[28:0] = out_75;
  //   _30_bit_str_19[28:0] = out_79; _30_bit_str_20[28:0] = out_83; _30_bit_str_21[28:0] = out_87;
  //   _30_bit_str_22[28:0] = out_91; _30_bit_str_23[28:0] = out_95; _30_bit_str_24[28:0] = out_99;
  //   _30_bit_str_25[28:0] = out_103; _30_bit_str_26[28:0] = out_107; _30_bit_str_27[28:0] = out_111;
  //   _30_bit_str_28[28:0] = out_115; _30_bit_str_29[28:0] = out_119; _30_bit_str_30[28:0] = out_123;
  //   _30_bit_str_31[28:0] = out_127; _30_bit_str_32[28:0] = out_131; _31_bit_str_1[29:0] = out_6;
  //   _31_bit_str_2[29:0] = out_10; _31_bit_str_3[29:0] = out_14; _31_bit_str_4[29:0] = out_18;
  //   _31_bit_str_5[29:0] = out_22; _31_bit_str_6[29:0] = out_26; _31_bit_str_7[29:0] = out_30;
  //   _31_bit_str_8[29:0] = out_34; _31_bit_str_9[29:0] = out_38; _31_bit_str_10[29:0] = out_42;
  //   _31_bit_str_11[29:0] = out_46; _31_bit_str_12[29:0] = out_50; _31_bit_str_13[29:0] = out_54;
  //   _31_bit_str_14[29:0] = out_58; _31_bit_str_15[29:0] = out_62; _31_bit_str_16[29:0] = out_66;
  //   _31_bit_str_17[29:0] = out_70; _31_bit_str_18[29:0] = out_74; _31_bit_str_19[29:0] = out_78;
  //   _31_bit_str_20[29:0] = out_82; _31_bit_str_21[29:0] = out_86; _31_bit_str_22[29:0] = out_90;
  //   _31_bit_str_23[29:0] = out_94; _31_bit_str_24[29:0] = out_98; _31_bit_str_25[29:0] = out_102;
  //   _31_bit_str_26[29:0] = out_106; _31_bit_str_27[29:0] = out_110; _31_bit_str_28[29:0] = out_114;
  //   _31_bit_str_29[29:0] = out_118; _31_bit_str_30[29:0] = out_122; _31_bit_str_31[29:0] = out_126;
  //   _31_bit_str_32[29:0] = out_130; _32_bit_str_1[30:0] = out_5; _32_bit_str_2[30:0] = out_9;
  //   _32_bit_str_3[30:0] = out_13; _32_bit_str_4[30:0] = out_17; _32_bit_str_5[30:0] = out_21;
  //   _32_bit_str_6[30:0] = out_25; _32_bit_str_7[30:0] = out_29; _32_bit_str_8[30:0] = out_33;
  //   _32_bit_str_9[30:0] = out_37; _32_bit_str_10[30:0] = out_41; _32_bit_str_11[30:0] = out_45;
  //   _32_bit_str_12[30:0] = out_49; _32_bit_str_13[30:0] = out_53; _32_bit_str_14[30:0] = out_57;
  //   _32_bit_str_15[30:0] = out_61; _32_bit_str_16[30:0] = out_65; _32_bit_str_17[30:0] = out_69;
  //   _32_bit_str_18[30:0] = out_73; _32_bit_str_19[30:0] = out_77; _32_bit_str_20[30:0] = out_81;
  //   _32_bit_str_21[30:0] = out_85; _32_bit_str_22[30:0] = out_89; _32_bit_str_23[30:0] = out_93;
  //   _32_bit_str_24[30:0] = out_97; _32_bit_str_25[30:0] = out_101; _32_bit_str_26[30:0] = out_105;
  //   _32_bit_str_27[30:0] = out_109; _32_bit_str_28[30:0] = out_113; _32_bit_str_29[30:0] = out_117;
  //   _32_bit_str_30[30:0] = out_121; _32_bit_str_31[30:0] = out_125; _32_bit_str_32[30:0] = out_129;
  //   enemy[1:0] = curr_enemy

  // Notes on the sheet:
  //   ФОН / 4 Цвет
  //   x-Bit = (x-1)-Bit
  //   Void / 3 Цвет
  //   Void / 2 Цвет
  //   Void / 1 Цвет
endmodule

module Tile_l_1_color (
  input  _11,
  input  _10,
  input  isBattle,
  input  is_a_chest,
  output [27:0] out_5,
  output [27:0] out_6,
  output [27:0] out_7,
  output [27:0] out_8,
  output [27:0] out_9,
  output [27:0] out_10,
  output [27:0] out_11,
  output [27:0] out_12,
  output [27:0] out_13,
  output [27:0] out_14,
  output [27:0] out_15,
  output [27:0] out_16,
  output [27:0] out_17,
  output [27:0] out_18,
  output [27:0] out_19,
  output [27:0] out_20,
  output [27:0] out_21,
  output [27:0] out_22,
  output [27:0] out_23,
  output [27:0] out_24,
  output [27:0] out_25,
  output [27:0] out_26,
  output [27:0] out_27,
  output [27:0] out_28,
  output [27:0] out_29,
  output [27:0] out_30,
  output [27:0] out_31,
  output [27:0] out_32,
  output [27:0] out_33,
  output [27:0] out_34,
  output [27:0] out_35,
  output [27:0] out_36
);

  wire _14, _15, chest, not_1_out;
  wire [27:0] _1_el_str_1, _1_el_str_2, _1_el_str_3, _1_el_str_4, _1_el_str_5, _1_el_str_6, _1_el_str_7,
       _1_el_str_8, _1_el_str_9, _1_el_str_10, _1_el_str_11, _1_el_str_12, _1_el_str_13, _1_el_str_14,
       _1_el_str_15, _1_el_str_16, _1_el_str_17, _1_el_str_18, _1_el_str_19, _1_el_str_20, _1_el_str_21,
       _1_el_str_22, _1_el_str_23, _1_el_str_24, _1_el_str_25, _1_el_str_26, _1_el_str_27, _1_el_str_28,
       _1_el_str_29, _1_el_str_30, _1_el_str_31, _1_el_str_32, chest_str_1, chest_str_2, chest_str_3,
       chest_str_4, chest_str_5, chest_str_6, chest_str_7, chest_str_8, chest_str_9, chest_str_10,
       chest_str_11, chest_str_12, chest_str_13, chest_str_14, chest_str_15, chest_str_16, chest_str_17,
       chest_str_18, chest_str_19, chest_str_20, chest_str_21, chest_str_22, chest_str_23, chest_str_24,
       chest_str_25, chest_str_26, chest_str_27, chest_str_28, chest_str_29, chest_str_30, chest_str_31,
       chest_str_32;

  assign _15 = not_1_out ? _11 : 1'bz;  // Controlled_Buffer controlled_buffer_1
  assign _14 = not_1_out ? _10 : 1'bz;  // Controlled_Buffer controlled_buffer_2
  not not_1 (not_1_out, isBattle);
  assign chest = not_1_out ? is_a_chest : 1'bz;  // Controlled_Buffer controlled_buffer_3
  assign _15 = isBattle ? 1'b0 : 1'bz;  // Controlled_Buffer controlled_buffer_4
  assign _14 = isBattle ? 1'b0 : 1'bz;  // Controlled_Buffer controlled_buffer_5
  assign chest = isBattle ? 1'b0 : 1'bz;  // Controlled_Buffer controlled_buffer_6
  assign _1_el_str_1 = _14 ? {28{1'b0}} : 28'bz;  // Controlled_Buffer controlled_buffer_7
  assign _1_el_str_2 = _14 ? {28{1'b0}} : 28'bz;  // Controlled_Buffer controlled_buffer_8
  assign _1_el_str_3 = _14 ? 28'hc000000 : 28'bz;  // Controlled_Buffer controlled_buffer_9
  assign _1_el_str_4 = _14 ? 28'hf000000 : 28'bz;  // Controlled_Buffer controlled_buffer_10
  assign _1_el_str_5 = _14 ? 28'hfc00000 : 28'bz;  // Controlled_Buffer controlled_buffer_11
  assign _1_el_str_6 = _14 ? 28'hff00000 : 28'bz;  // Controlled_Buffer controlled_buffer_12
  assign _1_el_str_7 = _14 ? 28'hff00000 : 28'bz;  // Controlled_Buffer controlled_buffer_13
  assign _1_el_str_8 = _14 ? 28'hff00000 : 28'bz;  // Controlled_Buffer controlled_buffer_14
  assign _1_el_str_9 = _14 ? 28'hff00000 : 28'bz;  // Controlled_Buffer controlled_buffer_15
  assign _1_el_str_10 = _14 ? 28'hff00000 : 28'bz;  // Controlled_Buffer controlled_buffer_16
  assign _1_el_str_11 = _14 ? 28'hff00000 : 28'bz;  // Controlled_Buffer controlled_buffer_17
  assign _1_el_str_12 = _14 ? 28'hff00000 : 28'bz;  // Controlled_Buffer controlled_buffer_18
  assign _1_el_str_13 = _14 ? 28'hff00000 : 28'bz;  // Controlled_Buffer controlled_buffer_19
  assign _1_el_str_14 = _14 ? 28'hff00000 : 28'bz;  // Controlled_Buffer controlled_buffer_20
  assign _1_el_str_15 = _14 ? 28'hff00000 : 28'bz;  // Controlled_Buffer controlled_buffer_21
  assign _1_el_str_16 = _14 ? 28'hff00000 : 28'bz;  // Controlled_Buffer controlled_buffer_22
  assign _1_el_str_17 = _14 ? 28'hff00000 : 28'bz;  // Controlled_Buffer controlled_buffer_23
  assign _1_el_str_18 = _14 ? 28'hff00000 : 28'bz;  // Controlled_Buffer controlled_buffer_24
  assign _1_el_str_19 = _14 ? 28'hff00000 : 28'bz;  // Controlled_Buffer controlled_buffer_25
  assign _1_el_str_20 = _14 ? 28'hff00000 : 28'bz;  // Controlled_Buffer controlled_buffer_26
  assign _1_el_str_21 = _14 ? 28'hff00000 : 28'bz;  // Controlled_Buffer controlled_buffer_27
  assign _1_el_str_22 = _14 ? 28'hff00000 : 28'bz;  // Controlled_Buffer controlled_buffer_28
  assign _1_el_str_23 = _14 ? 28'hff00000 : 28'bz;  // Controlled_Buffer controlled_buffer_29
  assign _1_el_str_24 = _14 ? 28'hff00000 : 28'bz;  // Controlled_Buffer controlled_buffer_30
  assign _1_el_str_25 = _14 ? 28'hfe00000 : 28'bz;  // Controlled_Buffer controlled_buffer_31
  assign _1_el_str_26 = _14 ? 28'hfc00000 : 28'bz;  // Controlled_Buffer controlled_buffer_32
  assign _1_el_str_27 = _14 ? 28'hf000000 : 28'bz;  // Controlled_Buffer controlled_buffer_33
  assign _1_el_str_28 = _14 ? 28'hc000000 : 28'bz;  // Controlled_Buffer controlled_buffer_34
  assign _1_el_str_29 = _14 ? 28'h8000000 : 28'bz;  // Controlled_Buffer controlled_buffer_35
  assign _1_el_str_30 = _14 ? {28{1'b0}} : 28'bz;  // Controlled_Buffer controlled_buffer_36
  assign _1_el_str_31 = _14 ? {28{1'b0}} : 28'bz;  // Controlled_Buffer controlled_buffer_37
  assign _1_el_str_32 = _14 ? {28{1'b0}} : 28'bz;  // Controlled_Buffer controlled_buffer_38
  assign chest_str_19 = chest ? 28'h1ff : 28'bz;  // Controlled_Buffer controlled_buffer_39
  assign chest_str_20 = chest ? 28'h180 : 28'bz;  // Controlled_Buffer controlled_buffer_40
  assign chest_str_21 = chest ? 28'h17f : 28'bz;  // Controlled_Buffer controlled_buffer_41
  assign chest_str_22 = chest ? 28'h100 : 28'bz;  // Controlled_Buffer controlled_buffer_42
  assign chest_str_23 = chest ? 28'h100 : 28'bz;  // Controlled_Buffer controlled_buffer_43
  assign chest_str_24 = chest ? 28'h1ff : 28'bz;  // Controlled_Buffer controlled_buffer_44
  or_for_str_28_bit or_for_str_28_bit_1 (
    .in_1(_1_el_str_1), .in_2(chest_str_1), .out_one_str(out_5));  // open: in_3, in_4, in_5, in_6, in_7, in_8
  or_for_str_28_bit or_for_str_28_bit_2 (
    .in_1(_1_el_str_2), .in_2(chest_str_2), .out_one_str(out_6));  // open: in_3, in_4, in_5, in_6, in_7, in_8
  or_for_str_28_bit or_for_str_28_bit_3 (
    .in_1(_1_el_str_3), .in_2(chest_str_3), .out_one_str(out_7));  // open: in_3, in_4, in_5, in_6, in_7, in_8
  or_for_str_28_bit or_for_str_28_bit_4 (
    .in_1(_1_el_str_4), .in_2(chest_str_4), .out_one_str(out_8));  // open: in_3, in_4, in_5, in_6, in_7, in_8
  or_for_str_28_bit or_for_str_28_bit_5 (
    .in_1(_1_el_str_5), .in_2(chest_str_5), .out_one_str(out_9));  // open: in_3, in_4, in_5, in_6, in_7, in_8
  or_for_str_28_bit or_for_str_28_bit_6 (
    .in_1(_1_el_str_6), .in_2(chest_str_6), .out_one_str(out_10));  // open: in_3, in_4, in_5, in_6, in_7, in_8
  or_for_str_28_bit or_for_str_28_bit_7 (
    .in_1(_1_el_str_7), .in_2(chest_str_7), .out_one_str(out_11));  // open: in_3, in_4, in_5, in_6, in_7, in_8
  or_for_str_28_bit or_for_str_28_bit_8 (
    .in_1(_1_el_str_8), .in_2(chest_str_8), .out_one_str(out_12));  // open: in_3, in_4, in_5, in_6, in_7, in_8
  or_for_str_28_bit or_for_str_28_bit_9 (
    .in_1(_1_el_str_9), .in_2(chest_str_9), .out_one_str(out_13));  // open: in_3, in_4, in_5, in_6, in_7, in_8
  or_for_str_28_bit or_for_str_28_bit_10 (
    .in_1(_1_el_str_10), .in_2(chest_str_10), .out_one_str(out_14));  // open: in_3, in_4, in_5, in_6, in_7, in_8
  or_for_str_28_bit or_for_str_28_bit_11 (
    .in_1(_1_el_str_11), .in_2(chest_str_11), .out_one_str(out_15));  // open: in_3, in_4, in_5, in_6, in_7, in_8
  or_for_str_28_bit or_for_str_28_bit_12 (
    .in_1(_1_el_str_12), .in_2(chest_str_12), .out_one_str(out_16));  // open: in_3, in_4, in_5, in_6, in_7, in_8
  or_for_str_28_bit or_for_str_28_bit_13 (
    .in_1(_1_el_str_13), .in_2(chest_str_13), .out_one_str(out_17));  // open: in_3, in_4, in_5, in_6, in_7, in_8
  or_for_str_28_bit or_for_str_28_bit_14 (
    .in_1(_1_el_str_14), .in_2(chest_str_14), .out_one_str(out_18));  // open: in_3, in_4, in_5, in_6, in_7, in_8
  or_for_str_28_bit or_for_str_28_bit_15 (
    .in_1(_1_el_str_15), .in_2(chest_str_15), .out_one_str(out_19));  // open: in_3, in_4, in_5, in_6, in_7, in_8
  or_for_str_28_bit or_for_str_28_bit_16 (
    .in_1(_1_el_str_16), .in_2(chest_str_16), .out_one_str(out_20));  // open: in_3, in_4, in_5, in_6, in_7, in_8
  or_for_str_28_bit or_for_str_28_bit_17 (
    .in_1(_1_el_str_17), .in_2(chest_str_17), .out_one_str(out_21));  // open: in_3, in_4, in_5, in_6, in_7, in_8
  or_for_str_28_bit or_for_str_28_bit_18 (
    .in_1(_1_el_str_18), .in_2(chest_str_18), .out_one_str(out_22));  // open: in_3, in_4, in_5, in_6, in_7, in_8
  or_for_str_28_bit or_for_str_28_bit_19 (
    .in_1(_1_el_str_19), .in_2(chest_str_19), .out_one_str(out_23));  // open: in_3, in_4, in_5, in_6, in_7, in_8
  or_for_str_28_bit or_for_str_28_bit_20 (
    .in_1(_1_el_str_20), .in_2(chest_str_20), .out_one_str(out_24));  // open: in_3, in_4, in_5, in_6, in_7, in_8
  or_for_str_28_bit or_for_str_28_bit_21 (
    .in_1(_1_el_str_21), .in_2(chest_str_21), .out_one_str(out_25));  // open: in_3, in_4, in_5, in_6, in_7, in_8
  or_for_str_28_bit or_for_str_28_bit_22 (
    .in_1(_1_el_str_22), .in_2(chest_str_22), .out_one_str(out_26));  // open: in_3, in_4, in_5, in_6, in_7, in_8
  or_for_str_28_bit or_for_str_28_bit_23 (
    .in_1(_1_el_str_23), .in_2(chest_str_23), .out_one_str(out_27));  // open: in_3, in_4, in_5, in_6, in_7, in_8
  or_for_str_28_bit or_for_str_28_bit_24 (
    .in_1(_1_el_str_24), .in_2(chest_str_24), .out_one_str(out_28));  // open: in_3, in_4, in_5, in_6, in_7, in_8
  or_for_str_28_bit or_for_str_28_bit_25 (
    .in_1(_1_el_str_25), .in_2(chest_str_25), .out_one_str(out_29));  // open: in_3, in_4, in_5, in_6, in_7, in_8
  or_for_str_28_bit or_for_str_28_bit_26 (
    .in_1(_1_el_str_26), .in_2(chest_str_26), .out_one_str(out_30));  // open: in_3, in_4, in_5, in_6, in_7, in_8
  or_for_str_28_bit or_for_str_28_bit_27 (
    .in_1(_1_el_str_27), .in_2(chest_str_27), .out_one_str(out_31));  // open: in_3, in_4, in_5, in_6, in_7, in_8
  or_for_str_28_bit or_for_str_28_bit_28 (
    .in_1(_1_el_str_28), .in_2(chest_str_28), .out_one_str(out_32));  // open: in_3, in_4, in_5, in_6, in_7, in_8
  or_for_str_28_bit or_for_str_28_bit_29 (
    .in_1(_1_el_str_29), .in_2(chest_str_29), .out_one_str(out_33));  // open: in_3, in_4, in_5, in_6, in_7, in_8
  or_for_str_28_bit or_for_str_28_bit_30 (
    .in_1(_1_el_str_30), .in_2(chest_str_30), .out_one_str(out_34));  // open: in_3, in_4, in_5, in_6, in_7, in_8
  or_for_str_28_bit or_for_str_28_bit_31 (
    .in_1(_1_el_str_31), .in_2(chest_str_31), .out_one_str(out_35));  // open: in_3, in_4, in_5, in_6, in_7, in_8
  or_for_str_28_bit or_for_str_28_bit_32 (
    .in_1(_1_el_str_32), .in_2(chest_str_32), .out_one_str(out_36));  // open: in_3, in_4, in_5, in_6, in_7, in_8

  // Other names for the same wires on the sheet: str_1[27:0] = out_5; str_2[27:0] = out_6; str_3[27:0] = out_7;
  //   str_4[27:0] = out_8; str_5[27:0] = out_9; str_6[27:0] = out_10; str_7[27:0] = out_11; str_8[27:0] = out_12;
  //   str_9[27:0] = out_13; str_10[27:0] = out_14; str_11[27:0] = out_15; str_12[27:0] = out_16;
  //   str_13[27:0] = out_17; str_14[27:0] = out_18; str_15[27:0] = out_19; str_16[27:0] = out_20;
  //   str_17[27:0] = out_21; str_18[27:0] = out_22; str_19[27:0] = out_23; str_20[27:0] = out_24;
  //   str_21[27:0] = out_25; str_22[27:0] = out_26; str_23[27:0] = out_27; str_24[27:0] = out_28;
  //   str_25[27:0] = out_29; str_26[27:0] = out_30; str_27[27:0] = out_31; str_28[27:0] = out_32;
  //   str_29[27:0] = out_33; str_30[27:0] = out_34; str_31[27:0] = out_35; str_32[27:0] = out_36

  // Notes on the sheet:
  //   1 цвет
endmodule

module Tile_l_2_color (
  input  _11,
  input  _10,
  input  _9,
  input  _8,
  input  _7,
  input  isBattle,
  output [28:0] out_7,
  output [28:0] out_8,
  output [28:0] out_9,
  output [28:0] out_10,
  output [28:0] out_11,
  output [28:0] out_12,
  output [28:0] out_13,
  output [28:0] out_14,
  output [28:0] out_15,
  output [28:0] out_16,
  output [28:0] out_17,
  output [28:0] out_18,
  output [28:0] out_19,
  output [28:0] out_20,
  output [28:0] out_21,
  output [28:0] out_22,
  output [28:0] out_23,
  output [28:0] out_24,
  output [28:0] out_25,
  output [28:0] out_26,
  output [28:0] out_27,
  output [28:0] out_28,
  output [28:0] out_29,
  output [28:0] out_30,
  output [28:0] out_31,
  output [28:0] out_32,
  output [28:0] out_33,
  output [28:0] out_34,
  output [28:0] out_35,
  output [28:0] out_36,
  output [28:0] out_37,
  output [28:0] out_38
);

  wire _9_t, _10_t, _11_t, _12, _13, and_1_out, and_2_out, and_3_out, and_4_out, not_1_out;
  wire [28:0] _1_el_str_1, _1_el_str_2, _1_el_str_3, _1_el_str_4, _1_el_str_5, _1_el_str_6, _1_el_str_7,
       _1_el_str_8, _1_el_str_9, _1_el_str_10, _1_el_str_11, _1_el_str_12, _1_el_str_13, _1_el_str_14,
       _1_el_str_15, _1_el_str_16, _1_el_str_17, _1_el_str_18, _1_el_str_19, _1_el_str_20, _1_el_str_21,
       _1_el_str_22, _1_el_str_23, _1_el_str_24, _1_el_str_25, _1_el_str_26, _1_el_str_27, _1_el_str_28,
       _1_el_str_29, _1_el_str_30, _1_el_str_31, _1_el_str_32, _9_el_str_1, _9_el_str_2, _9_el_str_3,
       _9_el_str_4, _9_el_str_5, _9_el_str_6, _9_el_str_7, _9_el_str_8, _9_el_str_9, _9_el_str_10,
       _9_el_str_11, _9_el_str_12, _9_el_str_13, _9_el_str_14, _9_el_str_15, _9_el_str_16, _9_el_str_17,
       _9_el_str_18, _9_el_str_19, _9_el_str_20, _9_el_str_21, _9_el_str_22, _9_el_str_23, _9_el_str_24,
       _9_el_str_25, _9_el_str_26, _9_el_str_27, _9_el_str_28, _9_el_str_29, _9_el_str_30, _9_el_str_31,
       _9_el_str_32, _12_el_str_1, _12_el_str_2, _12_el_str_3, _12_el_str_4, _12_el_str_5, _12_el_str_6,
       _12_el_str_7, _12_el_str_8, _12_el_str_9, _12_el_str_10, _12_el_str_11, _12_el_str_12, _12_el_str_13,
       _12_el_str_14, _12_el_str_15, _12_el_str_16, _12_el_str_17, _12_el_str_18, _12_el_str_19,
       _12_el_str_20, _12_el_str_21, _12_el_str_22, _12_el_str_23, _12_el_str_24, _12_el_str_25,
       _12_el_str_26, _12_el_str_27, _12_el_str_28, _12_el_str_29, _12_el_str_30, _12_el_str_31,
       _12_el_str_32;

  assign _1_el_str_1 = _11_t ? {29{1'b0}} : 29'bz;  // Controlled_Buffer controlled_buffer_1
  assign _1_el_str_2 = _11_t ? {29{1'b0}} : 29'bz;  // Controlled_Buffer controlled_buffer_2
  assign _1_el_str_3 = _11_t ? {29{1'b0}} : 29'bz;  // Controlled_Buffer controlled_buffer_3
  assign _1_el_str_4 = _11_t ? {29{1'b0}} : 29'bz;  // Controlled_Buffer controlled_buffer_4
  assign _1_el_str_5 = _11_t ? {29{1'b0}} : 29'bz;  // Controlled_Buffer controlled_buffer_5
  assign _1_el_str_6 = _11_t ? 29'hff00000 : 29'bz;  // Controlled_Buffer controlled_buffer_6
  assign _1_el_str_7 = _11_t ? 29'hff00000 : 29'bz;  // Controlled_Buffer controlled_buffer_7
  assign _1_el_str_8 = _11_t ? 29'hff00000 : 29'bz;  // Controlled_Buffer controlled_buffer_8
  assign _1_el_str_9 = _11_t ? 29'hff00000 : 29'bz;  // Controlled_Buffer controlled_buffer_9
  assign _1_el_str_10 = _11_t ? 29'hff00000 : 29'bz;  // Controlled_Buffer controlled_buffer_10
  assign _1_el_str_11 = _11_t ? 29'hff00000 : 29'bz;  // Controlled_Buffer controlled_buffer_11
  assign _1_el_str_12 = _11_t ? 29'hff00000 : 29'bz;  // Controlled_Buffer controlled_buffer_12
  assign _1_el_str_13 = _11_t ? 29'hff00000 : 29'bz;  // Controlled_Buffer controlled_buffer_13
  assign _1_el_str_14 = _11_t ? 29'hff00000 : 29'bz;  // Controlled_Buffer controlled_buffer_14
  assign _1_el_str_15 = _11_t ? 29'hff00000 : 29'bz;  // Controlled_Buffer controlled_buffer_15
  assign _1_el_str_16 = _11_t ? 29'hff00000 : 29'bz;  // Controlled_Buffer controlled_buffer_16
  assign _1_el_str_17 = _11_t ? 29'hff00000 : 29'bz;  // Controlled_Buffer controlled_buffer_17
  assign _1_el_str_18 = _11_t ? 29'hff00000 : 29'bz;  // Controlled_Buffer controlled_buffer_18
  assign _1_el_str_19 = _11_t ? 29'hff00000 : 29'bz;  // Controlled_Buffer controlled_buffer_19
  assign _1_el_str_20 = _11_t ? 29'hff00000 : 29'bz;  // Controlled_Buffer controlled_buffer_20
  assign _1_el_str_21 = _11_t ? 29'hff00000 : 29'bz;  // Controlled_Buffer controlled_buffer_21
  assign _1_el_str_22 = _11_t ? 29'hff00000 : 29'bz;  // Controlled_Buffer controlled_buffer_22
  assign _1_el_str_23 = _11_t ? 29'hff00000 : 29'bz;  // Controlled_Buffer controlled_buffer_23
  assign _1_el_str_24 = _11_t ? 29'hff00000 : 29'bz;  // Controlled_Buffer controlled_buffer_24
  assign _1_el_str_25 = _11_t ? {29{1'b0}} : 29'bz;  // Controlled_Buffer controlled_buffer_25
  assign _1_el_str_26 = _11_t ? {29{1'b0}} : 29'bz;  // Controlled_Buffer controlled_buffer_26
  assign _1_el_str_27 = _11_t ? {29{1'b0}} : 29'bz;  // Controlled_Buffer controlled_buffer_27
  assign _1_el_str_28 = _11_t ? {29{1'b0}} : 29'bz;  // Controlled_Buffer controlled_buffer_28
  assign _1_el_str_29 = _11_t ? {29{1'b0}} : 29'bz;  // Controlled_Buffer controlled_buffer_29
  assign _1_el_str_30 = _11_t ? {29{1'b0}} : 29'bz;  // Controlled_Buffer controlled_buffer_30
  assign _1_el_str_31 = _11_t ? {29{1'b0}} : 29'bz;  // Controlled_Buffer controlled_buffer_31
  assign _1_el_str_32 = _11_t ? {29{1'b0}} : 29'bz;  // Controlled_Buffer controlled_buffer_32
  assign _9_el_str_1 = _9_t ? {29{1'b0}} : 29'bz;  // Controlled_Buffer controlled_buffer_33
  assign _9_el_str_2 = _9_t ? {29{1'b0}} : 29'bz;  // Controlled_Buffer controlled_buffer_34
  assign _9_el_str_3 = _9_t ? {29{1'b0}} : 29'bz;  // Controlled_Buffer controlled_buffer_35
  assign _9_el_str_4 = _9_t ? {29{1'b0}} : 29'bz;  // Controlled_Buffer controlled_buffer_36
  assign _9_el_str_5 = _9_t ? {29{1'b0}} : 29'bz;  // Controlled_Buffer controlled_buffer_37
  assign _9_el_str_6 = _9_t ? 29'hc0000 : 29'bz;  // Controlled_Buffer controlled_buffer_38
  assign _9_el_str_7 = _9_t ? 29'hf0000 : 29'bz;  // Controlled_Buffer controlled_buffer_39
  assign _9_el_str_8 = _9_t ? 29'hfc000 : 29'bz;  // Controlled_Buffer controlled_buffer_40
  assign _9_el_str_9 = _9_t ? 29'hff000 : 29'bz;  // Controlled_Buffer controlled_buffer_41
  assign _9_el_str_10 = _9_t ? 29'hff000 : 29'bz;  // Controlled_Buffer controlled_buffer_42
  assign _9_el_str_11 = _9_t ? 29'hff000 : 29'bz;  // Controlled_Buffer controlled_buffer_43
  assign _9_el_str_12 = _9_t ? 29'hff000 : 29'bz;  // Controlled_Buffer controlled_buffer_44
  assign _9_el_str_13 = _9_t ? 29'hff000 : 29'bz;  // Controlled_Buffer controlled_buffer_45
  assign _9_el_str_14 = _9_t ? 29'hff000 : 29'bz;  // Controlled_Buffer controlled_buffer_46
  assign _9_el_str_15 = _9_t ? 29'hff000 : 29'bz;  // Controlled_Buffer controlled_buffer_47
  assign _9_el_str_16 = _9_t ? 29'hff000 : 29'bz;  // Controlled_Buffer controlled_buffer_48
  assign _9_el_str_17 = _9_t ? 29'hff000 : 29'bz;  // Controlled_Buffer controlled_buffer_49
  assign _9_el_str_18 = _9_t ? 29'hff000 : 29'bz;  // Controlled_Buffer controlled_buffer_50
  assign _9_el_str_19 = _9_t ? 29'hff000 : 29'bz;  // Controlled_Buffer controlled_buffer_51
  assign _9_el_str_20 = _9_t ? 29'hfe000 : 29'bz;  // Controlled_Buffer controlled_buffer_52
  assign _9_el_str_21 = _9_t ? 29'hfc000 : 29'bz;  // Controlled_Buffer controlled_buffer_53
  assign _9_el_str_22 = _9_t ? 29'hf0000 : 29'bz;  // Controlled_Buffer controlled_buffer_54
  assign _9_el_str_23 = _9_t ? 29'hc0000 : 29'bz;  // Controlled_Buffer controlled_buffer_55
  assign _9_el_str_24 = _9_t ? 29'h80000 : 29'bz;  // Controlled_Buffer controlled_buffer_56
  assign _9_el_str_25 = _9_t ? {29{1'b0}} : 29'bz;  // Controlled_Buffer controlled_buffer_57
  assign _9_el_str_26 = _9_t ? {29{1'b0}} : 29'bz;  // Controlled_Buffer controlled_buffer_58
  assign _9_el_str_27 = _9_t ? {29{1'b0}} : 29'bz;  // Controlled_Buffer controlled_buffer_59
  assign _9_el_str_28 = _9_t ? {29{1'b0}} : 29'bz;  // Controlled_Buffer controlled_buffer_60
  assign _9_el_str_29 = _9_t ? {29{1'b0}} : 29'bz;  // Controlled_Buffer controlled_buffer_61
  assign _9_el_str_30 = _9_t ? {29{1'b0}} : 29'bz;  // Controlled_Buffer controlled_buffer_62
  assign _9_el_str_31 = _9_t ? {29{1'b0}} : 29'bz;  // Controlled_Buffer controlled_buffer_63
  assign _9_el_str_32 = _9_t ? {29{1'b0}} : 29'bz;  // Controlled_Buffer controlled_buffer_64
  assign _12_el_str_1 = _12 ? {29{1'b0}} : 29'bz;  // Controlled_Buffer controlled_buffer_65
  assign _12_el_str_2 = _12 ? {29{1'b0}} : 29'bz;  // Controlled_Buffer controlled_buffer_66
  assign _12_el_str_3 = _12 ? {29{1'b0}} : 29'bz;  // Controlled_Buffer controlled_buffer_67
  assign _12_el_str_4 = _12 ? {29{1'b0}} : 29'bz;  // Controlled_Buffer controlled_buffer_68
  assign _12_el_str_5 = _12 ? {29{1'b0}} : 29'bz;  // Controlled_Buffer controlled_buffer_69
  assign _12_el_str_6 = _12 ? 29'hfffff : 29'bz;  // Controlled_Buffer controlled_buffer_70
  assign _12_el_str_7 = _12 ? 29'hfffff : 29'bz;  // Controlled_Buffer controlled_buffer_71
  assign _12_el_str_8 = _12 ? 29'hfffff : 29'bz;  // Controlled_Buffer controlled_buffer_72
  assign _12_el_str_9 = _12 ? 29'hfffff : 29'bz;  // Controlled_Buffer controlled_buffer_73
  assign _12_el_str_10 = _12 ? 29'hfffff : 29'bz;  // Controlled_Buffer controlled_buffer_74
  assign _12_el_str_11 = _12 ? 29'hfffff : 29'bz;  // Controlled_Buffer controlled_buffer_75
  assign _12_el_str_12 = _12 ? 29'hfffff : 29'bz;  // Controlled_Buffer controlled_buffer_76
  assign _12_el_str_13 = _12 ? 29'hfffff : 29'bz;  // Controlled_Buffer controlled_buffer_77
  assign _12_el_str_14 = _12 ? 29'hfffff : 29'bz;  // Controlled_Buffer controlled_buffer_78
  assign _12_el_str_15 = _12 ? 29'hfffff : 29'bz;  // Controlled_Buffer controlled_buffer_79
  assign _12_el_str_16 = _12 ? 29'hfffff : 29'bz;  // Controlled_Buffer controlled_buffer_80
  assign _12_el_str_17 = _12 ? 29'hfffff : 29'bz;  // Controlled_Buffer controlled_buffer_81
  assign _12_el_str_18 = _12 ? 29'hfffff : 29'bz;  // Controlled_Buffer controlled_buffer_82
  assign _12_el_str_19 = _12 ? 29'hfffff : 29'bz;  // Controlled_Buffer controlled_buffer_83
  assign _12_el_str_20 = _12 ? 29'hfffff : 29'bz;  // Controlled_Buffer controlled_buffer_84
  assign _12_el_str_21 = _12 ? 29'hfffff : 29'bz;  // Controlled_Buffer controlled_buffer_85
  assign _12_el_str_22 = _12 ? 29'hfffff : 29'bz;  // Controlled_Buffer controlled_buffer_86
  assign _12_el_str_23 = _12 ? 29'hfffff : 29'bz;  // Controlled_Buffer controlled_buffer_87
  assign _12_el_str_24 = _12 ? 29'hfffff : 29'bz;  // Controlled_Buffer controlled_buffer_88
  assign _12_el_str_25 = _12 ? {29{1'b0}} : 29'bz;  // Controlled_Buffer controlled_buffer_89
  assign _12_el_str_26 = _12 ? {29{1'b0}} : 29'bz;  // Controlled_Buffer controlled_buffer_90
  assign _12_el_str_27 = _12 ? {29{1'b0}} : 29'bz;  // Controlled_Buffer controlled_buffer_91
  assign _12_el_str_28 = _12 ? {29{1'b0}} : 29'bz;  // Controlled_Buffer controlled_buffer_92
  assign _12_el_str_29 = _12 ? {29{1'b0}} : 29'bz;  // Controlled_Buffer controlled_buffer_93
  assign _12_el_str_30 = _12 ? {29{1'b0}} : 29'bz;  // Controlled_Buffer controlled_buffer_94
  assign _12_el_str_31 = _12 ? {29{1'b0}} : 29'bz;  // Controlled_Buffer controlled_buffer_95
  assign _12_el_str_32 = _12 ? {29{1'b0}} : 29'bz;  // Controlled_Buffer controlled_buffer_96
  and and_1 (and_1_out, _9, ~_11);  // AND_Gate
  assign _13 = not_1_out ? and_1_out : 1'bz;  // Controlled_Buffer controlled_buffer_97
  assign _12 = not_1_out ? _8 : 1'bz;  // Controlled_Buffer controlled_buffer_98
  and and_2 (and_2_out, _7, ~_10);  // AND_Gate
  assign _11_t = not_1_out ? and_2_out : 1'bz;  // Controlled_Buffer controlled_buffer_99
  assign _10_t = not_1_out ? and_3_out : 1'bz;  // Controlled_Buffer controlled_buffer_100
  and and_3 (and_3_out, _9, ~_8);  // AND_Gate
  and and_4 (and_4_out, _7, ~_8);  // AND_Gate
  assign _9_t = not_1_out ? and_4_out : 1'bz;  // Controlled_Buffer controlled_buffer_101
  not not_1 (not_1_out, isBattle);
  assign _13 = isBattle ? 1'b0 : 1'bz;  // Controlled_Buffer controlled_buffer_102
  assign _12 = isBattle ? 1'b0 : 1'bz;  // Controlled_Buffer controlled_buffer_103
  assign _11_t = isBattle ? 1'b0 : 1'bz;  // Controlled_Buffer controlled_buffer_104
  assign _10_t = isBattle ? 1'b0 : 1'bz;  // Controlled_Buffer controlled_buffer_105
  assign _9_t = isBattle ? 1'b0 : 1'bz;  // Controlled_Buffer controlled_buffer_106
  look_on_minimap look_on_minimap_1 ();
  or_for_str_29_bit or_for_str_29_bit_1 (
    .in_1(_1_el_str_1), .in_2(_9_el_str_1), .in_3(_12_el_str_1), .out_one_str(out_7));  // open: in_4, in_5, in_6, in_7, in_8
  or_for_str_29_bit or_for_str_29_bit_2 (
    .in_1(_1_el_str_2), .in_2(_9_el_str_2), .in_3(_12_el_str_2), .out_one_str(out_8));  // open: in_4, in_5, in_6, in_7, in_8
  or_for_str_29_bit or_for_str_29_bit_3 (
    .in_1(_1_el_str_3), .in_2(_9_el_str_3), .in_3(_12_el_str_3), .out_one_str(out_9));  // open: in_4, in_5, in_6, in_7, in_8
  or_for_str_29_bit or_for_str_29_bit_4 (
    .in_1(_1_el_str_4), .in_2(_9_el_str_4), .in_3(_12_el_str_4), .out_one_str(out_10));  // open: in_4, in_5, in_6, in_7, in_8
  or_for_str_29_bit or_for_str_29_bit_5 (
    .in_1(_1_el_str_5), .in_2(_9_el_str_5), .in_3(_12_el_str_5), .out_one_str(out_11));  // open: in_4, in_5, in_6, in_7, in_8
  or_for_str_29_bit or_for_str_29_bit_6 (
    .in_1(_1_el_str_6), .in_2(_9_el_str_6), .in_3(_12_el_str_6), .out_one_str(out_12));  // open: in_4, in_5, in_6, in_7, in_8
  or_for_str_29_bit or_for_str_29_bit_7 (
    .in_1(_1_el_str_7), .in_2(_9_el_str_7), .in_3(_12_el_str_7), .out_one_str(out_13));  // open: in_4, in_5, in_6, in_7, in_8
  or_for_str_29_bit or_for_str_29_bit_8 (
    .in_1(_1_el_str_8), .in_2(_9_el_str_8), .in_3(_12_el_str_8), .out_one_str(out_14));  // open: in_4, in_5, in_6, in_7, in_8
  or_for_str_29_bit or_for_str_29_bit_9 (
    .in_1(_1_el_str_9), .in_2(_9_el_str_9), .in_3(_12_el_str_9), .out_one_str(out_15));  // open: in_4, in_5, in_6, in_7, in_8
  or_for_str_29_bit or_for_str_29_bit_10 (
    .in_1(_1_el_str_10), .in_2(_9_el_str_10), .in_3(_12_el_str_10), .out_one_str(out_16));  // open: in_4, in_5, in_6, in_7, in_8
  or_for_str_29_bit or_for_str_29_bit_11 (
    .in_1(_1_el_str_11), .in_2(_9_el_str_11), .in_3(_12_el_str_11), .out_one_str(out_17));  // open: in_4, in_5, in_6, in_7, in_8
  or_for_str_29_bit or_for_str_29_bit_12 (
    .in_1(_1_el_str_12), .in_2(_9_el_str_12), .in_3(_12_el_str_12), .out_one_str(out_18));  // open: in_4, in_5, in_6, in_7, in_8
  or_for_str_29_bit or_for_str_29_bit_13 (
    .in_1(_1_el_str_13), .in_2(_9_el_str_13), .in_3(_12_el_str_13), .out_one_str(out_19));  // open: in_4, in_5, in_6, in_7, in_8
  or_for_str_29_bit or_for_str_29_bit_14 (
    .in_1(_1_el_str_14), .in_2(_9_el_str_14), .in_3(_12_el_str_14), .out_one_str(out_20));  // open: in_4, in_5, in_6, in_7, in_8
  or_for_str_29_bit or_for_str_29_bit_15 (
    .in_1(_1_el_str_15), .in_2(_9_el_str_15), .in_3(_12_el_str_15), .out_one_str(out_21));  // open: in_4, in_5, in_6, in_7, in_8
  or_for_str_29_bit or_for_str_29_bit_16 (
    .in_1(_1_el_str_16), .in_2(_9_el_str_16), .in_3(_12_el_str_16), .out_one_str(out_22));  // open: in_4, in_5, in_6, in_7, in_8
  or_for_str_29_bit or_for_str_29_bit_17 (
    .in_1(_1_el_str_17), .in_2(_9_el_str_17), .in_3(_12_el_str_17), .out_one_str(out_23));  // open: in_4, in_5, in_6, in_7, in_8
  or_for_str_29_bit or_for_str_29_bit_18 (
    .in_1(_1_el_str_18), .in_2(_9_el_str_18), .in_3(_12_el_str_18), .out_one_str(out_24));  // open: in_4, in_5, in_6, in_7, in_8
  or_for_str_29_bit or_for_str_29_bit_19 (
    .in_1(_1_el_str_19), .in_2(_9_el_str_19), .in_3(_12_el_str_19), .out_one_str(out_25));  // open: in_4, in_5, in_6, in_7, in_8
  or_for_str_29_bit or_for_str_29_bit_20 (
    .in_1(_1_el_str_20), .in_2(_9_el_str_20), .in_3(_12_el_str_20), .out_one_str(out_26));  // open: in_4, in_5, in_6, in_7, in_8
  or_for_str_29_bit or_for_str_29_bit_21 (
    .in_1(_1_el_str_21), .in_2(_9_el_str_21), .in_3(_12_el_str_21), .out_one_str(out_27));  // open: in_4, in_5, in_6, in_7, in_8
  or_for_str_29_bit or_for_str_29_bit_22 (
    .in_1(_1_el_str_22), .in_2(_9_el_str_22), .in_3(_12_el_str_22), .out_one_str(out_28));  // open: in_4, in_5, in_6, in_7, in_8
  or_for_str_29_bit or_for_str_29_bit_23 (
    .in_1(_1_el_str_23), .in_2(_9_el_str_23), .in_3(_12_el_str_23), .out_one_str(out_29));  // open: in_4, in_5, in_6, in_7, in_8
  or_for_str_29_bit or_for_str_29_bit_24 (
    .in_1(_1_el_str_24), .in_2(_9_el_str_24), .in_3(_12_el_str_24), .out_one_str(out_30));  // open: in_4, in_5, in_6, in_7, in_8
  or_for_str_29_bit or_for_str_29_bit_25 (
    .in_1(_1_el_str_25), .in_2(_9_el_str_25), .in_3(_12_el_str_25), .out_one_str(out_31));  // open: in_4, in_5, in_6, in_7, in_8
  or_for_str_29_bit or_for_str_29_bit_26 (
    .in_1(_1_el_str_26), .in_2(_9_el_str_26), .in_3(_12_el_str_26), .out_one_str(out_32));  // open: in_4, in_5, in_6, in_7, in_8
  or_for_str_29_bit or_for_str_29_bit_27 (
    .in_1(_1_el_str_27), .in_2(_9_el_str_27), .in_3(_12_el_str_27), .out_one_str(out_33));  // open: in_4, in_5, in_6, in_7, in_8
  or_for_str_29_bit or_for_str_29_bit_28 (
    .in_1(_1_el_str_28), .in_2(_9_el_str_28), .in_3(_12_el_str_28), .out_one_str(out_34));  // open: in_4, in_5, in_6, in_7, in_8
  or_for_str_29_bit or_for_str_29_bit_29 (
    .in_1(_1_el_str_29), .in_2(_9_el_str_29), .in_3(_12_el_str_29), .out_one_str(out_35));  // open: in_4, in_5, in_6, in_7, in_8
  or_for_str_29_bit or_for_str_29_bit_30 (
    .in_1(_1_el_str_30), .in_2(_9_el_str_30), .in_3(_12_el_str_30), .out_one_str(out_36));  // open: in_4, in_5, in_6, in_7, in_8
  or_for_str_29_bit or_for_str_29_bit_31 (
    .in_1(_1_el_str_31), .in_2(_9_el_str_31), .in_3(_12_el_str_31), .out_one_str(out_37));  // open: in_4, in_5, in_6, in_7, in_8
  or_for_str_29_bit or_for_str_29_bit_32 (
    .in_1(_1_el_str_32), .in_2(_9_el_str_32), .in_3(_12_el_str_32), .out_one_str(out_38));  // open: in_4, in_5, in_6, in_7, in_8

  // Other names for the same wires on the sheet: str_1[28:0] = out_7; str_2[28:0] = out_8; str_3[28:0] = out_9;
  //   str_4[28:0] = out_10; str_5[28:0] = out_11; str_6[28:0] = out_12; str_7[28:0] = out_13; str_8[28:0] = out_14;
  //   str_9[28:0] = out_15; str_10[28:0] = out_16; str_11[28:0] = out_17; str_12[28:0] = out_18;
  //   str_13[28:0] = out_19; str_14[28:0] = out_20; str_15[28:0] = out_21; str_16[28:0] = out_22;
  //   str_17[28:0] = out_23; str_18[28:0] = out_24; str_19[28:0] = out_25; str_20[28:0] = out_26;
  //   str_21[28:0] = out_27; str_22[28:0] = out_28; str_23[28:0] = out_29; str_24[28:0] = out_30;
  //   str_25[28:0] = out_31; str_26[28:0] = out_32; str_27[28:0] = out_33; str_28[28:0] = out_34;
  //   str_29[28:0] = out_35; str_30[28:0] = out_36; str_31[28:0] = out_37; str_32[28:0] = out_38
endmodule
module Tile_l_3_color (
  input  _11,
  input  _10,
  input  _9,
  input  _8,
  input  _7,
  input  _6,
  input  _5,
  input  _4,
  input  isBattle,
  output [29:0] out_10,
  output [29:0] out_11,
  output [29:0] out_12,
  output [29:0] out_13,
  output [29:0] out_14,
  output [29:0] out_15,
  output [29:0] out_16,
  output [29:0] out_17,
  output [29:0] out_18,
  output [29:0] out_19,
  output [29:0] out_20,
  output [29:0] out_21,
  output [29:0] out_22,
  output [29:0] out_23,
  output [29:0] out_24,
  output [29:0] out_25,
  output [29:0] out_26,
  output [29:0] out_27,
  output [29:0] out_28,
  output [29:0] out_29,
  output [29:0] out_30,
  output [29:0] out_31,
  output [29:0] out_32,
  output [29:0] out_33,
  output [29:0] out_34,
  output [29:0] out_35,
  output [29:0] out_36,
  output [29:0] out_37,
  output [29:0] out_38,
  output [29:0] out_39,
  output [29:0] out_40,
  output [29:0] out_41
);

  wire _4_t, _5_t, _6_t, _7_t, _8_t, and_1_out, and_2_out, and_4_out, and_5_out, and_6_out, and_7_out,
       not_1_out, or_1_out;
  wire [29:0] _1_el_str_1, _1_el_str_2, _1_el_str_3, _1_el_str_4, _1_el_str_5, _1_el_str_6, _1_el_str_7,
       _1_el_str_8, _1_el_str_9, _1_el_str_10, _1_el_str_11, _1_el_str_12, _1_el_str_13, _1_el_str_14,
       _1_el_str_15, _1_el_str_16, _1_el_str_17, _1_el_str_18, _1_el_str_19, _1_el_str_20, _1_el_str_21,
       _1_el_str_22, _1_el_str_23, _1_el_str_24, _1_el_str_25, _1_el_str_26, _1_el_str_27, _1_el_str_28,
       _1_el_str_29, _1_el_str_30, _1_el_str_31, _1_el_str_32, _5_el_str_1, _5_el_str_2, _5_el_str_3,
       _5_el_str_4, _5_el_str_5, _5_el_str_6, _5_el_str_7, _5_el_str_8, _5_el_str_9, _5_el_str_10,
       _5_el_str_11, _5_el_str_12, _5_el_str_13, _5_el_str_14, _5_el_str_15, _5_el_str_16, _5_el_str_17,
       _5_el_str_18, _5_el_str_19, _5_el_str_20, _5_el_str_21, _5_el_str_22, _5_el_str_23, _5_el_str_24,
       _5_el_str_25, _5_el_str_26, _5_el_str_27, _5_el_str_28, _5_el_str_29, _5_el_str_30, _5_el_str_31,
       _5_el_str_32, _7_el_str_1, _7_el_str_2, _7_el_str_3, _7_el_str_4, _7_el_str_5, _7_el_str_6,
       _7_el_str_7, _7_el_str_8, _7_el_str_9, _7_el_str_10, _7_el_str_11, _7_el_str_12, _7_el_str_13,
       _7_el_str_14, _7_el_str_15, _7_el_str_16, _7_el_str_17, _7_el_str_18, _7_el_str_19, _7_el_str_20,
       _7_el_str_21, _7_el_str_22, _7_el_str_23, _7_el_str_24, _7_el_str_25, _7_el_str_26, _7_el_str_27,
       _7_el_str_28, _7_el_str_29, _7_el_str_30, _7_el_str_31, _7_el_str_32;

  assign _1_el_str_1 = _6_t ? {30{1'b0}} : 30'bz;  // Controlled_Buffer controlled_buffer_1
  assign _1_el_str_2 = _6_t ? {30{1'b0}} : 30'bz;  // Controlled_Buffer controlled_buffer_2
  assign _1_el_str_3 = _6_t ? {30{1'b0}} : 30'bz;  // Controlled_Buffer controlled_buffer_3
  assign _1_el_str_4 = _6_t ? {30{1'b0}} : 30'bz;  // Controlled_Buffer controlled_buffer_4
  assign _1_el_str_5 = _6_t ? {30{1'b0}} : 30'bz;  // Controlled_Buffer controlled_buffer_5
  assign _1_el_str_6 = _6_t ? {30{1'b0}} : 30'bz;  // Controlled_Buffer controlled_buffer_6
  assign _1_el_str_7 = _6_t ? {30{1'b0}} : 30'bz;  // Controlled_Buffer controlled_buffer_7
  assign _1_el_str_8 = _6_t ? {30{1'b0}} : 30'bz;  // Controlled_Buffer controlled_buffer_8
  assign _1_el_str_9 = _6_t ? 30'hff000 : 30'bz;  // Controlled_Buffer controlled_buffer_9
  assign _1_el_str_10 = _6_t ? 30'hff000 : 30'bz;  // Controlled_Buffer controlled_buffer_10
  assign _1_el_str_11 = _6_t ? 30'hff000 : 30'bz;  // Controlled_Buffer controlled_buffer_11
  assign _1_el_str_12 = _6_t ? 30'hff000 : 30'bz;  // Controlled_Buffer controlled_buffer_12
  assign _1_el_str_13 = _6_t ? 30'hff000 : 30'bz;  // Controlled_Buffer controlled_buffer_13
  assign _1_el_str_14 = _6_t ? 30'hff000 : 30'bz;  // Controlled_Buffer controlled_buffer_14
  assign _1_el_str_15 = _6_t ? 30'hff000 : 30'bz;  // Controlled_Buffer controlled_buffer_15
  assign _1_el_str_16 = _6_t ? 30'hff000 : 30'bz;  // Controlled_Buffer controlled_buffer_16
  assign _1_el_str_17 = _6_t ? 30'hff000 : 30'bz;  // Controlled_Buffer controlled_buffer_17
  assign _1_el_str_18 = _6_t ? 30'hff000 : 30'bz;  // Controlled_Buffer controlled_buffer_18
  assign _1_el_str_19 = _6_t ? 30'hff000 : 30'bz;  // Controlled_Buffer controlled_buffer_19
  assign _1_el_str_20 = _6_t ? {30{1'b0}} : 30'bz;  // Controlled_Buffer controlled_buffer_20
  assign _1_el_str_21 = _6_t ? {30{1'b0}} : 30'bz;  // Controlled_Buffer controlled_buffer_21
  assign _1_el_str_22 = _6_t ? {30{1'b0}} : 30'bz;  // Controlled_Buffer controlled_buffer_22
  assign _1_el_str_23 = _6_t ? {30{1'b0}} : 30'bz;  // Controlled_Buffer controlled_buffer_23
  assign _1_el_str_24 = _6_t ? {30{1'b0}} : 30'bz;  // Controlled_Buffer controlled_buffer_24
  assign _1_el_str_25 = _6_t ? {30{1'b0}} : 30'bz;  // Controlled_Buffer controlled_buffer_25
  assign _1_el_str_26 = _6_t ? {30{1'b0}} : 30'bz;  // Controlled_Buffer controlled_buffer_26
  assign _1_el_str_27 = _6_t ? {30{1'b0}} : 30'bz;  // Controlled_Buffer controlled_buffer_27
  assign _1_el_str_28 = _6_t ? {30{1'b0}} : 30'bz;  // Controlled_Buffer controlled_buffer_28
  assign _1_el_str_29 = _6_t ? {30{1'b0}} : 30'bz;  // Controlled_Buffer controlled_buffer_29
  assign _1_el_str_30 = _6_t ? {30{1'b0}} : 30'bz;  // Controlled_Buffer controlled_buffer_30
  assign _1_el_str_31 = _6_t ? {30{1'b0}} : 30'bz;  // Controlled_Buffer controlled_buffer_31
  assign _1_el_str_32 = _6_t ? {30{1'b0}} : 30'bz;  // Controlled_Buffer controlled_buffer_32
  assign _7_el_str_1 = _4_t ? {30{1'b0}} : 30'bz;  // Controlled_Buffer controlled_buffer_33
  assign _7_el_str_2 = _4_t ? {30{1'b0}} : 30'bz;  // Controlled_Buffer controlled_buffer_34
  assign _7_el_str_3 = _4_t ? {30{1'b0}} : 30'bz;  // Controlled_Buffer controlled_buffer_35
  assign _7_el_str_4 = _4_t ? {30{1'b0}} : 30'bz;  // Controlled_Buffer controlled_buffer_36
  assign _7_el_str_5 = _4_t ? {30{1'b0}} : 30'bz;  // Controlled_Buffer controlled_buffer_37
  assign _7_el_str_6 = _4_t ? {30{1'b0}} : 30'bz;  // Controlled_Buffer controlled_buffer_38
  assign _7_el_str_7 = _4_t ? {30{1'b0}} : 30'bz;  // Controlled_Buffer controlled_buffer_39
  assign _7_el_str_8 = _4_t ? {30{1'b0}} : 30'bz;  // Controlled_Buffer controlled_buffer_40
  assign _7_el_str_9 = _4_t ? 30'hc00 : 30'bz;  // Controlled_Buffer controlled_buffer_41
  assign _7_el_str_10 = _4_t ? 30'hf80 : 30'bz;  // Controlled_Buffer controlled_buffer_42
  assign _7_el_str_11 = _4_t ? 30'hfe0 : 30'bz;  // Controlled_Buffer controlled_buffer_43
  assign _7_el_str_12 = _4_t ? 30'hfe0 : 30'bz;  // Controlled_Buffer controlled_buffer_44
  assign _7_el_str_13 = _4_t ? 30'hfe0 : 30'bz;  // Controlled_Buffer controlled_buffer_45
  assign _7_el_str_14 = _4_t ? 30'hfe0 : 30'bz;  // Controlled_Buffer controlled_buffer_46
  assign _7_el_str_15 = _4_t ? 30'hfe0 : 30'bz;  // Controlled_Buffer controlled_buffer_47
  assign _7_el_str_16 = _4_t ? 30'hfe0 : 30'bz;  // Controlled_Buffer controlled_buffer_48
  assign _7_el_str_17 = _4_t ? 30'hfe0 : 30'bz;  // Controlled_Buffer controlled_buffer_49
  assign _7_el_str_18 = _4_t ? 30'hf80 : 30'bz;  // Controlled_Buffer controlled_buffer_50
  assign _7_el_str_19 = _4_t ? 30'hc00 : 30'bz;  // Controlled_Buffer controlled_buffer_51
  assign _7_el_str_20 = _4_t ? {30{1'b0}} : 30'bz;  // Controlled_Buffer controlled_buffer_52
  assign _7_el_str_21 = _4_t ? {30{1'b0}} : 30'bz;  // Controlled_Buffer controlled_buffer_53
  assign _7_el_str_22 = _4_t ? {30{1'b0}} : 30'bz;  // Controlled_Buffer controlled_buffer_54
  assign _7_el_str_23 = _4_t ? {30{1'b0}} : 30'bz;  // Controlled_Buffer controlled_buffer_55
  assign _7_el_str_24 = _4_t ? {30{1'b0}} : 30'bz;  // Controlled_Buffer controlled_buffer_56
  assign _7_el_str_25 = _4_t ? {30{1'b0}} : 30'bz;  // Controlled_Buffer controlled_buffer_57
  assign _7_el_str_26 = _4_t ? {30{1'b0}} : 30'bz;  // Controlled_Buffer controlled_buffer_58
  assign _7_el_str_27 = _4_t ? {30{1'b0}} : 30'bz;  // Controlled_Buffer controlled_buffer_59
  assign _7_el_str_28 = _4_t ? {30{1'b0}} : 30'bz;  // Controlled_Buffer controlled_buffer_60
  assign _7_el_str_29 = _4_t ? {30{1'b0}} : 30'bz;  // Controlled_Buffer controlled_buffer_61
  assign _7_el_str_30 = _4_t ? {30{1'b0}} : 30'bz;  // Controlled_Buffer controlled_buffer_62
  assign _7_el_str_31 = _4_t ? {30{1'b0}} : 30'bz;  // Controlled_Buffer controlled_buffer_63
  assign _7_el_str_32 = _4_t ? {30{1'b0}} : 30'bz;  // Controlled_Buffer controlled_buffer_64
  and and_1 (and_1_out, _6, ~_11, ~_9);  // AND_Gate
  and and_2 (and_2_out, _11, ~_9, ~_8, _6);  // AND_Gate
  // AND_Gate and_3 has open pins: in0=_4, in1=_7, in2=_10, out=open
  and and_4 (and_4_out, ~_7, ~_8, _4);  // AND_Gate
  or or_1 (or_1_out, and_1_out, and_2_out);
  assign _5_el_str_1 = _7_t ? {30{1'b0}} : 30'bz;  // Controlled_Buffer controlled_buffer_65
  assign _5_el_str_2 = _7_t ? {30{1'b0}} : 30'bz;  // Controlled_Buffer controlled_buffer_66
  assign _5_el_str_3 = _7_t ? {30{1'b0}} : 30'bz;  // Controlled_Buffer controlled_buffer_67
  assign _5_el_str_4 = _7_t ? {30{1'b0}} : 30'bz;  // Controlled_Buffer controlled_buffer_68
  assign _5_el_str_5 = _7_t ? {30{1'b0}} : 30'bz;  // Controlled_Buffer controlled_buffer_69
  assign _5_el_str_6 = _7_t ? {30{1'b0}} : 30'bz;  // Controlled_Buffer controlled_buffer_70
  assign _5_el_str_7 = _7_t ? {30{1'b0}} : 30'bz;  // Controlled_Buffer controlled_buffer_71
  assign _5_el_str_8 = _7_t ? {30{1'b0}} : 30'bz;  // Controlled_Buffer controlled_buffer_72
  assign _5_el_str_9 = _7_t ? 30'hfff : 30'bz;  // Controlled_Buffer controlled_buffer_73
  assign _5_el_str_10 = _7_t ? 30'hfff : 30'bz;  // Controlled_Buffer controlled_buffer_74
  assign _5_el_str_11 = _7_t ? 30'hfff : 30'bz;  // Controlled_Buffer controlled_buffer_75
  assign _5_el_str_12 = _7_t ? 30'hfff : 30'bz;  // Controlled_Buffer controlled_buffer_76
  assign _5_el_str_13 = _7_t ? 30'hfff : 30'bz;  // Controlled_Buffer controlled_buffer_77
  assign _5_el_str_14 = _7_t ? 30'hfff : 30'bz;  // Controlled_Buffer controlled_buffer_78
  assign _5_el_str_15 = _7_t ? 30'hfff : 30'bz;  // Controlled_Buffer controlled_buffer_79
  assign _5_el_str_16 = _7_t ? 30'hfff : 30'bz;  // Controlled_Buffer controlled_buffer_80
  assign _5_el_str_17 = _7_t ? 30'hfff : 30'bz;  // Controlled_Buffer controlled_buffer_81
  assign _5_el_str_18 = _7_t ? 30'hfff : 30'bz;  // Controlled_Buffer controlled_buffer_82
  assign _5_el_str_19 = _7_t ? 30'hfff : 30'bz;  // Controlled_Buffer controlled_buffer_83
  assign _5_el_str_20 = _7_t ? {30{1'b0}} : 30'bz;  // Controlled_Buffer controlled_buffer_84
  assign _5_el_str_21 = _7_t ? {30{1'b0}} : 30'bz;  // Controlled_Buffer controlled_buffer_85
  assign _5_el_str_22 = _7_t ? {30{1'b0}} : 30'bz;  // Controlled_Buffer controlled_buffer_86
  assign _5_el_str_23 = _7_t ? {30{1'b0}} : 30'bz;  // Controlled_Buffer controlled_buffer_87
  assign _5_el_str_24 = _7_t ? {30{1'b0}} : 30'bz;  // Controlled_Buffer controlled_buffer_88
  assign _5_el_str_25 = _7_t ? {30{1'b0}} : 30'bz;  // Controlled_Buffer controlled_buffer_89
  assign _5_el_str_26 = _7_t ? {30{1'b0}} : 30'bz;  // Controlled_Buffer controlled_buffer_90
  assign _5_el_str_27 = _7_t ? {30{1'b0}} : 30'bz;  // Controlled_Buffer controlled_buffer_91
  assign _5_el_str_28 = _7_t ? {30{1'b0}} : 30'bz;  // Controlled_Buffer controlled_buffer_92
  assign _5_el_str_29 = _7_t ? {30{1'b0}} : 30'bz;  // Controlled_Buffer controlled_buffer_93
  assign _5_el_str_30 = _7_t ? {30{1'b0}} : 30'bz;  // Controlled_Buffer controlled_buffer_94
  assign _5_el_str_31 = _7_t ? {30{1'b0}} : 30'bz;  // Controlled_Buffer controlled_buffer_95
  assign _5_el_str_32 = _7_t ? {30{1'b0}} : 30'bz;  // Controlled_Buffer controlled_buffer_96
  assign _8_t = not_1_out ? or_1_out : 1'bz;  // Controlled_Buffer controlled_buffer_97
  and and_5 (and_5_out, ~_8, _5);  // AND_Gate
  assign _7_t = not_1_out ? and_5_out : 1'bz;  // Controlled_Buffer controlled_buffer_98
  assign _6_t = not_1_out ? and_4_out : 1'bz;  // Controlled_Buffer controlled_buffer_99
  assign _5_t = not_1_out ? and_6_out : 1'bz;  // Controlled_Buffer controlled_buffer_100
  and and_6 (and_6_out, _6, ~_8, ~_5);  // AND_Gate
  assign _4_t = not_1_out ? and_7_out : 1'bz;  // Controlled_Buffer controlled_buffer_101
  and and_7 (and_7_out, _4, ~_8, ~_5);  // AND_Gate
  not not_1 (not_1_out, isBattle);
  assign _8_t = isBattle ? 1'b0 : 1'bz;  // Controlled_Buffer controlled_buffer_102
  assign _7_t = isBattle ? 1'b0 : 1'bz;  // Controlled_Buffer controlled_buffer_103
  assign _6_t = isBattle ? 1'b0 : 1'bz;  // Controlled_Buffer controlled_buffer_104
  assign _5_t = isBattle ? 1'b0 : 1'bz;  // Controlled_Buffer controlled_buffer_105
  assign _4_t = isBattle ? 1'b0 : 1'bz;  // Controlled_Buffer controlled_buffer_106
  or_for_str_30_bit or_for_str_30_bit_1 (
    .in_1(_1_el_str_1), .in_2(_7_el_str_1), .in_3(_5_el_str_1), .out_one_str(out_10));  // open: in_4, in_5, in_6, in_7, in_8
  or_for_str_30_bit or_for_str_30_bit_2 (
    .in_1(_1_el_str_2), .in_2(_7_el_str_2), .in_3(_5_el_str_2), .out_one_str(out_11));  // open: in_4, in_5, in_6, in_7, in_8
  or_for_str_30_bit or_for_str_30_bit_3 (
    .in_1(_1_el_str_3), .in_2(_7_el_str_3), .in_3(_5_el_str_3), .out_one_str(out_12));  // open: in_4, in_5, in_6, in_7, in_8
  or_for_str_30_bit or_for_str_30_bit_4 (
    .in_1(_1_el_str_4), .in_2(_7_el_str_4), .in_3(_5_el_str_4), .out_one_str(out_13));  // open: in_4, in_5, in_6, in_7, in_8
  or_for_str_30_bit or_for_str_30_bit_5 (
    .in_1(_1_el_str_5), .in_2(_7_el_str_5), .in_3(_5_el_str_5), .out_one_str(out_14));  // open: in_4, in_5, in_6, in_7, in_8
  or_for_str_30_bit or_for_str_30_bit_6 (
    .in_1(_1_el_str_6), .in_2(_7_el_str_6), .in_3(_5_el_str_6), .out_one_str(out_15));  // open: in_4, in_5, in_6, in_7, in_8
  or_for_str_30_bit or_for_str_30_bit_7 (
    .in_1(_1_el_str_7), .in_2(_7_el_str_7), .in_3(_5_el_str_7), .out_one_str(out_16));  // open: in_4, in_5, in_6, in_7, in_8
  or_for_str_30_bit or_for_str_30_bit_8 (
    .in_1(_1_el_str_8), .in_2(_7_el_str_8), .in_3(_5_el_str_8), .out_one_str(out_17));  // open: in_4, in_5, in_6, in_7, in_8
  or_for_str_30_bit or_for_str_30_bit_9 (
    .in_1(_1_el_str_9), .in_2(_7_el_str_9), .in_3(_5_el_str_9), .out_one_str(out_18));  // open: in_4, in_5, in_6, in_7, in_8
  or_for_str_30_bit or_for_str_30_bit_10 (
    .in_1(_1_el_str_10), .in_2(_7_el_str_10), .in_3(_5_el_str_10), .out_one_str(out_19));  // open: in_4, in_5, in_6, in_7, in_8
  or_for_str_30_bit or_for_str_30_bit_11 (
    .in_1(_1_el_str_11), .in_2(_7_el_str_11), .in_3(_5_el_str_11), .out_one_str(out_20));  // open: in_4, in_5, in_6, in_7, in_8
  or_for_str_30_bit or_for_str_30_bit_12 (
    .in_1(_1_el_str_12), .in_2(_7_el_str_12), .in_3(_5_el_str_12), .out_one_str(out_21));  // open: in_4, in_5, in_6, in_7, in_8
  or_for_str_30_bit or_for_str_30_bit_13 (
    .in_1(_1_el_str_13), .in_2(_7_el_str_13), .in_3(_5_el_str_13), .out_one_str(out_22));  // open: in_4, in_5, in_6, in_7, in_8
  or_for_str_30_bit or_for_str_30_bit_14 (
    .in_1(_1_el_str_14), .in_2(_7_el_str_14), .in_3(_5_el_str_14), .out_one_str(out_23));  // open: in_4, in_5, in_6, in_7, in_8
  or_for_str_30_bit or_for_str_30_bit_15 (
    .in_1(_1_el_str_15), .in_2(_7_el_str_15), .in_3(_5_el_str_15), .out_one_str(out_24));  // open: in_4, in_5, in_6, in_7, in_8
  or_for_str_30_bit or_for_str_30_bit_16 (
    .in_1(_1_el_str_16), .in_2(_7_el_str_16), .in_3(_5_el_str_16), .out_one_str(out_25));  // open: in_4, in_5, in_6, in_7, in_8
  or_for_str_30_bit or_for_str_30_bit_17 (
    .in_1(_1_el_str_17), .in_2(_7_el_str_17), .in_3(_5_el_str_17), .out_one_str(out_26));  // open: in_4, in_5, in_6, in_7, in_8
  or_for_str_30_bit or_for_str_30_bit_18 (
    .in_1(_1_el_str_18), .in_2(_7_el_str_18), .in_3(_5_el_str_18), .out_one_str(out_27));  // open: in_4, in_5, in_6, in_7, in_8
  or_for_str_30_bit or_for_str_30_bit_19 (
    .in_1(_1_el_str_19), .in_2(_7_el_str_19), .in_3(_5_el_str_19), .out_one_str(out_28));  // open: in_4, in_5, in_6, in_7, in_8
  or_for_str_30_bit or_for_str_30_bit_20 (
    .in_1(_1_el_str_20), .in_2(_7_el_str_20), .in_3(_5_el_str_20), .out_one_str(out_29));  // open: in_4, in_5, in_6, in_7, in_8
  or_for_str_30_bit or_for_str_30_bit_21 (
    .in_1(_1_el_str_21), .in_2(_7_el_str_21), .in_3(_5_el_str_21), .out_one_str(out_30));  // open: in_4, in_5, in_6, in_7, in_8
  or_for_str_30_bit or_for_str_30_bit_22 (
    .in_1(_1_el_str_22), .in_2(_7_el_str_22), .in_3(_5_el_str_22), .out_one_str(out_31));  // open: in_4, in_5, in_6, in_7, in_8
  or_for_str_30_bit or_for_str_30_bit_23 (
    .in_1(_1_el_str_23), .in_2(_7_el_str_23), .in_3(_5_el_str_23), .out_one_str(out_32));  // open: in_4, in_5, in_6, in_7, in_8
  or_for_str_30_bit or_for_str_30_bit_24 (
    .in_1(_1_el_str_24), .in_2(_7_el_str_24), .in_3(_5_el_str_24), .out_one_str(out_33));  // open: in_4, in_5, in_6, in_7, in_8
  or_for_str_30_bit or_for_str_30_bit_25 (
    .in_1(_1_el_str_25), .in_2(_7_el_str_25), .in_3(_5_el_str_25), .out_one_str(out_34));  // open: in_4, in_5, in_6, in_7, in_8
  or_for_str_30_bit or_for_str_30_bit_26 (
    .in_1(_1_el_str_26), .in_2(_7_el_str_26), .in_3(_5_el_str_26), .out_one_str(out_35));  // open: in_4, in_5, in_6, in_7, in_8
  or_for_str_30_bit or_for_str_30_bit_27 (
    .in_1(_1_el_str_27), .in_2(_7_el_str_27), .in_3(_5_el_str_27), .out_one_str(out_36));  // open: in_4, in_5, in_6, in_7, in_8
  or_for_str_30_bit or_for_str_30_bit_28 (
    .in_1(_1_el_str_28), .in_2(_7_el_str_28), .in_3(_5_el_str_28), .out_one_str(out_37));  // open: in_4, in_5, in_6, in_7, in_8
  or_for_str_30_bit or_for_str_30_bit_29 (
    .in_1(_1_el_str_29), .in_2(_7_el_str_29), .in_3(_5_el_str_29), .out_one_str(out_38));  // open: in_4, in_5, in_6, in_7, in_8
  or_for_str_30_bit or_for_str_30_bit_30 (
    .in_1(_1_el_str_30), .in_2(_7_el_str_30), .in_3(_5_el_str_30), .out_one_str(out_39));  // open: in_4, in_5, in_6, in_7, in_8
  or_for_str_30_bit or_for_str_30_bit_31 (
    .in_1(_1_el_str_31), .in_2(_7_el_str_31), .in_3(_5_el_str_31), .out_one_str(out_40));  // open: in_4, in_5, in_6, in_7, in_8
  or_for_str_30_bit or_for_str_30_bit_32 (
    .in_1(_1_el_str_32), .in_2(_7_el_str_32), .in_3(_5_el_str_32), .out_one_str(out_41));  // open: in_4, in_5, in_6, in_7, in_8

  // Other names for the same wires on the sheet: str_1[29:0] = out_10; str_2[29:0] = out_11; str_3[29:0] = out_12;
  //   str_4[29:0] = out_13; str_5[29:0] = out_14; str_6[29:0] = out_15; str_7[29:0] = out_16; str_8[29:0] = out_17;
  //   str_9[29:0] = out_18; str_10[29:0] = out_19; str_11[29:0] = out_20; str_12[29:0] = out_21;
  //   str_13[29:0] = out_22; str_14[29:0] = out_23; str_15[29:0] = out_24; str_16[29:0] = out_25;
  //   str_17[29:0] = out_26; str_18[29:0] = out_27; str_19[29:0] = out_28; str_20[29:0] = out_29;
  //   str_21[29:0] = out_30; str_22[29:0] = out_31; str_23[29:0] = out_32; str_24[29:0] = out_33;
  //   str_25[29:0] = out_34; str_26[29:0] = out_35; str_27[29:0] = out_36; str_28[29:0] = out_37;
  //   str_29[29:0] = out_38; str_30[29:0] = out_39; str_31[29:0] = out_40; str_32[29:0] = out_41

  // Notes on the sheet:
  //   6 -> 1
  //   4 -> 7
  //   7 -> 5
endmodule

module Tile_l_4_color (
  input  _8,
  input  _6,
  input  _5,
  input  _4,
  input  _3,
  input  _2,
  input  _1,
  input  [1:0] enemy,
  input  [1:0] gameState,
  output [30:0] out_10,
  output [30:0] out_11,
  output [30:0] out_12,
  output [30:0] out_13,
  output [30:0] out_14,
  output [30:0] out_15,
  output [30:0] out_16,
  output [30:0] out_17,
  output [30:0] out_18,
  output [30:0] out_19,
  output [30:0] out_20,
  output [30:0] out_21,
  output [30:0] out_22,
  output [30:0] out_23,
  output [30:0] out_24,
  output [30:0] out_25,
  output [30:0] out_26,
  output [30:0] out_27,
  output [30:0] out_28,
  output [30:0] out_29,
  output [30:0] out_30,
  output [30:0] out_31,
  output [30:0] out_32,
  output [30:0] out_33,
  output [30:0] out_34,
  output [30:0] out_35,
  output [30:0] out_36,
  output [30:0] out_37,
  output [30:0] out_38,
  output [30:0] out_39,
  output [30:0] out_40,
  output [30:0] out_41
);

  wire _1_t, _2_t, _3_t, and_1_out, and_2_out, and_3_out, isBattle, not_1_out;
  wire [30:0] _1_el_str_1, _1_el_str_2, _1_el_str_3, _1_el_str_4, _1_el_str_5, _1_el_str_6, _1_el_str_7,
       _1_el_str_8, _1_el_str_9, _1_el_str_10, _1_el_str_11, _1_el_str_12, _1_el_str_13, _1_el_str_14,
       _1_el_str_15, _1_el_str_16, _1_el_str_17, _1_el_str_18, _1_el_str_19, _1_el_str_20, _1_el_str_21,
       _1_el_str_22, _1_el_str_23, _1_el_str_24, _1_el_str_25, _1_el_str_26, _1_el_str_27, _1_el_str_28,
       _1_el_str_29, _1_el_str_30, _1_el_str_31, _1_el_str_32, _7_el_str_1, _7_el_str_2, _7_el_str_3,
       _7_el_str_4, _7_el_str_5, _7_el_str_6, _7_el_str_7, _7_el_str_8, _7_el_str_9, _7_el_str_10,
       _7_el_str_11, _7_el_str_12, _7_el_str_13, _7_el_str_14, _7_el_str_15, _7_el_str_16, _7_el_str_17,
       _7_el_str_18, _7_el_str_19, _7_el_str_20, _7_el_str_21, _7_el_str_22, _7_el_str_23, _7_el_str_24,
       _7_el_str_25, _7_el_str_26, _7_el_str_27, _7_el_str_28, _7_el_str_29, _7_el_str_30, _7_el_str_31,
       _7_el_str_32, mole_str_1, mole_str_2, mole_str_3, mole_str_4, mole_str_5, mole_str_6, mole_str_7,
       mole_str_8, mole_str_9, mole_str_10, mole_str_11, mole_str_12, mole_str_13, mole_str_14, mole_str_15,
       mole_str_16, mole_str_17, mole_str_18, mole_str_19, mole_str_20, mole_str_21, mole_str_22,
       mole_str_23, mole_str_24, mole_str_25, mole_str_26, mole_str_27, mole_str_28, mole_str_29,
       mole_str_30, mole_str_31, mole_str_32;

  assign _1_el_str_1 = _1_t ? {31{1'b0}} : 31'bz;  // Controlled_Buffer controlled_buffer_1
  assign _1_el_str_2 = _1_t ? {31{1'b0}} : 31'bz;  // Controlled_Buffer controlled_buffer_2
  assign _1_el_str_3 = _1_t ? {31{1'b0}} : 31'bz;  // Controlled_Buffer controlled_buffer_3
  assign _1_el_str_4 = _1_t ? {31{1'b0}} : 31'bz;  // Controlled_Buffer controlled_buffer_4
  assign _1_el_str_5 = _1_t ? {31{1'b0}} : 31'bz;  // Controlled_Buffer controlled_buffer_5
  assign _1_el_str_6 = _1_t ? {31{1'b0}} : 31'bz;  // Controlled_Buffer controlled_buffer_6
  assign _1_el_str_7 = _1_t ? {31{1'b0}} : 31'bz;  // Controlled_Buffer controlled_buffer_7
  assign _1_el_str_8 = _1_t ? {31{1'b0}} : 31'bz;  // Controlled_Buffer controlled_buffer_8
  assign _1_el_str_9 = _1_t ? {31{1'b0}} : 31'bz;  // Controlled_Buffer controlled_buffer_9
  assign _1_el_str_10 = _1_t ? {31{1'b0}} : 31'bz;  // Controlled_Buffer controlled_buffer_10
  assign _1_el_str_11 = _1_t ? 31'hfe0 : 31'bz;  // Controlled_Buffer controlled_buffer_11
  assign _1_el_str_12 = _1_t ? 31'hfe0 : 31'bz;  // Controlled_Buffer controlled_buffer_12
  assign _1_el_str_13 = _1_t ? 31'hfe0 : 31'bz;  // Controlled_Buffer controlled_buffer_13
  assign _1_el_str_14 = _1_t ? 31'hfe0 : 31'bz;  // Controlled_Buffer controlled_buffer_14
  assign _1_el_str_15 = _1_t ? 31'hfe0 : 31'bz;  // Controlled_Buffer controlled_buffer_15
  assign _1_el_str_16 = _1_t ? 31'hfe0 : 31'bz;  // Controlled_Buffer controlled_buffer_16
  assign _1_el_str_17 = _1_t ? 31'hfe0 : 31'bz;  // Controlled_Buffer controlled_buffer_17
  assign _1_el_str_18 = _1_t ? {31{1'b0}} : 31'bz;  // Controlled_Buffer controlled_buffer_18
  assign _1_el_str_19 = _1_t ? {31{1'b0}} : 31'bz;  // Controlled_Buffer controlled_buffer_19
  assign _1_el_str_20 = _1_t ? {31{1'b0}} : 31'bz;  // Controlled_Buffer controlled_buffer_20
  assign _1_el_str_21 = _1_t ? {31{1'b0}} : 31'bz;  // Controlled_Buffer controlled_buffer_21
  assign _1_el_str_22 = _1_t ? {31{1'b0}} : 31'bz;  // Controlled_Buffer controlled_buffer_22
  assign _1_el_str_23 = _1_t ? {31{1'b0}} : 31'bz;  // Controlled_Buffer controlled_buffer_23
  assign _1_el_str_24 = _1_t ? {31{1'b0}} : 31'bz;  // Controlled_Buffer controlled_buffer_24
  assign _1_el_str_25 = _1_t ? {31{1'b0}} : 31'bz;  // Controlled_Buffer controlled_buffer_25
  assign _1_el_str_26 = _1_t ? {31{1'b0}} : 31'bz;  // Controlled_Buffer controlled_buffer_26
  assign _1_el_str_27 = _1_t ? {31{1'b0}} : 31'bz;  // Controlled_Buffer controlled_buffer_27
  assign _1_el_str_28 = _1_t ? {31{1'b0}} : 31'bz;  // Controlled_Buffer controlled_buffer_28
  assign _1_el_str_29 = _1_t ? {31{1'b0}} : 31'bz;  // Controlled_Buffer controlled_buffer_29
  assign _1_el_str_30 = _1_t ? {31{1'b0}} : 31'bz;  // Controlled_Buffer controlled_buffer_30
  assign _1_el_str_31 = _1_t ? {31{1'b0}} : 31'bz;  // Controlled_Buffer controlled_buffer_31
  assign _1_el_str_32 = _1_t ? {31{1'b0}} : 31'bz;  // Controlled_Buffer controlled_buffer_32
  assign _7_el_str_1 = _2_t ? {31{1'b0}} : 31'bz;  // Controlled_Buffer controlled_buffer_33
  assign _7_el_str_2 = _2_t ? {31{1'b0}} : 31'bz;  // Controlled_Buffer controlled_buffer_34
  assign _7_el_str_3 = _2_t ? {31{1'b0}} : 31'bz;  // Controlled_Buffer controlled_buffer_35
  assign _7_el_str_4 = _2_t ? {31{1'b0}} : 31'bz;  // Controlled_Buffer controlled_buffer_36
  assign _7_el_str_5 = _2_t ? {31{1'b0}} : 31'bz;  // Controlled_Buffer controlled_buffer_37
  assign _7_el_str_6 = _2_t ? {31{1'b0}} : 31'bz;  // Controlled_Buffer controlled_buffer_38
  assign _7_el_str_7 = _2_t ? {31{1'b0}} : 31'bz;  // Controlled_Buffer controlled_buffer_39
  assign _7_el_str_8 = _2_t ? {31{1'b0}} : 31'bz;  // Controlled_Buffer controlled_buffer_40
  assign _7_el_str_9 = _2_t ? {31{1'b0}} : 31'bz;  // Controlled_Buffer controlled_buffer_41
  assign _7_el_str_10 = _2_t ? {31{1'b0}} : 31'bz;  // Controlled_Buffer controlled_buffer_42
  assign _7_el_str_11 = _2_t ? 31'h1f : 31'bz;  // Controlled_Buffer controlled_buffer_43
  assign _7_el_str_12 = _2_t ? 31'h1f : 31'bz;  // Controlled_Buffer controlled_buffer_44
  assign _7_el_str_13 = _2_t ? 31'h1f : 31'bz;  // Controlled_Buffer controlled_buffer_45
  assign _7_el_str_14 = _2_t ? 31'h1f : 31'bz;  // Controlled_Buffer controlled_buffer_46
  assign _7_el_str_15 = _2_t ? 31'h1f : 31'bz;  // Controlled_Buffer controlled_buffer_47
  assign _7_el_str_16 = _2_t ? 31'h1f : 31'bz;  // Controlled_Buffer controlled_buffer_48
  assign _7_el_str_17 = _2_t ? 31'h1f : 31'bz;  // Controlled_Buffer controlled_buffer_49
  assign _7_el_str_18 = _2_t ? {31{1'b0}} : 31'bz;  // Controlled_Buffer controlled_buffer_50
  assign _7_el_str_19 = _2_t ? {31{1'b0}} : 31'bz;  // Controlled_Buffer controlled_buffer_51
  assign _7_el_str_20 = _2_t ? {31{1'b0}} : 31'bz;  // Controlled_Buffer controlled_buffer_52
  assign _7_el_str_21 = _2_t ? {31{1'b0}} : 31'bz;  // Controlled_Buffer controlled_buffer_53
  assign _7_el_str_22 = _2_t ? {31{1'b0}} : 31'bz;  // Controlled_Buffer controlled_buffer_54
  assign _7_el_str_23 = _2_t ? {31{1'b0}} : 31'bz;  // Controlled_Buffer controlled_buffer_55
  assign _7_el_str_24 = _2_t ? {31{1'b0}} : 31'bz;  // Controlled_Buffer controlled_buffer_56
  assign _7_el_str_25 = _2_t ? {31{1'b0}} : 31'bz;  // Controlled_Buffer controlled_buffer_57
  assign _7_el_str_26 = _2_t ? {31{1'b0}} : 31'bz;  // Controlled_Buffer controlled_buffer_58
  assign _7_el_str_27 = _2_t ? {31{1'b0}} : 31'bz;  // Controlled_Buffer controlled_buffer_59
  assign _7_el_str_28 = _2_t ? {31{1'b0}} : 31'bz;  // Controlled_Buffer controlled_buffer_60
  assign _7_el_str_29 = _2_t ? {31{1'b0}} : 31'bz;  // Controlled_Buffer controlled_buffer_61
  assign _7_el_str_30 = _2_t ? {31{1'b0}} : 31'bz;  // Controlled_Buffer controlled_buffer_62
  assign _7_el_str_31 = _2_t ? {31{1'b0}} : 31'bz;  // Controlled_Buffer controlled_buffer_63
  assign _7_el_str_32 = _2_t ? {31{1'b0}} : 31'bz;  // Controlled_Buffer controlled_buffer_64
  assign _3_t = not_1_out ? and_1_out : 1'bz;  // Controlled_Buffer controlled_buffer_65
  and and_1 (and_1_out, ~_8, ~_5, _3, ~_6);  // AND_Gate
  and and_2 (and_2_out, ~_8, ~_5, _2);  // AND_Gate
  assign _2_t = not_1_out ? and_2_out : 1'bz;  // Controlled_Buffer controlled_buffer_66
  and and_3 (and_3_out, ~_8, ~_5, _1, ~_4);  // AND_Gate
  assign _1_t = not_1_out ? and_3_out : 1'bz;  // Controlled_Buffer controlled_buffer_67
  not not_1 (not_1_out, isBattle);
  assign _3_t = isBattle ? 1'b0 : 1'bz;  // Controlled_Buffer controlled_buffer_68
  assign _2_t = isBattle ? 1'b0 : 1'bz;  // Controlled_Buffer controlled_buffer_69
  assign _1_t = isBattle ? 1'b0 : 1'bz;  // Controlled_Buffer controlled_buffer_70
  isBattle_whichenemy isbattle_whichenemy_1 (
    .curr_enemy(enemy), .GameState(gameState), .isBattle(isBattle));  // open: rat, mouse, ferret, snake
  assign mole_str_1 = isBattle ? 31'h3800000 : 31'bz;  // Controlled_Buffer controlled_buffer_71
  assign mole_str_2 = isBattle ? 31'h6c00000 : 31'bz;  // Controlled_Buffer controlled_buffer_72
  assign mole_str_3 = isBattle ? 31'h7c600000 : 31'bz;  // Controlled_Buffer controlled_buffer_73
  assign mole_str_4 = isBattle ? 31'h7821f000 : 31'bz;  // Controlled_Buffer controlled_buffer_74
  assign mole_str_5 = isBattle ? 31'h7823f800 : 31'bz;  // Controlled_Buffer controlled_buffer_75
  assign mole_str_6 = isBattle ? 31'h7ba70400 : 31'bz;  // Controlled_Buffer controlled_buffer_76
  assign mole_str_7 = isBattle ? 31'h7aaeee00 : 31'bz;  // Controlled_Buffer controlled_buffer_77
  assign mole_str_8 = isBattle ? 31'h7eefba00 : 31'bz;  // Controlled_Buffer controlled_buffer_78
  assign mole_str_9 = isBattle ? 31'h29ce600 : 31'bz;  // Controlled_Buffer controlled_buffer_79
  assign mole_str_10 = isBattle ? 31'h2f803b8 : 31'bz;  // Controlled_Buffer controlled_buffer_80
  assign mole_str_11 = isBattle ? 31'h2fc00e8 : 31'bz;  // Controlled_Buffer controlled_buffer_81
  assign mole_str_12 = isBattle ? 31'h6fe1838 : 31'bz;  // Controlled_Buffer controlled_buffer_82
  assign mole_str_13 = isBattle ? 31'h7eee0c60 : 31'bz;  // Controlled_Buffer controlled_buffer_83
  assign mole_str_14 = isBattle ? 31'h7ef787c0 : 31'bz;  // Controlled_Buffer controlled_buffer_84
  assign mole_str_15 = isBattle ? 31'h7bf4ff00 : 31'bz;  // Controlled_Buffer controlled_buffer_85
  assign mole_str_16 = isBattle ? 31'h78fe1d80 : 31'bz;  // Controlled_Buffer controlled_buffer_86
  assign mole_str_17 = isBattle ? 31'h78023880 : 31'bz;  // Controlled_Buffer controlled_buffer_87
  assign mole_str_18 = isBattle ? 31'h780fe080 : 31'bz;  // Controlled_Buffer controlled_buffer_88
  assign mole_str_19 = isBattle ? 31'h7c020080 : 31'bz;  // Controlled_Buffer controlled_buffer_89
  assign mole_str_20 = isBattle ? 31'h61f8180 : 31'bz;  // Controlled_Buffer controlled_buffer_90
  assign mole_str_21 = isBattle ? 31'h3e60300 : 31'bz;  // Controlled_Buffer controlled_buffer_91
  assign mole_str_22 = isBattle ? 31'h2ff8f80 : 31'bz;  // Controlled_Buffer controlled_buffer_92
  assign mole_str_23 = isBattle ? 31'h2e13dc0 : 31'bz;  // Controlled_Buffer controlled_buffer_93
  assign mole_str_24 = isBattle ? 31'h7c1f0c0 : 31'bz;  // Controlled_Buffer controlled_buffer_94
  assign mole_str_25 = isBattle ? 31'h44000e0 : 31'bz;  // Controlled_Buffer controlled_buffer_95
  assign mole_str_26 = isBattle ? 31'h7c00060 : 31'bz;  // Controlled_Buffer controlled_buffer_96
  assign mole_str_27 = isBattle ? 31'h1e00060 : 31'bz;  // Controlled_Buffer controlled_buffer_97
  assign mole_str_28 = isBattle ? 31'h1e00060 : 31'bz;  // Controlled_Buffer controlled_buffer_98
  assign mole_str_29 = isBattle ? 31'he000e0 : 31'bz;  // Controlled_Buffer controlled_buffer_99
  assign mole_str_30 = isBattle ? 31'he003c0 : 31'bz;  // Controlled_Buffer controlled_buffer_100
  assign mole_str_31 = isBattle ? {31{1'b0}} : 31'bz;  // Controlled_Buffer controlled_buffer_101
  assign mole_str_32 = isBattle ? {31{1'b0}} : 31'bz;  // Controlled_Buffer controlled_buffer_102
  or_for_str_31_bit or_for_str_31_bit_1 (
    .in_1(_1_el_str_1), .in_2(_7_el_str_1), .in_3(mole_str_1), .out_one_str(out_10));  // open: in_4, in_5, in_6, in_7, in_8
  or_for_str_31_bit or_for_str_31_bit_2 (
    .in_1(_1_el_str_2), .in_2(_7_el_str_2), .in_3(mole_str_2), .out_one_str(out_11));  // open: in_4, in_5, in_6, in_7, in_8
  or_for_str_31_bit or_for_str_31_bit_3 (
    .in_1(_1_el_str_3), .in_2(_7_el_str_3), .in_3(mole_str_3), .out_one_str(out_12));  // open: in_4, in_5, in_6, in_7, in_8
  or_for_str_31_bit or_for_str_31_bit_4 (
    .in_1(_1_el_str_4), .in_2(_7_el_str_4), .in_3(mole_str_4), .out_one_str(out_13));  // open: in_4, in_5, in_6, in_7, in_8
  or_for_str_31_bit or_for_str_31_bit_5 (
    .in_1(_1_el_str_5), .in_2(_7_el_str_5), .in_3(mole_str_5), .out_one_str(out_14));  // open: in_4, in_5, in_6, in_7, in_8
  or_for_str_31_bit or_for_str_31_bit_6 (
    .in_1(_1_el_str_6), .in_2(_7_el_str_6), .in_3(mole_str_6), .out_one_str(out_15));  // open: in_4, in_5, in_6, in_7, in_8
  or_for_str_31_bit or_for_str_31_bit_7 (
    .in_1(_1_el_str_7), .in_2(_7_el_str_7), .in_3(mole_str_7), .out_one_str(out_16));  // open: in_4, in_5, in_6, in_7, in_8
  or_for_str_31_bit or_for_str_31_bit_8 (
    .in_1(_1_el_str_8), .in_2(_7_el_str_8), .in_3(mole_str_8), .out_one_str(out_17));  // open: in_4, in_5, in_6, in_7, in_8
  or_for_str_31_bit or_for_str_31_bit_9 (
    .in_1(_1_el_str_9), .in_2(_7_el_str_9), .in_3(mole_str_9), .out_one_str(out_18));  // open: in_4, in_5, in_6, in_7, in_8
  or_for_str_31_bit or_for_str_31_bit_10 (
    .in_1(_1_el_str_10), .in_2(_7_el_str_10), .in_3(mole_str_10), .out_one_str(out_19));  // open: in_4, in_5, in_6, in_7, in_8
  or_for_str_31_bit or_for_str_31_bit_11 (
    .in_1(_1_el_str_11), .in_2(_7_el_str_11), .in_3(mole_str_11), .out_one_str(out_20));  // open: in_4, in_5, in_6, in_7, in_8
  or_for_str_31_bit or_for_str_31_bit_12 (
    .in_1(_1_el_str_12), .in_2(_7_el_str_12), .in_3(mole_str_12), .out_one_str(out_21));  // open: in_4, in_5, in_6, in_7, in_8
  or_for_str_31_bit or_for_str_31_bit_13 (
    .in_1(_1_el_str_13), .in_2(_7_el_str_13), .in_3(mole_str_13), .out_one_str(out_22));  // open: in_4, in_5, in_6, in_7, in_8
  or_for_str_31_bit or_for_str_31_bit_14 (
    .in_1(_1_el_str_14), .in_2(_7_el_str_14), .in_3(mole_str_14), .out_one_str(out_23));  // open: in_4, in_5, in_6, in_7, in_8
  or_for_str_31_bit or_for_str_31_bit_15 (
    .in_1(_1_el_str_15), .in_2(_7_el_str_15), .in_3(mole_str_15), .out_one_str(out_24));  // open: in_4, in_5, in_6, in_7, in_8
  or_for_str_31_bit or_for_str_31_bit_16 (
    .in_1(_1_el_str_16), .in_2(_7_el_str_16), .in_3(mole_str_16), .out_one_str(out_25));  // open: in_4, in_5, in_6, in_7, in_8
  or_for_str_31_bit or_for_str_31_bit_17 (
    .in_1(_1_el_str_17), .in_2(_7_el_str_17), .in_3(mole_str_17), .out_one_str(out_26));  // open: in_4, in_5, in_6, in_7, in_8
  or_for_str_31_bit or_for_str_31_bit_18 (
    .in_1(_1_el_str_18), .in_2(_7_el_str_18), .in_3(mole_str_18), .out_one_str(out_27));  // open: in_4, in_5, in_6, in_7, in_8
  or_for_str_31_bit or_for_str_31_bit_19 (
    .in_1(_1_el_str_19), .in_2(_7_el_str_19), .in_3(mole_str_19), .out_one_str(out_28));  // open: in_4, in_5, in_6, in_7, in_8
  or_for_str_31_bit or_for_str_31_bit_20 (
    .in_1(_1_el_str_20), .in_2(_7_el_str_20), .in_3(mole_str_20), .out_one_str(out_29));  // open: in_4, in_5, in_6, in_7, in_8
  or_for_str_31_bit or_for_str_31_bit_21 (
    .in_1(_1_el_str_21), .in_2(_7_el_str_21), .in_3(mole_str_21), .out_one_str(out_30));  // open: in_4, in_5, in_6, in_7, in_8
  or_for_str_31_bit or_for_str_31_bit_22 (
    .in_1(_1_el_str_22), .in_2(_7_el_str_22), .in_3(mole_str_22), .out_one_str(out_31));  // open: in_4, in_5, in_6, in_7, in_8
  or_for_str_31_bit or_for_str_31_bit_23 (
    .in_1(_1_el_str_23), .in_2(_7_el_str_23), .in_3(mole_str_23), .out_one_str(out_32));  // open: in_4, in_5, in_6, in_7, in_8
  or_for_str_31_bit or_for_str_31_bit_24 (
    .in_1(_1_el_str_24), .in_2(_7_el_str_24), .in_3(mole_str_24), .out_one_str(out_33));  // open: in_4, in_5, in_6, in_7, in_8
  or_for_str_31_bit or_for_str_31_bit_25 (
    .in_1(_1_el_str_25), .in_2(_7_el_str_25), .in_3(mole_str_25), .out_one_str(out_34));  // open: in_4, in_5, in_6, in_7, in_8
  or_for_str_31_bit or_for_str_31_bit_26 (
    .in_1(_1_el_str_26), .in_2(_7_el_str_26), .in_3(mole_str_26), .out_one_str(out_35));  // open: in_4, in_5, in_6, in_7, in_8
  or_for_str_31_bit or_for_str_31_bit_27 (
    .in_1(_1_el_str_27), .in_2(_7_el_str_27), .in_3(mole_str_27), .out_one_str(out_36));  // open: in_4, in_5, in_6, in_7, in_8
  or_for_str_31_bit or_for_str_31_bit_28 (
    .in_1(_1_el_str_28), .in_2(_7_el_str_28), .in_3(mole_str_28), .out_one_str(out_37));  // open: in_4, in_5, in_6, in_7, in_8
  or_for_str_31_bit or_for_str_31_bit_29 (
    .in_1(_1_el_str_29), .in_2(_7_el_str_29), .in_3(mole_str_29), .out_one_str(out_38));  // open: in_4, in_5, in_6, in_7, in_8
  or_for_str_31_bit or_for_str_31_bit_30 (
    .in_1(_1_el_str_30), .in_2(_7_el_str_30), .in_3(mole_str_30), .out_one_str(out_39));  // open: in_4, in_5, in_6, in_7, in_8
  or_for_str_31_bit or_for_str_31_bit_31 (
    .in_1(_1_el_str_31), .in_2(_7_el_str_31), .in_3(mole_str_31), .out_one_str(out_40));  // open: in_4, in_5, in_6, in_7, in_8
  or_for_str_31_bit or_for_str_31_bit_32 (
    .in_1(_1_el_str_32), .in_2(_7_el_str_32), .in_3(mole_str_32), .out_one_str(out_41));  // open: in_4, in_5, in_6, in_7, in_8

  // Other names for the same wires on the sheet: str_1[30:0] = out_10; str_2[30:0] = out_11; str_3[30:0] = out_12;
  //   str_4[30:0] = out_13; str_5[30:0] = out_14; str_6[30:0] = out_15; str_7[30:0] = out_16; str_8[30:0] = out_17;
  //   str_9[30:0] = out_18; str_10[30:0] = out_19; str_11[30:0] = out_20; str_12[30:0] = out_21;
  //   str_13[30:0] = out_22; str_14[30:0] = out_23; str_15[30:0] = out_24; str_16[30:0] = out_25;
  //   str_17[30:0] = out_26; str_18[30:0] = out_27; str_19[30:0] = out_28; str_20[30:0] = out_29;
  //   str_21[30:0] = out_30; str_22[30:0] = out_31; str_23[30:0] = out_32; str_24[30:0] = out_33;
  //   str_25[30:0] = out_34; str_26[30:0] = out_35; str_27[30:0] = out_36; str_28[30:0] = out_37;
  //   str_29[30:0] = out_38; str_30[30:0] = out_39; str_31[30:0] = out_40; str_32[30:0] = out_41

  // Notes on the sheet:
  //   2 -> 7
endmodule

module isBattle_whichenemy (
  input  [1:0] curr_enemy,
  input  [1:0] GameState,
  output rat,
  output mouse,
  output ferret,
  output snake,
  output isBattle
);

  Demultiplexer #(.select(2), .enable("false")) demultiplexer_1 (
    .out0(rat), .out1(mouse), .out2(ferret), .out3(snake), .in(1'b1), .sel(curr_enemy));
  Comparator #(.width(2)) comparator_1 (.a(GameState), .b(2'b10), .eq(isBattle));  // open: gt, lt
endmodule

module chest_or_not (
  input  [7:0] Worm,
  output Chest
);

  wire comparator_1_eq, comparator_2_eq, comparator_3_eq, comparator_4_eq, comparator_5_eq, comparator_6_eq,
       comparator_7_eq, comparator_8_eq, comparator_9_eq;

  Comparator comparator_1 (.a(Worm), .b(8'h61), .eq(comparator_1_eq));  // open: gt, lt
  Comparator comparator_2 (.a(Worm), .b(8'h62), .eq(comparator_2_eq));  // open: gt, lt
  Comparator comparator_3 (.a(Worm), .b(8'h63), .eq(comparator_3_eq));  // open: gt, lt
  Comparator comparator_4 (.a(Worm), .b(8'h64), .eq(comparator_4_eq));  // open: gt, lt
  Comparator comparator_5 (.a(Worm), .b(8'h66), .eq(comparator_5_eq));  // open: gt, lt
  Comparator comparator_6 (.a(Worm), .b(8'h67), .eq(comparator_6_eq));  // open: gt, lt
  Comparator comparator_7 (.a(Worm), .b(8'h68), .eq(comparator_7_eq));  // open: gt, lt
  Comparator comparator_8 (.a(Worm), .b(8'h69), .eq(comparator_8_eq));  // open: gt, lt
  Comparator comparator_9 (.a(Worm), .b(8'h6a), .eq(comparator_9_eq));  // open: gt, lt
  Pull_Resistor pull_resistor_1 (.node(Chest));
  or or_1 (Chest, comparator_1_eq, comparator_2_eq, comparator_3_eq, comparator_4_eq, comparator_5_eq, comparator_6_eq, comparator_7_eq, comparator_8_eq, comparator_9_eq);

  // Notes on the sheet:
  //   Bug
  //   Spider
  //   Centipede
  //   Weapons
  //   Stick
  //   OLD_claw
  //   bone cudgel
  //   BFG 9000
  //   FOOD
  //   sharpened bone
endmodule
